// Logisim project 分支预测.circ as structural Verilog: 17 circuits, main circuit ◇单周期MIPS
module \单周期MIPS  (
);

  wire and_1_out, and_2_out, and_3_out, and_5_out, and_6_out, and_7_out, and_8_out, BLEZ, branch, branchsc,
       CLK, comparator_1_eq, comparator_2_eq, ex_mem_1_jalout, ex_mem_1_mem_lhu, ex_mem_1_memwriteout,
       ex_mem_1_systemcallout, EX_RegWrite, Go, id_ex_1_alusrcout, id_ex_1_beqout, id_ex_1_bneout,
       id_ex_1_ex_lhu, id_ex_1_memtoregout, id_ex_1_memwriteout, id_ex_1_systemcallout, JAL, JMP, JR,
       Loaduse, MEM_MemReg, MEM_RegWrite, mem_wb_1_jalout, mem_wb_1_memtoregout, mips_alu_1_equal, miss,
       not_1_out, not_3_out, not_4_out, or_2_out, or_3_out, or_4_out, or_5_out, or_6_out, or_7_out, or_8_out,
       or_10_out, or_12_out, PCen, register_2_q, RegWrite, RST, SignedExt, syscall, \分支 , \硬布线控制器_1_alu_src ,
       \硬布线控制器_1_beq , \硬布线控制器_1_blez , \硬布线控制器_1_bne , \硬布线控制器_1_jal , \硬布线控制器_1_jmp , \硬布线控制器_1_jr ,
       \硬布线控制器_1_lhu , \硬布线控制器_1_memtoreg , \硬布线控制器_1_memwrite , \硬布线控制器_1_regdst , \硬布线控制器_1_regwrite ,
       \硬布线控制器_1_shift , \硬布线控制器_1_syscall , \跳转 , \预测正确 ;
  wire [1:0] EX_ChooseA, EX_ChooseB, ID_ChooseA, ID_ChooseB;
  wire [3:0] id_ex_1_aluopout, \硬布线控制器_1_alu_op ;
  wire [4:0] EX_WriteReg, id_ex_1_shamtout, MEM_WriteReg, multiplexer_7_out, multiplexer_8_out, R1_num,
       R2_num, shamt, WriteRegSign;
  wire [5:0] FUNC, OP;
  wire [15:0] loaduse_t, \Miss数 , \总周期数 , \插入气泡数 , \无条件分支数 , \条件分支成功数 , \预测成功 ;
  wire [25:6] if_id_1_irout;
  wire [31:0] adder_1_out, adder_2_out, ALUR, Aout, bit_extender_1_out, bit_extender_2_out,
       bit_extender_3_out, bit_extender_4_out, branch_add, branch_adds, ChooseR2, Din, EX_IR, ex_mem_1_aout,
       ex_mem_1_bout, ex_mem_1_irout, ex_mem_1_pc_4out, ex_mem_1_pcout, id_ex_1_eimmout, id_ex_1_immout,
       id_ex_1_pc_4out, if_id_1_pc_4out, if_id_1_pcout, \if_id_1_预测out , IR, LedData, MEM_ALU,
       mem_wb_1_pc_4out, mips_ram_1_p8, mips_regifile_1_r1, mips_regifile_1_r2, multiplexer_3_out,
       multiplexer_9_out, multiplexer_10_out, multiplexer_13_out, multiplexer_14_out, multiplexer_15_out, PC,
       PCM, pre_add, R1, R2, RegR1, RegR2, rom_1_data, shifter_1_out, WB_ALU, WB_Mem, \分支指令地址 , \前预测 ;

  Button \u_总复位  (.out(RST));
  Button u_Go (.out(Go));
  Clock clock_1 (.out(CLK));
  Multiplexer #(.select(3), .width(32), .enable("false")) multiplexer_1 (
    .in0(id_ex_1_pc_4out), .in1(Aout), .in2({adder_2_out[31:28], EX_IR[25:0], 2'b00}), .in3(Aout),
    .in4(adder_2_out), .in5(Aout), .in6({adder_2_out[31:28], EX_IR[25:0], 2'b00}), .in7(Aout),
    .out(branch_add), .sel({branch, JMP, JR}));
  Multiplexer #(.select(3), .width(32), .enable("false")) multiplexer_2 (
    .in0(id_ex_1_pc_4out), .in1(Aout), .in2({adder_2_out[31:28], EX_IR[25:0], 2'b00}), .in3(Aout),
    .in4(adder_2_out), .in5(Aout), .in6({adder_2_out[31:28], EX_IR[25:0], 2'b00}), .in7(Aout),
    .out(branch_adds), .sel({branchsc, JMP, JR}));
  Hex_Digit_Display hex_digit_display_1 (.value(LedData[27:24]));  // open: dp
  Hex_Digit_Display hex_digit_display_2 (.value(LedData[31:28]));  // open: dp
  Comparator #(.width(32)) comparator_1 (.a(R1), .b(32'h22), .eq(comparator_1_eq));  // open: gt, lt
  Hex_Digit_Display hex_digit_display_3 (.value(LedData[19:16]));  // open: dp
  Hex_Digit_Display hex_digit_display_4 (.value(LedData[23:20]));  // open: dp
  or or_1 (\分支 , branchsc, JAL, JMP, JR);
  or or_2 (or_2_out, \预测正确 , ~\跳转 );  // OR_Gate
  Hex_Digit_Display hex_digit_display_5 (.value(LedData[11:8]));  // open: dp
  Hex_Digit_Display hex_digit_display_6 (.value(LedData[15:12]));  // open: dp
  Counter #(.width(16), .max('hffff)) counter_1 (
    .count(or_3_out), .Q(\无条件分支数 ), .clk(CLK), .clr(RST));  // open: load, D, carry
  or or_3 (or_3_out, JR, JMP, JAL);
  Multiplexer #(.width(32), .enable("false")) multiplexer_3 (
    .in0(branch_adds), .in1(pre_add), .out(multiplexer_3_out), .sel(or_2_out));
  and and_1 (and_1_out, comparator_1_eq, syscall);
  Hex_Digit_Display hex_digit_display_7 (.value(LedData[3:0]));  // open: dp
  Hex_Digit_Display hex_digit_display_8 (.value(LedData[7:4]));  // open: dp
  Register #(.width(32)) register_1 (.D(R2), .en(and_1_out), .Q(LedData), .clk(CLK), .clr(RST));
  and and_2 (and_2_out, ~comparator_1_eq, syscall);  // AND_Gate
  Comparator #(.width(32)) comparator_2 (.a(\前预测 ), .b(branch_adds), .eq(comparator_2_eq));  // open: gt, lt
  and and_3 (and_3_out, PCen, not_1_out);
  not not_1 (not_1_out, Loaduse);
  not not_2 (PCen, register_2_q);
  Register #(.width(1)) register_2 (.D(syscall), .en(and_2_out), .Q(register_2_q), .clk(CLK), .clr(or_4_out));
  or or_4 (or_4_out, RST, Go);
  and and_4 (\预测正确 , comparator_2_eq, \跳转 );
  Register #(.width(32)) u_PC (.D(multiplexer_3_out), .en(and_3_out), .Q(PCM), .clk(CLK), .clr(RST));
  not not_3 (not_3_out, PCen);
  // Probe on \总周期数 
  // Probe on \无条件分支数 
  // Probe on \条件分支成功数 
  // Probe on \插入气泡数 
  // Probe on loaduse_t
  Counter #(.width(16), .max('hffff)) counter_2 (
    .count(PCen), .Q(\总周期数 ), .clk(CLK), .clr(RST));  // open: load, D, carry
  ROM #(.addrWidth(10), .dataWidth(32)) rom_1 (.addr(PCM[11:2]), .data(rom_1_data));  // open: sel
  Adder #(.width(32)) adder_1 (.a(PCM), .b(32'h4), .out(adder_1_out));  // open: cin, cout
  or or_5 (or_5_out, Loaduse, not_3_out);
  // Probe on \Miss数 
  // Probe on \预测成功 
  \分支预测BHT  \u_分支预测bht_1  (
    .\分支指令地址 (\分支指令地址 ), .\分支目标地址 (branch_add), .CLK(CLK), .\分支 (\分支 ), .in_1(PCM), .Enable(1'b1),
    .Miss(miss), .DataOut(pre_add), .\跳转 (\跳转 ));
  or or_6 (or_6_out, \预测正确 , ~\跳转 );  // OR_Gate
  Multiplexer #(.width(5), .enable("false")) multiplexer_4 (
    .in0(if_id_1_irout[10:6]), .in1(5'b10000), .out(shamt), .sel(\硬布线控制器_1_shift ));
  IF_ID if_id_1 (
    .PCin(PCM), .IRin(rom_1_data), .CLK(CLK), .PCout(if_id_1_pcout), .IRout({OP, if_id_1_irout, FUNC}),
    .\同步清零 (not_4_out), .\使能端 (or_5_out), .PC_4in(adder_1_out), .PC_4out(if_id_1_pc_4out),
    .\预测out (\if_id_1_预测out ), .\预测in (pre_add));
  not not_4 (not_4_out, or_6_out);
  and and_5 (and_5_out, PCen, Loaduse);
  Counter #(.width(16), .max('hffff)) counter_3 (
    .count(\预测正确 ), .Q(\预测成功 ), .clk(CLK), .clr(RST));  // open: load, D, carry
  or or_7 (or_7_out, not_4_out, and_5_out);
  \硬布线控制器  \u_硬布线控制器_1  (
    .Func(FUNC), .OP(OP), .ALU_OP(\硬布线控制器_1_alu_op ), .MemToReg(\硬布线控制器_1_memtoreg ),
    .MemWrite(\硬布线控制器_1_memwrite ), .ALU_SRC(\硬布线控制器_1_alu_src ), .RegWrite(\硬布线控制器_1_regwrite ),
    .SysCALL(\硬布线控制器_1_syscall ), .SignedExt(SignedExt), .RegDst(\硬布线控制器_1_regdst ), .JR(\硬布线控制器_1_jr ),
    .JMP(\硬布线控制器_1_jmp ), .Beq(\硬布线控制器_1_beq ), .JAL(\硬布线控制器_1_jal ), .Bne(\硬布线控制器_1_bne ),
    .Shift(\硬布线控制器_1_shift ), .BLEZ(\硬布线控制器_1_blez ), .LHU(\硬布线控制器_1_lhu ));
  Multiplexer #(.width(5), .enable("false")) multiplexer_5 (
    .in0(if_id_1_irout[25:21]), .in1(5'b00010), .out(R1_num), .sel(\硬布线控制器_1_syscall ));
  Multiplexer #(.width(5), .enable("false")) multiplexer_6 (
    .in0(if_id_1_irout[20:16]), .in1(5'b00100), .out(R2_num), .sel(\硬布线控制器_1_syscall ));
  assign bit_extender_1_out = {{16{1'b0}}, {if_id_1_irout[15:6], FUNC}};  // Bit_Extender bit_extender_1
  assign bit_extender_2_out = {{16{if_id_1_irout[15]}}, {if_id_1_irout[15:6], FUNC}};  // Bit_Extender bit_extender_2
  Counter #(.width(16), .max('hffff)) counter_4 (
    .count(or_7_out), .Q(\插入气泡数 ), .clk(CLK), .clr(RST));  // open: load, D, carry
  Counter #(.width(16), .max('hffff)) counter_5 (
    .count(and_5_out), .Q(loaduse_t), .clk(CLK), .clr(RST));  // open: load, D, carry
  Multiplexer #(.width(5), .enable("false")) multiplexer_7 (
    .in0(if_id_1_irout[20:16]), .in1(if_id_1_irout[15:11]), .out(multiplexer_7_out), .sel(\硬布线控制器_1_regdst ));
  Multiplexer #(.width(5), .enable("false")) multiplexer_8 (
    .in0(multiplexer_7_out), .in1({5{1'b1}}), .out(multiplexer_8_out), .sel(\硬布线控制器_1_jal ));
  Multiplexer #(.width(32), .enable("false")) multiplexer_9 (
    .in0(bit_extender_1_out), .in1(bit_extender_2_out), .out(multiplexer_9_out), .sel(SignedExt));
  Counter #(.width(16), .max('hffff)) counter_6 (
    .count(miss), .Q(\Miss数 ), .clk(CLK), .clr(RST));  // open: load, D, carry
  MIPS_Regifile mips_regifile_1 (
    .Din(Din), .Clk(CLK), .R1(mips_regifile_1_r1), .R2(mips_regifile_1_r2), .WE(RegWrite),
    .W_num(WriteRegSign), .R1_num(R1_num), .R2_num(R2_num));
  or or_8 (or_8_out, Loaduse, not_4_out);
  ID_EX id_ex_1 (
    .PCin(if_id_1_pcout), .IRin({OP, if_id_1_irout, FUNC}), .Ain(mips_regifile_1_r1),
    .Bin(mips_regifile_1_r2), .IMMin(multiplexer_9_out), .CLK(CLK), .PCout(\分支指令地址 ), .IRout(EX_IR),
    .Aout(RegR1), .Bout(RegR2), .IMMout(id_ex_1_immout), .\同步清零 (or_8_out), .\使能端 (not_3_out),
    .MemToRegin(\硬布线控制器_1_memtoreg ), .MemToRegout(id_ex_1_memtoregout), .MemWritein(\硬布线控制器_1_memwrite ),
    .MemWriteout(id_ex_1_memwriteout), .AluOPin(\硬布线控制器_1_alu_op ), .AluOPout(id_ex_1_aluopout),
    .AluSrcin(\硬布线控制器_1_alu_src ), .AluSrcout(id_ex_1_alusrcout), .RegWritein(\硬布线控制器_1_regwrite ),
    .RegWriteout(EX_RegWrite), .WriteRegin(multiplexer_8_out), .WriteRegout(EX_WriteReg),
    .JALin(\硬布线控制器_1_jal ), .JALout(JAL), .PC_4in(if_id_1_pc_4out), .PC_4out(id_ex_1_pc_4out),
    .EIMMin(bit_extender_2_out), .EIMMout(id_ex_1_eimmout), .Bnein(\硬布线控制器_1_bne ), .Bneout(id_ex_1_bneout),
    .Beqin(\硬布线控制器_1_beq ), .Beqout(id_ex_1_beqout), .JMPin(\硬布线控制器_1_jmp ), .JMPout(JMP), .JRout(JR),
    .JRin(\硬布线控制器_1_jr ), .Systemcallin(\硬布线控制器_1_syscall ), .Systemcallout(id_ex_1_systemcallout),
    .Shamtin(shamt), .Shamtout(id_ex_1_shamtout), .ID_ChooseA(ID_ChooseA), .EX_ChooseA(EX_ChooseA),
    .ID_ChooseB(ID_ChooseB), .EX_ChooseB(EX_ChooseB), .ID_LHU(\硬布线控制器_1_lhu ), .EX_LHU(id_ex_1_ex_lhu),
    .ID_BLEZ(\硬布线控制器_1_blez ), .EX_BLEZ(BLEZ), .\预测in (\if_id_1_预测out ), .\预测out (\前预测 ));
  \重定向选择  \u_重定向选择_1  (
    .EX_WriteReg(EX_WriteReg), .OP_CODE(OP), .R1(R1_num), .chooseA(ID_ChooseA), .MEM_WriteReg(MEM_WriteReg),
    .FUNC(FUNC), .R2(R2_num), .chooseB(ID_ChooseB), .EX_RegWrite(EX_RegWrite), .EX_OP(EX_IR[31:26]),
    .Loaduse(Loaduse), .MEM_RegWrite(MEM_RegWrite), .MEM_MemReg(MEM_MemReg));
  Multiplexer #(.width(32), .enable("false")) multiplexer_10 (
    .in0(ChooseR2), .in1(id_ex_1_immout), .out(multiplexer_10_out), .sel(id_ex_1_alusrcout));
  or or_9 (branch, id_ex_1_beqout, id_ex_1_bneout, BLEZ);
  MIPS_ALU mips_alu_1 (
    .X(Aout), .Y(multiplexer_10_out), .AluOP(id_ex_1_aluopout), .Equal(mips_alu_1_equal), .Result(ALUR),
    .shamt(id_ex_1_shamtout));  // open: Result_2
  Shifter #(.width(32)) shifter_1 (.in(id_ex_1_eimmout), .\dist (5'b00010), .out(shifter_1_out));
  Multiplexer #(.select(2), .width(32), .enable("false")) multiplexer_11 (
    .in0(RegR1), .in1(WB_Mem), .in2(WB_ALU), .in3(MEM_ALU), .out(Aout), .sel(EX_ChooseA));
  Multiplexer #(.select(2), .width(32), .enable("false")) multiplexer_12 (
    .in0(RegR2), .in1(WB_Mem), .in2(WB_ALU), .in3(MEM_ALU), .out(ChooseR2), .sel(EX_ChooseB));
  or or_10 (or_10_out, ALUR[0], mips_alu_1_equal);
  and and_6 (and_6_out, mips_alu_1_equal, id_ex_1_beqout);
  and and_7 (and_7_out, ~mips_alu_1_equal, id_ex_1_bneout);  // AND_Gate
  EX_MEM ex_mem_1 (
    .MemToRegin(id_ex_1_memtoregout), .MemToRegout(MEM_MemReg), .MemWritein(id_ex_1_memwriteout),
    .MemWriteout(ex_mem_1_memwriteout), .RegWritein(EX_RegWrite), .RegWriteout(MEM_RegWrite),
    .PCin(\分支指令地址 ), .PCout(ex_mem_1_pcout), .IRin(EX_IR), .IRout(ex_mem_1_irout), .Bin(ChooseR2),
    .Bout(ex_mem_1_bout), .CLK(CLK), .\同步清零 (RST), .\使能端 (not_3_out), .ALUin(ALUR), .ALUout(MEM_ALU),
    .WriteRegin(EX_WriteReg), .WriteRegout(MEM_WriteReg), .JALin(JAL), .JALout(ex_mem_1_jalout),
    .PC_4in(id_ex_1_pc_4out), .PC_4out(ex_mem_1_pc_4out), .Systemcallin(id_ex_1_systemcallout),
    .Systemcallout(ex_mem_1_systemcallout), .Ain(Aout), .Aout(ex_mem_1_aout), .EX_LHU(id_ex_1_ex_lhu),
    .MEM_LHU(ex_mem_1_mem_lhu));
  Adder #(.width(32)) adder_2 (.a(shifter_1_out), .b(id_ex_1_pc_4out), .out(adder_2_out));  // open: cin, cout
  or or_11 (\跳转 , id_ex_1_beqout, id_ex_1_bneout, JAL, JMP, JR, BLEZ);
  and and_8 (and_8_out, or_10_out, BLEZ);
  or or_12 (or_12_out, and_6_out, and_7_out);
  // MIPS_RAM mips_ram_1: pin names not known; wires that end beside it: {{10{1'b0}}, MEM_ALU[11:2]}, ex_mem_1_bout, ex_mem_1_memwriteout, 4'b1111, CLK, MEM_MemReg, RST, mips_ram_1_p8
  or or_13 (branchsc, and_8_out, or_12_out);
  Counter #(.width(16), .max('hffff)) counter_7 (
    .count(branchsc), .Q(\条件分支成功数 ), .clk(CLK), .clr(RST));  // open: load, D, carry
  assign bit_extender_3_out = {{16{1'b0}}, mips_ram_1_p8[15:0]};  // Bit_Extender bit_extender_3
  assign bit_extender_4_out = {{16{1'b0}}, mips_ram_1_p8[31:16]};  // Bit_Extender bit_extender_4
  Multiplexer #(.width(32), .enable("false")) multiplexer_13 (
    .in0(bit_extender_3_out), .in1(bit_extender_4_out), .out(multiplexer_13_out), .sel(MEM_ALU[1]));
  Multiplexer #(.width(32), .enable("false")) multiplexer_14 (
    .in0(mips_ram_1_p8), .in1(multiplexer_13_out), .out(multiplexer_14_out), .sel(ex_mem_1_mem_lhu));
  MEM_WB mem_wb_1 (
    .RegWritein(MEM_RegWrite), .IRin(ex_mem_1_irout), .PCin(ex_mem_1_pcout), .ALUin(MEM_ALU),
    .MDin(multiplexer_14_out), .CLK(CLK), .RegWriteout(RegWrite), .IRout(IR), .PCout(PC), .ALUout(WB_ALU),
    .MDout(WB_Mem), .\同步清零 (RST), .\使能端 (not_3_out), .MemToRegin(MEM_MemReg),
    .MemToRegout(mem_wb_1_memtoregout), .WriteRegin(MEM_WriteReg), .WriteRegout(WriteRegSign),
    .JALin(ex_mem_1_jalout), .JALout(mem_wb_1_jalout), .PC_4in(ex_mem_1_pc_4out), .PC_4out(mem_wb_1_pc_4out),
    .Systemcallin(ex_mem_1_systemcallout), .Systemcallout(syscall), .Ain(ex_mem_1_aout), .Aout(R1),
    .Bin(ex_mem_1_bout), .Bout(R2));
  Multiplexer #(.width(32), .enable("false")) multiplexer_15 (
    .in0(WB_ALU), .in1(WB_Mem), .out(multiplexer_15_out), .sel(mem_wb_1_memtoregout));
  // Probe on WriteRegSign
  Multiplexer #(.width(32), .enable("false")) multiplexer_16 (
    .in0(multiplexer_15_out), .in1(mem_wb_1_pc_4out), .out(Din), .sel(mem_wb_1_jalout));

  // Other names for the same wires on the sheet: ChooseR1[31:0] = Aout; IRI[31:0] = EX_IR

  // Notes on the sheet:
  //   数码管输出
  //   contents of rom_1 (hex, n*v repeats v):
  //   20110001 8100005 20110001 20120002 20130003 8100009 20110001 20120002 20130003 810000d 20110001
  //   20120002 20130003 8100011 20110001 20120002 20130003 c1000fb 20100001 20110001 118fc0 112020
  //   20020022 c 118882 12200001 8100015 112020 20020022 c 20110001 118880 112020 20020022 c 12200001
  //   810001f 20110001 118fc0 112020 20020022 c 1188c3 112020 20020022 c 118903 112020 20020022 c 118903
  //   112020 20020022 c 118903 112020 20020022 c 118903 112020 20020022 c 118903 112020 20020022 c 118903
  //   112020 20020022 c 118903 112020 20020022 c 20100001 109fc0 139fc3 8021 2012000c 24160003 26100001
  //   3210000f 20080008 20090001 139900 2709825 132020 20020022 c 1094022 1500fff9 22100001 2018000f
  //   2188024 108700 20080008 20090001 139902 2709825 132021 20020022 c 1094022 1500fff9 108702 2c9b022
  //   12c00001 8100050 4020 1084027 84400 3508ffff 82021 20020022 c 2010ffff 20110000 ae300000 22100001
  //   22310004 ae300000 22100001 22310004 ae300000 22100001 22310004 ae300000 22100001 22310004 ae300000
  //   22100001 22310004 ae300000 22100001 22310004 ae300000 22100001 22310004 ae300000 22100001 22310004
  //   ae300000 22100001 22310004 ae300000 22100001 22310004 ae300000 22100001 22310004 ae300000 22100001
  //   22310004 ae300000 22100001 22310004 ae300000 22100001 22310004 ae300000 22100001 22310004 ae300000
  //   22100001 22310004 22100001 8020 2011003c 8e130000 8e340000 274402a 11000002 ae330000 ae140000
  //   2231fffc 1611fff8 102020 20020022 c 22100004 2011003c 1611fff2 20020032 c 2008ffff 20117777 112020
  //   20020022 c 200b0010 2288826 112020 20020022 c 216bffff 1560fffa 2002000a c 200b0008 3c11fedc
  //   3631ffff 112020 20020022 c 3c11ba98 112020 c 3c117654 112020 c 3c113210 112020 c 216bffff 1560fff0
  //   2002000a c 20090000 200b0010 34118483 20120404 118c00 129400 36318281 22520404 ad310000 2328820
  //   21290004 216bffff 1560fffb 200b0020 20090000 95310000 112020 20020022 c 21290002 216bffff 1560fff9
  //   2002000a c 2011fff1 112020 20020022 c 22310001 1a20fffb 2002000a c 2002000a c 20100000 22100001
  //   102020 20020022 c 22100002 102020 20020022 c 22100003 102020 20020022 c 22100004 102020 20020022 c
  //   22100005 102020 20020022 c 22100006 102020 20020022 c 22100007 102020 20020022 c 22100008 102020
  //   20020022 20020022 c 3e00008
  //   指令存储器
  //   指令字
  //   OP
  //   Func
  //   rs
  //   rt
  //   rd
  //   JR
  //   OP
  //   Func
  //   Syscall
  //   MemToReg
  //   MemWrite
  //   AluOP
  //   AluSrcB
  //   JAL
  //   RegDst
endmodule

// 单周期硬布线控制器
module \硬布线控制器  (
  input  [5:0] OP,
  input  [5:0] Func,
  output [3:0] ALU_OP,
  output MemToReg,
  output MemWrite,
  output ALU_SRC,
  output RegWrite,
  output SysCALL,
  output SignedExt,
  output RegDst,
  output Beq,
  output Bne,
  output JR,
  output JMP,
  output JAL,
  output Shift,
  output BLEZ,
  output LHU
);

  \cpu28__运算控制器  \u_运算控制器_1  (
    .OP0(OP[0]), .OP1(OP[1]), .OP2(OP[2]), .OP3(OP[3]), .OP4(OP[4]), .OP5(OP[5]), .F0(Func[0]), .F1(Func[1]),
    .F2(Func[2]), .F3(Func[3]), .F4(Func[4]), .F5(Func[5]), .S0(ALU_OP[0]), .S1(ALU_OP[1]), .S2(ALU_OP[2]),
    .S3(ALU_OP[3]));
  \cpu28__控制信号生成  \u_控制信号生成_1  (
    .OP0(OP[0]), .OP1(OP[1]), .OP2(OP[2]), .OP3(OP[3]), .OP4(OP[4]), .OP5(OP[5]), .F0(Func[0]), .F1(Func[1]),
    .F2(Func[2]), .F3(Func[3]), .F4(Func[4]), .F5(Func[5]), .MemToReg(MemToReg), .MemWrite(MemWrite),
    .ALU_SRCB_1(ALU_SRC), .RegWrite(RegWrite), .SysCALL(SysCALL), .SignedExt(SignedExt), .RegDst(RegDst),
    .BEQ(Beq), .BNE(Bne), .JR(JR), .JMP(JMP), .JAL(JAL));
  \控制信号生成2  \u_控制信号生成2_1  (
    .OP0(OP[0]), .OP1(OP[1]), .OP2(OP[2]), .OP3(OP[3]), .OP4(OP[4]), .OP5(OP[5]), .F0(Func[0]), .F1(Func[1]),
    .F2(Func[2]), .F3(Func[3]), .F4(Func[4]), .F5(Func[5]), .Shift(Shift), .MemtoPC(BLEZ), .LUH(LHU));

  // Other names for the same wires on the sheet: OP_CODE[5:0] = OP

  // Notes on the sheet:
  //   运算器控制器，根据指令生成运算器功能选择信号
  //   控制信号生成，产生数据通路需要的其他控制信号
endmodule

// 运算器控制器
module \运算控制器  (
  input  OP0,
  input  OP1,
  input  OP2,
  input  OP3,
  input  OP4,
  input  OP5,
  input  F0,
  input  F1,
  input  F2,
  input  F3,
  input  F4,
  input  F5,
  output S0,
  output S1,
  output S2,
  output S3
);

  wire and_1_out, and_2_out, and_3_out, and_4_out, and_5_out, and_6_out, and_7_out, and_8_out, and_9_out,
       and_10_out, and_11_out, and_12_out, and_13_out, and_14_out, and_15_out, and_16_out, and_17_out,
       and_18_out, and_19_out, and_20_out, and_21_out, and_22_out, and_23_out, and_24_out, and_25_out,
       and_26_out, and_27_out, and_28_out, and_29_out, and_30_out, and_31_out, and_32_out, and_33_out,
       and_34_out, and_35_out, and_36_out, and_37_out, and_38_out, and_39_out, and_40_out, and_41_out,
       and_42_out, and_43_out, not_1_out, not_2_out, not_3_out, not_4_out, not_5_out, not_6_out, not_7_out,
       not_8_out, not_9_out, not_10_out, not_11_out, not_12_out, not_13_out, not_14_out, not_15_out,
       not_16_out, not_17_out, not_18_out, not_19_out, not_20_out, not_21_out, not_22_out, not_23_out,
       not_24_out, not_25_out, not_26_out, not_27_out, not_28_out, not_29_out, not_30_out, not_31_out,
       not_32_out, not_33_out, not_34_out, not_35_out, not_36_out, not_37_out, not_38_out, not_39_out,
       not_40_out, not_41_out, not_42_out, not_43_out, not_44_out, not_45_out, not_46_out, not_47_out,
       not_48_out, not_49_out, not_50_out, not_51_out, not_52_out, not_53_out, not_54_out, not_55_out,
       not_56_out, not_57_out, not_58_out, not_59_out, not_60_out, not_61_out, not_62_out, not_63_out,
       not_64_out, not_65_out, not_66_out, not_67_out, not_68_out, not_69_out, not_70_out, not_71_out,
       not_72_out, not_73_out, not_74_out, not_75_out, not_76_out, not_77_out, not_78_out, not_79_out,
       not_80_out, not_81_out, not_82_out, not_83_out, not_84_out, not_85_out, not_86_out, not_87_out,
       not_88_out, not_89_out, not_90_out, not_91_out, not_92_out, not_93_out, not_94_out, not_95_out,
       not_96_out, not_97_out, not_98_out, not_99_out, not_100_out, not_101_out, not_102_out, not_103_out,
       not_104_out, not_105_out, not_106_out, not_107_out, not_108_out, not_109_out, not_110_out,
       not_111_out, not_112_out, not_113_out, not_114_out, not_115_out, not_116_out, not_117_out,
       not_118_out, not_119_out, not_120_out, not_121_out, not_122_out, not_123_out, not_124_out,
       not_125_out, not_126_out, not_127_out, not_128_out, not_129_out, not_130_out, not_131_out,
       not_132_out, not_133_out, not_134_out, not_135_out, not_136_out, not_137_out, not_138_out,
       not_139_out, not_140_out, not_141_out, not_142_out, not_143_out, not_144_out, not_145_out,
       not_146_out, not_147_out, not_148_out, not_149_out, not_150_out, not_151_out, not_152_out,
       not_153_out, not_154_out, not_155_out, not_156_out, not_157_out, not_158_out, not_159_out,
       not_160_out, not_161_out, not_162_out, not_163_out, not_164_out, not_165_out, not_166_out,
       not_167_out, not_168_out, not_169_out, not_170_out, not_171_out, not_172_out, not_173_out,
       not_174_out, not_175_out, not_176_out, not_177_out, not_178_out, not_179_out, not_180_out,
       not_181_out, not_182_out, not_183_out, not_184_out, not_185_out, not_186_out, not_187_out,
       not_188_out, not_189_out, not_190_out, not_191_out, not_192_out, not_193_out, not_194_out,
       not_195_out, not_196_out, not_197_out, not_198_out, not_199_out, not_200_out, not_201_out,
       not_202_out, not_203_out, not_204_out, not_205_out, not_206_out, not_207_out, not_208_out,
       not_209_out, not_210_out, not_211_out, not_212_out, not_213_out, not_214_out, not_215_out,
       not_216_out, not_217_out, not_218_out, not_219_out, not_220_out, not_221_out, not_222_out,
       not_223_out, not_224_out, not_225_out, not_226_out, not_227_out, not_228_out, not_229_out,
       not_230_out, not_231_out, not_232_out, not_233_out, not_234_out, not_235_out, not_236_out,
       not_237_out, not_238_out, not_239_out, not_240_out, not_241_out, not_242_out, not_243_out,
       not_244_out, not_245_out, not_246_out, not_247_out, not_248_out, not_249_out, not_250_out,
       not_251_out, not_252_out, not_253_out, not_254_out, not_255_out, not_256_out, not_257_out,
       not_258_out, not_259_out, not_260_out, not_261_out, not_262_out, not_263_out, not_264_out,
       not_265_out, not_266_out, not_267_out, not_268_out, not_269_out, not_270_out, not_271_out,
       not_272_out, not_273_out, not_274_out, not_275_out, not_276_out, not_277_out, not_278_out,
       not_279_out, not_280_out, not_281_out, not_282_out, not_283_out, not_284_out, not_285_out,
       not_286_out, not_287_out, not_288_out, not_289_out;

  not not_1 (not_1_out, OP5);
  not not_2 (not_2_out, OP4);
  not not_3 (not_3_out, OP3);
  not not_4 (not_4_out, OP2);
  not not_5 (not_5_out, OP1);
  not not_6 (not_6_out, OP0);
  not not_7 (not_7_out, F5);
  not not_8 (not_8_out, F4);
  not not_9 (not_9_out, F3);
  not not_10 (not_10_out, F2);
  not not_11 (not_11_out, OP5);
  not not_12 (not_12_out, OP4);
  not not_13 (not_13_out, OP3);
  not not_14 (not_14_out, OP2);
  not not_15 (not_15_out, OP1);
  not not_16 (not_16_out, OP0);
  not not_17 (not_17_out, F4);
  not not_18 (not_18_out, F3);
  not not_19 (not_19_out, F2);
  not not_20 (not_20_out, F1);
  not not_21 (not_21_out, F0);
  not not_22 (not_22_out, OP5);
  not not_23 (not_23_out, OP4);
  not not_24 (not_24_out, OP3);
  not not_25 (not_25_out, OP2);
  not not_26 (not_26_out, OP1);
  not not_27 (not_27_out, OP0);
  not not_28 (not_28_out, F4);
  not not_29 (not_29_out, F3);
  not not_30 (not_30_out, F2);
  not not_31 (not_31_out, F1);
  not not_32 (not_32_out, OP5);
  not not_33 (not_33_out, OP4);
  not not_34 (not_34_out, OP3);
  not not_35 (not_35_out, OP2);
  not not_36 (not_36_out, OP1);
  not not_37 (not_37_out, OP0);
  not not_38 (not_38_out, F4);
  not not_39 (not_39_out, F3);
  not not_40 (not_40_out, F1);
  not not_41 (not_41_out, F0);
  not not_42 (not_42_out, OP5);
  not not_43 (not_43_out, OP4);
  not not_44 (not_44_out, OP3);
  not not_45 (not_45_out, OP2);
  not not_46 (not_46_out, OP1);
  not not_47 (not_47_out, OP0);
  not not_48 (not_48_out, F4);
  not not_49 (not_49_out, F2);
  not not_50 (not_50_out, F0);
  not not_51 (not_51_out, OP5);
  not not_52 (not_52_out, OP4);
  not not_53 (not_53_out, OP2);
  not not_54 (not_54_out, OP1);
  not not_55 (not_55_out, OP0);
  not not_56 (not_56_out, OP5);
  not not_57 (not_57_out, OP4);
  not not_58 (not_58_out, OP1);
  not not_59 (not_59_out, OP0);
  not not_60 (not_60_out, OP5);
  not not_61 (not_61_out, OP4);
  not not_62 (not_62_out, OP2);
  not not_63 (not_63_out, OP1);
  not not_64 (not_64_out, OP5);
  not not_65 (not_65_out, OP4);
  not not_66 (not_66_out, OP2);
  not not_67 (not_67_out, OP0);
  not not_68 (not_68_out, OP4);
  not not_69 (not_69_out, OP3);
  not not_70 (not_70_out, OP2);
  not not_71 (not_71_out, OP4);
  not not_72 (not_72_out, OP2);
  not not_73 (not_73_out, OP5);
  not not_74 (not_74_out, OP4);
  not not_75 (not_75_out, OP3);
  not not_76 (not_76_out, OP2);
  not not_77 (not_77_out, OP1);
  not not_78 (not_78_out, OP0);
  not not_79 (not_79_out, F4);
  not not_80 (not_80_out, F3);
  not not_81 (not_81_out, F0);
  not not_82 (not_82_out, OP4);
  not not_83 (not_83_out, OP3);
  not not_84 (not_84_out, OP1);
  not not_85 (not_85_out, OP5);
  not not_86 (not_86_out, OP4);
  not not_87 (not_87_out, OP3);
  not not_88 (not_88_out, OP0);
  not not_89 (not_89_out, OP5);
  not not_90 (not_90_out, OP4);
  not not_91 (not_91_out, OP3);
  not not_92 (not_92_out, OP2);
  not not_93 (not_93_out, OP1);
  not not_94 (not_94_out, OP0);
  not not_95 (not_95_out, F5);
  not not_96 (not_96_out, F4);
  not not_97 (not_97_out, F3);
  not not_98 (not_98_out, F2);
  not not_99 (not_99_out, F0);
  not not_100 (not_100_out, OP5);
  not not_101 (not_101_out, OP4);
  not not_102 (not_102_out, OP3);
  not not_103 (not_103_out, OP2);
  not not_104 (not_104_out, OP1);
  not not_105 (not_105_out, OP0);
  not not_106 (not_106_out, F4);
  not not_107 (not_107_out, F3);
  not not_108 (not_108_out, F2);
  not not_109 (not_109_out, F0);
  not not_110 (not_110_out, OP5);
  not not_111 (not_111_out, OP4);
  not not_112 (not_112_out, OP3);
  not not_113 (not_113_out, OP2);
  not not_114 (not_114_out, OP1);
  not not_115 (not_115_out, OP0);
  not not_116 (not_116_out, F4);
  not not_117 (not_117_out, F3);
  not not_118 (not_118_out, F1);
  not not_119 (not_119_out, F0);
  not not_120 (not_120_out, OP5);
  not not_121 (not_121_out, OP4);
  not not_122 (not_122_out, OP3);
  not not_123 (not_123_out, OP2);
  not not_124 (not_124_out, OP1);
  not not_125 (not_125_out, OP0);
  not not_126 (not_126_out, F4);
  not not_127 (not_127_out, F3);
  not not_128 (not_128_out, OP5);
  not not_129 (not_129_out, OP4);
  not not_130 (not_130_out, OP3);
  not not_131 (not_131_out, OP2);
  not not_132 (not_132_out, OP1);
  not not_133 (not_133_out, OP0);
  not not_134 (not_134_out, F4);
  not not_135 (not_135_out, F2);
  not not_136 (not_136_out, F0);
  not not_137 (not_137_out, OP5);
  not not_138 (not_138_out, OP4);
  not not_139 (not_139_out, OP1);
  not not_140 (not_140_out, OP0);
  not not_141 (not_141_out, OP5);
  not not_142 (not_142_out, OP4);
  not not_143 (not_143_out, OP2);
  not not_144 (not_144_out, OP0);
  not not_145 (not_145_out, OP5);
  not not_146 (not_146_out, OP4);
  not not_147 (not_147_out, OP3);
  not not_148 (not_148_out, OP0);
  not not_149 (not_149_out, OP5);
  not not_150 (not_150_out, OP4);
  not not_151 (not_151_out, OP3);
  not not_152 (not_152_out, OP2);
  not not_153 (not_153_out, OP1);
  not not_154 (not_154_out, OP0);
  not not_155 (not_155_out, F4);
  not not_156 (not_156_out, F3);
  not not_157 (not_157_out, F2);
  not not_158 (not_158_out, F1);
  not not_159 (not_159_out, F0);
  not not_160 (not_160_out, OP5);
  not not_161 (not_161_out, OP4);
  not not_162 (not_162_out, OP3);
  not not_163 (not_163_out, OP2);
  not not_164 (not_164_out, OP1);
  not not_165 (not_165_out, OP0);
  not not_166 (not_166_out, F4);
  not not_167 (not_167_out, F3);
  not not_168 (not_168_out, F2);
  not not_169 (not_169_out, F1);
  not not_170 (not_170_out, OP5);
  not not_171 (not_171_out, OP4);
  not not_172 (not_172_out, OP3);
  not not_173 (not_173_out, OP2);
  not not_174 (not_174_out, OP1);
  not not_175 (not_175_out, OP0);
  not not_176 (not_176_out, F4);
  not not_177 (not_177_out, F3);
  not not_178 (not_178_out, F2);
  not not_179 (not_179_out, F0);
  not not_180 (not_180_out, OP5);
  not not_181 (not_181_out, OP4);
  not not_182 (not_182_out, OP3);
  not not_183 (not_183_out, OP2);
  not not_184 (not_184_out, OP1);
  not not_185 (not_185_out, OP0);
  not not_186 (not_186_out, F4);
  not not_187 (not_187_out, F3);
  not not_188 (not_188_out, F1);
  not not_189 (not_189_out, F0);
  not not_190 (not_190_out, OP5);
  not not_191 (not_191_out, OP4);
  not not_192 (not_192_out, OP3);
  not not_193 (not_193_out, OP2);
  not not_194 (not_194_out, OP1);
  not not_195 (not_195_out, OP0);
  not not_196 (not_196_out, F4);
  not not_197 (not_197_out, F2);
  not not_198 (not_198_out, OP5);
  not not_199 (not_199_out, OP4);
  not not_200 (not_200_out, OP2);
  not not_201 (not_201_out, OP1);
  not not_202 (not_202_out, OP0);
  not not_203 (not_203_out, OP5);
  not not_204 (not_204_out, OP4);
  not not_205 (not_205_out, OP1);
  not not_206 (not_206_out, OP0);
  not not_207 (not_207_out, OP5);
  not not_208 (not_208_out, OP4);
  not not_209 (not_209_out, OP2);
  not not_210 (not_210_out, OP1);
  not not_211 (not_211_out, OP4);
  not not_212 (not_212_out, OP3);
  not not_213 (not_213_out, OP2);
  not not_214 (not_214_out, OP4);
  not not_215 (not_215_out, OP2);
  not not_216 (not_216_out, OP4);
  not not_217 (not_217_out, OP3);
  not not_218 (not_218_out, OP1);
  not not_219 (not_219_out, OP5);
  not not_220 (not_220_out, OP4);
  not not_221 (not_221_out, OP3);
  not not_222 (not_222_out, OP2);
  not not_223 (not_223_out, OP1);
  not not_224 (not_224_out, OP0);
  not not_225 (not_225_out, F4);
  not not_226 (not_226_out, F3);
  not not_227 (not_227_out, F1);
  not not_228 (not_228_out, OP5);
  not not_229 (not_229_out, OP4);
  not not_230 (not_230_out, OP3);
  not not_231 (not_231_out, OP2);
  not not_232 (not_232_out, OP1);
  not not_233 (not_233_out, OP0);
  not not_234 (not_234_out, F4);
  not not_235 (not_235_out, F3);
  not not_236 (not_236_out, OP5);
  not not_237 (not_237_out, OP4);
  not not_238 (not_238_out, OP3);
  not not_239 (not_239_out, OP2);
  not not_240 (not_240_out, OP1);
  not not_241 (not_241_out, OP0);
  not not_242 (not_242_out, F4);
  not not_243 (not_243_out, F3);
  not not_244 (not_244_out, F1);
  not not_245 (not_245_out, OP5);
  not not_246 (not_246_out, OP4);
  not not_247 (not_247_out, OP3);
  not not_248 (not_248_out, OP2);
  not not_249 (not_249_out, OP1);
  not not_250 (not_250_out, OP0);
  not not_251 (not_251_out, F4);
  not not_252 (not_252_out, F3);
  not not_253 (not_253_out, OP5);
  not not_254 (not_254_out, OP4);
  not not_255 (not_255_out, OP3);
  not not_256 (not_256_out, OP2);
  not not_257 (not_257_out, OP1);
  not not_258 (not_258_out, OP0);
  not not_259 (not_259_out, F4);
  not not_260 (not_260_out, F2);
  not not_261 (not_261_out, F0);
  not not_262 (not_262_out, OP5);
  not not_263 (not_263_out, OP4);
  not not_264 (not_264_out, OP3);
  not not_265 (not_265_out, OP2);
  not not_266 (not_266_out, OP1);
  not not_267 (not_267_out, OP0);
  not not_268 (not_268_out, F4);
  not not_269 (not_269_out, F2);
  not not_270 (not_270_out, OP5);
  not not_271 (not_271_out, OP4);
  not not_272 (not_272_out, OP2);
  not not_273 (not_273_out, OP0);
  not not_274 (not_274_out, OP5);
  not not_275 (not_275_out, OP4);
  not not_276 (not_276_out, OP1);
  not not_277 (not_277_out, OP5);
  not not_278 (not_278_out, OP4);
  not not_279 (not_279_out, OP3);
  not not_280 (not_280_out, OP2);
  not not_281 (not_281_out, OP1);
  not not_282 (not_282_out, OP0);
  not not_283 (not_283_out, F4);
  not not_284 (not_284_out, F3);
  not not_285 (not_285_out, F0);
  not not_286 (not_286_out, OP5);
  not not_287 (not_287_out, OP4);
  not not_288 (not_288_out, OP3);
  not not_289 (not_289_out, OP0);
  and and_1 (and_1_out, not_1_out, not_2_out, not_3_out, not_4_out, not_5_out, not_6_out, not_7_out, not_8_out, not_9_out, not_10_out, F1, F0);
  and and_2 (and_2_out, not_11_out, not_12_out, not_13_out, not_14_out, not_15_out, not_16_out, F5, not_17_out, not_18_out, not_19_out, not_20_out, not_21_out);
  and and_3 (and_3_out, not_22_out, not_23_out, not_24_out, not_25_out, not_26_out, not_27_out, F5, not_28_out, not_29_out, not_30_out, not_31_out, F0);
  and and_4 (and_4_out, not_32_out, not_33_out, not_34_out, not_35_out, not_36_out, not_37_out, F5, not_38_out, not_39_out, F2, not_40_out, not_41_out);
  and and_5 (and_5_out, not_42_out, not_43_out, not_44_out, not_45_out, not_46_out, not_47_out, F5, not_48_out, F3, not_49_out, F1, not_50_out);
  and and_6 (and_6_out, not_51_out, not_52_out, OP3, not_53_out, not_54_out, not_55_out);
  and and_7 (and_7_out, not_56_out, not_57_out, OP3, OP2, not_58_out, not_59_out);
  and and_8 (and_8_out, not_60_out, not_61_out, OP3, not_62_out, not_63_out, OP0);
  and and_9 (and_9_out, not_64_out, not_65_out, OP3, not_66_out, OP1, not_67_out);
  and and_10 (and_10_out, OP5, not_68_out, not_69_out, not_70_out, OP1, OP0);
  and and_11 (and_11_out, OP5, not_71_out, OP3, not_72_out, OP1, OP0);
  and and_12 (and_12_out, not_73_out, not_74_out, not_75_out, not_76_out, not_77_out, not_78_out, F5, not_79_out, not_80_out, F2, F1, not_81_out);
  and and_13 (and_13_out, OP5, not_82_out, not_83_out, OP2, not_84_out, OP0);
  and and_14 (and_14_out, not_85_out, not_86_out, not_87_out, OP2, OP1, not_88_out);
  and and_15 (and_15_out, not_89_out, not_90_out, not_91_out, not_92_out, not_93_out, not_94_out, not_95_out, not_96_out, not_97_out, not_98_out, F1, not_99_out);
  and and_16 (and_16_out, not_100_out, not_101_out, not_102_out, not_103_out, not_104_out, not_105_out, F5, not_106_out, not_107_out, not_108_out, F1, not_109_out);
  and and_17 (and_17_out, not_110_out, not_111_out, not_112_out, not_113_out, not_114_out, not_115_out, F5, not_116_out, not_117_out, F2, not_118_out, not_119_out);
  and and_18 (and_18_out, not_120_out, not_121_out, not_122_out, not_123_out, not_124_out, not_125_out, F5, not_126_out, not_127_out, F2, F1, F0);
  and and_19 (and_19_out, not_128_out, not_129_out, not_130_out, not_131_out, not_132_out, not_133_out, F5, not_134_out, F3, not_135_out, F1, not_136_out);
  and and_20 (and_20_out, not_137_out, not_138_out, OP3, OP2, not_139_out, not_140_out);
  and and_21 (and_21_out, not_141_out, not_142_out, OP3, not_143_out, OP1, not_144_out);
  and and_22 (and_22_out, not_145_out, not_146_out, not_147_out, OP2, OP1, not_148_out);
  and and_23 (and_23_out, not_149_out, not_150_out, not_151_out, not_152_out, not_153_out, not_154_out, F5, not_155_out, not_156_out, not_157_out, not_158_out, not_159_out);
  and and_24 (and_24_out, not_160_out, not_161_out, not_162_out, not_163_out, not_164_out, not_165_out, F5, not_166_out, not_167_out, not_168_out, not_169_out, F0);
  and and_25 (and_25_out, not_170_out, not_171_out, not_172_out, not_173_out, not_174_out, not_175_out, F5, not_176_out, not_177_out, not_178_out, F1, not_179_out);
  and and_26 (and_26_out, not_180_out, not_181_out, not_182_out, not_183_out, not_184_out, not_185_out, F5, not_186_out, not_187_out, F2, not_188_out, not_189_out);
  and and_27 (and_27_out, not_190_out, not_191_out, not_192_out, not_193_out, not_194_out, not_195_out, F5, not_196_out, F3, not_197_out, F1, F0);
  and and_28 (and_28_out, not_198_out, not_199_out, OP3, not_200_out, not_201_out, not_202_out);
  and and_29 (and_29_out, not_203_out, not_204_out, OP3, OP2, not_205_out, not_206_out);
  and and_30 (and_30_out, not_207_out, not_208_out, OP3, not_209_out, not_210_out, OP0);
  and and_31 (and_31_out, OP5, not_211_out, not_212_out, not_213_out, OP1, OP0);
  and and_32 (and_32_out, OP5, not_214_out, OP3, not_215_out, OP1, OP0);
  and and_33 (and_33_out, OP5, not_216_out, not_217_out, OP2, not_218_out, OP0);
  and and_34 (and_34_out, not_219_out, not_220_out, not_221_out, not_222_out, not_223_out, not_224_out, F5, not_225_out, not_226_out, F2, not_227_out, F0);
  and and_35 (and_35_out, not_228_out, not_229_out, not_230_out, not_231_out, not_232_out, not_233_out, F5, not_234_out, not_235_out, F2, F1, F0);
  and and_36 (and_36_out, not_236_out, not_237_out, not_238_out, not_239_out, not_240_out, not_241_out, F5, not_242_out, not_243_out, F2, not_244_out, F0);
  and and_37 (and_37_out, not_245_out, not_246_out, not_247_out, not_248_out, not_249_out, not_250_out, F5, not_251_out, not_252_out, F2, F1, F0);
  and and_38 (and_38_out, not_253_out, not_254_out, not_255_out, not_256_out, not_257_out, not_258_out, F5, not_259_out, F3, not_260_out, F1, not_261_out);
  and and_39 (and_39_out, not_262_out, not_263_out, not_264_out, not_265_out, not_266_out, not_267_out, F5, not_268_out, F3, not_269_out, F1, F0);
  and and_40 (and_40_out, not_270_out, not_271_out, OP3, not_272_out, OP1, not_273_out);
  and and_41 (and_41_out, not_274_out, not_275_out, OP3, OP2, not_276_out, OP0);
  and and_42 (and_42_out, not_277_out, not_278_out, not_279_out, not_280_out, not_281_out, not_282_out, F5, not_283_out, not_284_out, F2, F1, not_285_out);
  and and_43 (and_43_out, not_286_out, not_287_out, not_288_out, OP2, OP1, not_289_out);
  or or_1 (S1, and_15_out, and_16_out, and_17_out, and_18_out, and_19_out, and_20_out, and_21_out, and_22_out);
  or or_2 (S0, and_1_out, and_2_out, and_3_out, and_4_out, and_5_out, and_6_out, and_7_out, and_8_out, and_9_out, and_10_out, and_11_out, and_12_out, and_13_out, and_14_out);
  or or_3 (S2, and_23_out, and_24_out, and_25_out, and_26_out, and_27_out, and_28_out, and_29_out, and_30_out, and_31_out, and_32_out, and_33_out);
  or or_4 (S3, and_34_out, and_35_out, and_36_out, and_37_out, and_38_out, and_39_out, and_40_out, and_41_out, and_42_out, and_43_out);
endmodule

// 控制信号生成
module \控制信号生成  (
  input  OP0,
  input  OP1,
  input  OP2,
  input  OP3,
  input  OP4,
  input  OP5,
  input  F0,
  input  F1,
  input  F2,
  input  F3,
  input  F4,
  input  F5,
  output MemToReg,
  output MemWrite,
  output ALU_SRCB_1,
  output RegWrite,
  output SysCALL,
  output SignedExt,
  output RegDst,
  output BEQ,
  output BNE,
  output JR,
  output JMP,
  output JAL
);

  wire and_1_out, and_2_out, and_4_out, and_5_out, and_6_out, and_7_out, and_8_out, and_9_out, and_10_out,
       and_11_out, and_12_out, and_13_out, and_14_out, and_15_out, and_16_out, and_17_out, and_18_out,
       and_19_out, and_20_out, and_21_out, and_22_out, and_23_out, and_24_out, and_25_out, and_26_out,
       and_27_out, and_28_out, and_29_out, and_30_out, and_31_out, and_32_out, and_33_out, and_35_out,
       and_36_out, and_37_out, and_38_out, and_39_out, and_40_out, and_41_out, and_42_out, and_43_out,
       and_44_out, and_45_out, and_46_out, and_47_out, and_48_out, and_49_out, and_50_out, and_51_out,
       and_52_out, and_56_out, and_57_out, not_1_out, not_2_out, not_3_out, not_4_out, not_5_out, not_6_out,
       not_7_out, not_8_out, not_9_out, not_10_out, not_11_out, not_12_out, not_13_out, not_14_out,
       not_15_out, not_16_out, not_17_out, not_18_out, not_19_out, not_20_out, not_21_out, not_22_out,
       not_23_out, not_24_out, not_25_out, not_26_out, not_27_out, not_28_out, not_29_out, not_30_out,
       not_31_out, not_32_out, not_33_out, not_34_out, not_35_out, not_36_out, not_37_out, not_38_out,
       not_39_out, not_40_out, not_41_out, not_42_out, not_43_out, not_44_out, not_45_out, not_46_out,
       not_47_out, not_48_out, not_49_out, not_50_out, not_51_out, not_52_out, not_53_out, not_54_out,
       not_55_out, not_56_out, not_57_out, not_58_out, not_59_out, not_60_out, not_61_out, not_62_out,
       not_63_out, not_64_out, not_65_out, not_66_out, not_67_out, not_68_out, not_69_out, not_70_out,
       not_71_out, not_72_out, not_73_out, not_74_out, not_75_out, not_76_out, not_77_out, not_78_out,
       not_79_out, not_80_out, not_81_out, not_82_out, not_83_out, not_84_out, not_85_out, not_86_out,
       not_87_out, not_88_out, not_89_out, not_90_out, not_91_out, not_92_out, not_93_out, not_94_out,
       not_95_out, not_96_out, not_97_out, not_98_out, not_99_out, not_100_out, not_101_out, not_102_out,
       not_103_out, not_104_out, not_105_out, not_106_out, not_107_out, not_108_out, not_109_out,
       not_110_out, not_111_out, not_112_out, not_113_out, not_114_out, not_115_out, not_116_out,
       not_117_out, not_118_out, not_119_out, not_120_out, not_121_out, not_122_out, not_123_out,
       not_124_out, not_125_out, not_126_out, not_127_out, not_128_out, not_129_out, not_130_out,
       not_131_out, not_132_out, not_133_out, not_134_out, not_135_out, not_136_out, not_137_out,
       not_138_out, not_139_out, not_140_out, not_141_out, not_142_out, not_143_out, not_144_out,
       not_145_out, not_146_out, not_147_out, not_148_out, not_149_out, not_150_out, not_151_out,
       not_152_out, not_153_out, not_154_out, not_155_out, not_156_out, not_157_out, not_158_out,
       not_159_out, not_160_out, not_161_out, not_162_out, not_163_out, not_164_out, not_165_out,
       not_166_out, not_167_out, not_168_out, not_169_out, not_170_out, not_171_out, not_172_out,
       not_173_out, not_174_out, not_175_out, not_176_out, not_177_out, not_178_out, not_179_out,
       not_180_out, not_181_out, not_182_out, not_183_out, not_184_out, not_185_out, not_186_out,
       not_187_out, not_188_out, not_189_out, not_190_out, not_191_out, not_192_out, not_193_out,
       not_194_out, not_195_out, not_196_out, not_197_out, not_198_out, not_199_out, not_200_out,
       not_201_out, not_202_out, not_203_out, not_204_out, not_205_out, not_206_out, not_207_out,
       not_208_out, not_209_out, not_210_out, not_211_out, not_212_out, not_213_out, not_214_out,
       not_215_out, not_216_out, not_217_out, not_218_out, not_219_out, not_220_out, not_221_out,
       not_222_out, not_223_out, not_224_out, not_225_out, not_226_out, not_227_out, not_228_out,
       not_229_out, not_230_out, not_231_out, not_232_out, not_233_out, not_234_out, not_235_out,
       not_236_out, not_237_out, not_238_out, not_239_out, not_240_out, not_241_out, not_242_out,
       not_243_out, not_244_out, not_245_out, not_246_out, not_247_out, not_248_out, not_249_out,
       not_250_out, not_251_out, not_252_out, not_253_out, not_254_out, not_255_out, not_256_out,
       not_257_out, not_258_out, not_259_out, not_260_out, not_261_out, not_262_out, not_263_out,
       not_264_out, not_265_out, not_266_out, not_267_out, not_268_out, not_269_out, not_270_out,
       not_271_out, not_272_out, not_273_out, not_274_out, not_275_out, not_276_out, not_277_out,
       not_278_out, not_279_out, not_280_out, not_281_out, not_282_out, not_283_out, not_284_out,
       not_285_out, not_286_out, not_287_out, not_288_out, not_289_out, not_290_out, not_291_out,
       not_292_out, not_293_out, not_294_out, not_295_out, not_296_out, not_297_out, not_298_out,
       not_299_out, not_300_out, not_301_out, not_302_out, not_303_out, not_304_out, not_305_out,
       not_306_out, not_307_out, not_308_out, not_309_out, not_310_out, not_311_out, not_312_out,
       not_313_out, not_314_out, not_315_out, not_316_out, not_317_out, not_318_out, not_319_out,
       not_320_out, not_321_out, not_322_out, not_323_out, not_324_out, not_325_out, not_326_out,
       not_327_out, not_328_out, not_329_out, not_330_out, not_331_out, not_332_out, not_333_out,
       not_334_out, not_335_out, not_336_out, not_337_out, not_338_out, not_339_out, not_340_out,
       not_341_out, not_342_out, not_343_out, not_344_out, not_345_out, not_346_out, not_347_out,
       not_348_out, not_349_out, not_350_out, not_351_out, not_352_out, not_353_out, not_354_out,
       not_355_out, not_356_out, not_357_out, not_358_out, not_359_out, not_360_out, not_361_out,
       not_362_out, not_363_out, not_364_out, not_365_out, not_366_out, not_367_out, not_368_out;

  not not_1 (not_1_out, OP4);
  not not_2 (not_2_out, OP3);
  not not_3 (not_3_out, OP2);
  not not_4 (not_4_out, OP4);
  not not_5 (not_5_out, OP3);
  not not_6 (not_6_out, OP1);
  not not_7 (not_7_out, OP4);
  not not_8 (not_8_out, OP2);
  not not_9 (not_9_out, OP5);
  not not_10 (not_10_out, OP4);
  not not_11 (not_11_out, OP2);
  not not_12 (not_12_out, OP1);
  not not_13 (not_13_out, OP0);
  not not_14 (not_14_out, OP5);
  not not_15 (not_15_out, OP4);
  not not_16 (not_16_out, OP1);
  not not_17 (not_17_out, OP0);
  not not_18 (not_18_out, OP5);
  not not_19 (not_19_out, OP4);
  not not_20 (not_20_out, OP2);
  not not_21 (not_21_out, OP1);
  not not_22 (not_22_out, OP5);
  not not_23 (not_23_out, OP4);
  not not_24 (not_24_out, OP2);
  not not_25 (not_25_out, OP0);
  not not_26 (not_26_out, OP5);
  not not_27 (not_27_out, OP4);
  not not_28 (not_28_out, OP1);
  not not_29 (not_29_out, OP4);
  not not_30 (not_30_out, OP3);
  not not_31 (not_31_out, OP2);
  not not_32 (not_32_out, OP4);
  not not_33 (not_33_out, OP2);
  not not_34 (not_34_out, OP5);
  not not_35 (not_35_out, OP4);
  not not_36 (not_36_out, OP4);
  not not_37 (not_37_out, OP3);
  not not_38 (not_38_out, OP1);
  not not_39 (not_39_out, OP5);
  not not_40 (not_40_out, OP4);
  not not_41 (not_41_out, OP3);
  not not_42 (not_42_out, OP2);
  not not_43 (not_43_out, OP1);
  not not_44 (not_44_out, OP0);
  not not_45 (not_45_out, F5);
  not not_46 (not_46_out, F4);
  not not_47 (not_47_out, F3);
  not not_48 (not_48_out, F2);
  not not_49 (not_49_out, F1);
  not not_50 (not_50_out, F0);
  not not_51 (not_51_out, OP5);
  not not_52 (not_52_out, OP4);
  not not_53 (not_53_out, OP3);
  not not_54 (not_54_out, OP2);
  not not_55 (not_55_out, OP1);
  not not_56 (not_56_out, OP0);
  not not_57 (not_57_out, F5);
  not not_58 (not_58_out, F4);
  not not_59 (not_59_out, F3);
  not not_60 (not_60_out, F2);
  not not_61 (not_61_out, OP5);
  not not_62 (not_62_out, OP4);
  not not_63 (not_63_out, OP3);
  not not_64 (not_64_out, OP2);
  not not_65 (not_65_out, OP1);
  not not_66 (not_66_out, OP0);
  not not_67 (not_67_out, F5);
  not not_68 (not_68_out, F4);
  not not_69 (not_69_out, F3);
  not not_70 (not_70_out, F2);
  not not_71 (not_71_out, F0);
  not not_72 (not_72_out, OP5);
  not not_73 (not_73_out, OP4);
  not not_74 (not_74_out, OP3);
  not not_75 (not_75_out, OP2);
  not not_76 (not_76_out, OP1);
  not not_77 (not_77_out, OP0);
  not not_78 (not_78_out, F4);
  not not_79 (not_79_out, F3);
  not not_80 (not_80_out, F2);
  not not_81 (not_81_out, F1);
  not not_82 (not_82_out, F0);
  not not_83 (not_83_out, OP5);
  not not_84 (not_84_out, OP4);
  not not_85 (not_85_out, OP3);
  not not_86 (not_86_out, OP2);
  not not_87 (not_87_out, OP1);
  not not_88 (not_88_out, OP0);
  not not_89 (not_89_out, F4);
  not not_90 (not_90_out, F3);
  not not_91 (not_91_out, F2);
  not not_92 (not_92_out, F1);
  not not_93 (not_93_out, OP5);
  not not_94 (not_94_out, OP4);
  not not_95 (not_95_out, OP3);
  not not_96 (not_96_out, OP2);
  not not_97 (not_97_out, OP1);
  not not_98 (not_98_out, OP0);
  not not_99 (not_99_out, F4);
  not not_100 (not_100_out, F3);
  not not_101 (not_101_out, F2);
  not not_102 (not_102_out, F0);
  not not_103 (not_103_out, OP5);
  not not_104 (not_104_out, OP4);
  not not_105 (not_105_out, OP3);
  not not_106 (not_106_out, OP2);
  not not_107 (not_107_out, OP1);
  not not_108 (not_108_out, OP0);
  not not_109 (not_109_out, F4);
  not not_110 (not_110_out, F3);
  not not_111 (not_111_out, F1);
  not not_112 (not_112_out, F0);
  not not_113 (not_113_out, OP5);
  not not_114 (not_114_out, OP4);
  not not_115 (not_115_out, OP3);
  not not_116 (not_116_out, OP2);
  not not_117 (not_117_out, OP1);
  not not_118 (not_118_out, OP0);
  not not_119 (not_119_out, F4);
  not not_120 (not_120_out, F3);
  not not_121 (not_121_out, F1);
  not not_122 (not_122_out, OP5);
  not not_123 (not_123_out, OP4);
  not not_124 (not_124_out, OP3);
  not not_125 (not_125_out, OP2);
  not not_126 (not_126_out, OP1);
  not not_127 (not_127_out, OP0);
  not not_128 (not_128_out, F4);
  not not_129 (not_129_out, F3);
  not not_130 (not_130_out, OP5);
  not not_131 (not_131_out, OP4);
  not not_132 (not_132_out, OP3);
  not not_133 (not_133_out, OP2);
  not not_134 (not_134_out, OP1);
  not not_135 (not_135_out, OP0);
  not not_136 (not_136_out, F4);
  not not_137 (not_137_out, F2);
  not not_138 (not_138_out, F0);
  not not_139 (not_139_out, OP5);
  not not_140 (not_140_out, OP4);
  not not_141 (not_141_out, OP3);
  not not_142 (not_142_out, OP2);
  not not_143 (not_143_out, OP1);
  not not_144 (not_144_out, OP0);
  not not_145 (not_145_out, F4);
  not not_146 (not_146_out, F2);
  not not_147 (not_147_out, OP5);
  not not_148 (not_148_out, OP4);
  not not_149 (not_149_out, OP3);
  not not_150 (not_150_out, OP2);
  not not_151 (not_151_out, OP5);
  not not_152 (not_152_out, OP4);
  not not_153 (not_153_out, OP2);
  not not_154 (not_154_out, OP1);
  not not_155 (not_155_out, OP0);
  not not_156 (not_156_out, OP5);
  not not_157 (not_157_out, OP4);
  not not_158 (not_158_out, OP1);
  not not_159 (not_159_out, OP0);
  not not_160 (not_160_out, OP5);
  not not_161 (not_161_out, OP4);
  not not_162 (not_162_out, OP2);
  not not_163 (not_163_out, OP1);
  not not_164 (not_164_out, OP5);
  not not_165 (not_165_out, OP4);
  not not_166 (not_166_out, OP2);
  not not_167 (not_167_out, OP0);
  not not_168 (not_168_out, OP5);
  not not_169 (not_169_out, OP4);
  not not_170 (not_170_out, OP1);
  not not_171 (not_171_out, OP4);
  not not_172 (not_172_out, OP3);
  not not_173 (not_173_out, OP2);
  not not_174 (not_174_out, OP5);
  not not_175 (not_175_out, OP4);
  not not_176 (not_176_out, OP3);
  not not_177 (not_177_out, OP2);
  not not_178 (not_178_out, OP1);
  not not_179 (not_179_out, OP0);
  not not_180 (not_180_out, F4);
  not not_181 (not_181_out, F3);
  not not_182 (not_182_out, F0);
  not not_183 (not_183_out, OP5);
  not not_184 (not_184_out, OP4);
  not not_185 (not_185_out, OP4);
  not not_186 (not_186_out, OP3);
  not not_187 (not_187_out, OP1);
  not not_188 (not_188_out, OP5);
  not not_189 (not_189_out, OP4);
  not not_190 (not_190_out, OP3);
  not not_191 (not_191_out, OP2);
  not not_192 (not_192_out, OP1);
  not not_193 (not_193_out, OP0);
  not not_194 (not_194_out, F5);
  not not_195 (not_195_out, F4);
  not not_196 (not_196_out, F1);
  not not_197 (not_197_out, F0);
  not not_198 (not_198_out, OP5);
  not not_199 (not_199_out, OP4);
  not not_200 (not_200_out, OP2);
  not not_201 (not_201_out, OP1);
  not not_202 (not_202_out, OP0);
  not not_203 (not_203_out, OP5);
  not not_204 (not_204_out, OP4);
  not not_205 (not_205_out, OP2);
  not not_206 (not_206_out, OP1);
  not not_207 (not_207_out, OP5);
  not not_208 (not_208_out, OP4);
  not not_209 (not_209_out, OP2);
  not not_210 (not_210_out, OP0);
  not not_211 (not_211_out, OP4);
  not not_212 (not_212_out, OP3);
  not not_213 (not_213_out, OP2);
  not not_214 (not_214_out, OP4);
  not not_215 (not_215_out, OP2);
  not not_216 (not_216_out, OP4);
  not not_217 (not_217_out, OP3);
  not not_218 (not_218_out, OP1);
  not not_219 (not_219_out, OP5);
  not not_220 (not_220_out, OP4);
  not not_221 (not_221_out, OP3);
  not not_222 (not_222_out, OP2);
  not not_223 (not_223_out, OP1);
  not not_224 (not_224_out, OP0);
  not not_225 (not_225_out, F5);
  not not_226 (not_226_out, F4);
  not not_227 (not_227_out, F3);
  not not_228 (not_228_out, F2);
  not not_229 (not_229_out, F1);
  not not_230 (not_230_out, F0);
  not not_231 (not_231_out, OP5);
  not not_232 (not_232_out, OP4);
  not not_233 (not_233_out, OP3);
  not not_234 (not_234_out, OP2);
  not not_235 (not_235_out, OP1);
  not not_236 (not_236_out, OP0);
  not not_237 (not_237_out, F5);
  not not_238 (not_238_out, F4);
  not not_239 (not_239_out, F3);
  not not_240 (not_240_out, F2);
  not not_241 (not_241_out, OP5);
  not not_242 (not_242_out, OP4);
  not not_243 (not_243_out, OP3);
  not not_244 (not_244_out, OP2);
  not not_245 (not_245_out, OP1);
  not not_246 (not_246_out, OP0);
  not not_247 (not_247_out, F5);
  not not_248 (not_248_out, F4);
  not not_249 (not_249_out, F3);
  not not_250 (not_250_out, F2);
  not not_251 (not_251_out, F0);
  not not_252 (not_252_out, OP5);
  not not_253 (not_253_out, OP4);
  not not_254 (not_254_out, OP3);
  not not_255 (not_255_out, OP2);
  not not_256 (not_256_out, OP1);
  not not_257 (not_257_out, OP0);
  not not_258 (not_258_out, F4);
  not not_259 (not_259_out, F3);
  not not_260 (not_260_out, F2);
  not not_261 (not_261_out, F1);
  not not_262 (not_262_out, F0);
  not not_263 (not_263_out, OP5);
  not not_264 (not_264_out, OP4);
  not not_265 (not_265_out, OP3);
  not not_266 (not_266_out, OP2);
  not not_267 (not_267_out, OP1);
  not not_268 (not_268_out, OP0);
  not not_269 (not_269_out, F4);
  not not_270 (not_270_out, F3);
  not not_271 (not_271_out, F2);
  not not_272 (not_272_out, F1);
  not not_273 (not_273_out, OP5);
  not not_274 (not_274_out, OP4);
  not not_275 (not_275_out, OP3);
  not not_276 (not_276_out, OP2);
  not not_277 (not_277_out, OP1);
  not not_278 (not_278_out, OP0);
  not not_279 (not_279_out, F4);
  not not_280 (not_280_out, F3);
  not not_281 (not_281_out, F2);
  not not_282 (not_282_out, F0);
  not not_283 (not_283_out, OP5);
  not not_284 (not_284_out, OP4);
  not not_285 (not_285_out, OP3);
  not not_286 (not_286_out, OP2);
  not not_287 (not_287_out, OP1);
  not not_288 (not_288_out, OP0);
  not not_289 (not_289_out, F4);
  not not_290 (not_290_out, F3);
  not not_291 (not_291_out, F1);
  not not_292 (not_292_out, F0);
  not not_293 (not_293_out, OP5);
  not not_294 (not_294_out, OP4);
  not not_295 (not_295_out, OP3);
  not not_296 (not_296_out, OP2);
  not not_297 (not_297_out, OP1);
  not not_298 (not_298_out, OP0);
  not not_299 (not_299_out, F4);
  not not_300 (not_300_out, F3);
  not not_301 (not_301_out, F1);
  not not_302 (not_302_out, OP5);
  not not_303 (not_303_out, OP4);
  not not_304 (not_304_out, OP3);
  not not_305 (not_305_out, OP2);
  not not_306 (not_306_out, OP1);
  not not_307 (not_307_out, OP0);
  not not_308 (not_308_out, F4);
  not not_309 (not_309_out, F3);
  not not_310 (not_310_out, OP5);
  not not_311 (not_311_out, OP4);
  not not_312 (not_312_out, OP3);
  not not_313 (not_313_out, OP2);
  not not_314 (not_314_out, OP1);
  not not_315 (not_315_out, OP0);
  not not_316 (not_316_out, F4);
  not not_317 (not_317_out, F2);
  not not_318 (not_318_out, F0);
  not not_319 (not_319_out, OP5);
  not not_320 (not_320_out, OP4);
  not not_321 (not_321_out, OP3);
  not not_322 (not_322_out, OP2);
  not not_323 (not_323_out, OP1);
  not not_324 (not_324_out, OP0);
  not not_325 (not_325_out, F4);
  not not_326 (not_326_out, F2);
  not not_327 (not_327_out, OP5);
  not not_328 (not_328_out, OP4);
  not not_329 (not_329_out, OP3);
  not not_330 (not_330_out, OP2);
  not not_331 (not_331_out, OP1);
  not not_332 (not_332_out, OP0);
  not not_333 (not_333_out, F4);
  not not_334 (not_334_out, F3);
  not not_335 (not_335_out, F0);
  not not_336 (not_336_out, OP5);
  not not_337 (not_337_out, OP4);
  not not_338 (not_338_out, OP3);
  not not_339 (not_339_out, OP1);
  not not_340 (not_340_out, OP0);
  not not_341 (not_341_out, OP5);
  not not_342 (not_342_out, OP4);
  not not_343 (not_343_out, OP3);
  not not_344 (not_344_out, OP1);
  not not_345 (not_345_out, OP5);
  not not_346 (not_346_out, OP4);
  not not_347 (not_347_out, OP3);
  not not_348 (not_348_out, OP2);
  not not_349 (not_349_out, OP1);
  not not_350 (not_350_out, OP0);
  not not_351 (not_351_out, F5);
  not not_352 (not_352_out, F4);
  not not_353 (not_353_out, F2);
  not not_354 (not_354_out, F1);
  not not_355 (not_355_out, F0);
  not not_356 (not_356_out, OP5);
  not not_357 (not_357_out, OP4);
  not not_358 (not_358_out, OP3);
  not not_359 (not_359_out, OP2);
  not not_360 (not_360_out, OP0);
  not not_361 (not_361_out, OP5);
  not not_362 (not_362_out, OP4);
  not not_363 (not_363_out, OP3);
  not not_364 (not_364_out, OP2);
  not not_365 (not_365_out, OP5);
  not not_366 (not_366_out, OP4);
  not not_367 (not_367_out, OP3);
  not not_368 (not_368_out, OP2);
  and and_1 (and_1_out, OP5, not_1_out, not_2_out, not_3_out, OP1, OP0);
  and and_2 (and_2_out, OP5, not_4_out, not_5_out, OP2, not_6_out, OP0);
  and and_3 (MemWrite, OP5, not_7_out, OP3, not_8_out, OP1, OP0);
  and and_4 (and_4_out, not_9_out, not_10_out, OP3, not_11_out, not_12_out, not_13_out);
  and and_5 (and_5_out, not_14_out, not_15_out, OP3, OP2, not_16_out, not_17_out);
  and and_6 (and_6_out, not_18_out, not_19_out, OP3, not_20_out, not_21_out, OP0);
  and and_7 (and_7_out, not_22_out, not_23_out, OP3, not_24_out, OP1, not_25_out);
  and and_8 (and_8_out, not_26_out, not_27_out, OP3, OP2, not_28_out, OP0);
  and and_9 (and_9_out, OP5, not_29_out, not_30_out, not_31_out, OP1, OP0);
  and and_10 (and_10_out, OP5, not_32_out, OP3, not_33_out, OP1, OP0);
  and and_11 (and_11_out, not_34_out, not_35_out, OP3, OP2, OP1, OP0);
  and and_12 (and_12_out, OP5, not_36_out, not_37_out, OP2, not_38_out, OP0);
  and and_13 (and_13_out, not_39_out, not_40_out, not_41_out, not_42_out, not_43_out, not_44_out, not_45_out, not_46_out, not_47_out, not_48_out, not_49_out, not_50_out);
  and and_14 (and_14_out, not_51_out, not_52_out, not_53_out, not_54_out, not_55_out, not_56_out, not_57_out, not_58_out, not_59_out, not_60_out, F1, F0);
  and and_15 (and_15_out, not_61_out, not_62_out, not_63_out, not_64_out, not_65_out, not_66_out, not_67_out, not_68_out, not_69_out, not_70_out, F1, not_71_out);
  and and_16 (and_16_out, not_72_out, not_73_out, not_74_out, not_75_out, not_76_out, not_77_out, F5, not_78_out, not_79_out, not_80_out, not_81_out, not_82_out);
  and and_17 (and_17_out, not_83_out, not_84_out, not_85_out, not_86_out, not_87_out, not_88_out, F5, not_89_out, not_90_out, not_91_out, not_92_out, F0);
  and and_18 (and_18_out, not_93_out, not_94_out, not_95_out, not_96_out, not_97_out, not_98_out, F5, not_99_out, not_100_out, not_101_out, F1, not_102_out);
  and and_19 (and_19_out, not_103_out, not_104_out, not_105_out, not_106_out, not_107_out, not_108_out, F5, not_109_out, not_110_out, F2, not_111_out, not_112_out);
  and and_20 (and_20_out, not_113_out, not_114_out, not_115_out, not_116_out, not_117_out, not_118_out, F5, not_119_out, not_120_out, F2, not_121_out, F0);
  and and_21 (and_21_out, not_122_out, not_123_out, not_124_out, not_125_out, not_126_out, not_127_out, F5, not_128_out, not_129_out, F2, F1, F0);
  and and_22 (and_22_out, not_130_out, not_131_out, not_132_out, not_133_out, not_134_out, not_135_out, F5, not_136_out, F3, not_137_out, F1, not_138_out);
  and and_23 (and_23_out, not_139_out, not_140_out, not_141_out, not_142_out, not_143_out, not_144_out, F5, not_145_out, F3, not_146_out, F1, F0);
  and and_24 (and_24_out, not_147_out, not_148_out, not_149_out, not_150_out, OP1, OP0);
  and and_25 (and_25_out, not_151_out, not_152_out, OP3, not_153_out, not_154_out, not_155_out);
  and and_26 (and_26_out, not_156_out, not_157_out, OP3, OP2, not_158_out, not_159_out);
  and and_27 (and_27_out, not_160_out, not_161_out, OP3, not_162_out, not_163_out, OP0);
  and and_28 (and_28_out, not_164_out, not_165_out, OP3, not_166_out, OP1, not_167_out);
  and and_29 (and_29_out, not_168_out, not_169_out, OP3, OP2, not_170_out, OP0);
  and and_30 (and_30_out, OP5, not_171_out, not_172_out, not_173_out, OP1, OP0);
  and and_31 (and_31_out, not_174_out, not_175_out, not_176_out, not_177_out, not_178_out, not_179_out, F5, not_180_out, not_181_out, F2, F1, not_182_out);
  and and_32 (and_32_out, not_183_out, not_184_out, OP3, OP2, OP1, OP0);
  and and_33 (and_33_out, OP5, not_185_out, not_186_out, OP2, not_187_out, OP0);
  and and_34 (SysCALL, not_188_out, not_189_out, not_190_out, not_191_out, not_192_out, not_193_out, not_194_out, not_195_out, F3, F2, not_196_out, not_197_out);
  and and_35 (and_35_out, not_198_out, not_199_out, OP3, not_200_out, not_201_out, not_202_out);
  and and_36 (and_36_out, not_203_out, not_204_out, OP3, not_205_out, not_206_out, OP0);
  and and_37 (and_37_out, not_207_out, not_208_out, OP3, not_209_out, OP1, not_210_out);
  and and_38 (and_38_out, OP5, not_211_out, not_212_out, not_213_out, OP1, OP0);
  and and_39 (and_39_out, OP5, not_214_out, OP3, not_215_out, OP1, OP0);
  and and_40 (and_40_out, OP5, not_216_out, not_217_out, OP2, not_218_out, OP0);
  and and_41 (and_41_out, not_219_out, not_220_out, not_221_out, not_222_out, not_223_out, not_224_out, not_225_out, not_226_out, not_227_out, not_228_out, not_229_out, not_230_out);
  and and_42 (and_42_out, not_231_out, not_232_out, not_233_out, not_234_out, not_235_out, not_236_out, not_237_out, not_238_out, not_239_out, not_240_out, F1, F0);
  and and_43 (and_43_out, not_241_out, not_242_out, not_243_out, not_244_out, not_245_out, not_246_out, not_247_out, not_248_out, not_249_out, not_250_out, F1, not_251_out);
  and and_44 (and_44_out, not_252_out, not_253_out, not_254_out, not_255_out, not_256_out, not_257_out, F5, not_258_out, not_259_out, not_260_out, not_261_out, not_262_out);
  and and_45 (and_45_out, not_263_out, not_264_out, not_265_out, not_266_out, not_267_out, not_268_out, F5, not_269_out, not_270_out, not_271_out, not_272_out, F0);
  and and_46 (and_46_out, not_273_out, not_274_out, not_275_out, not_276_out, not_277_out, not_278_out, F5, not_279_out, not_280_out, not_281_out, F1, not_282_out);
  and and_47 (and_47_out, not_283_out, not_284_out, not_285_out, not_286_out, not_287_out, not_288_out, F5, not_289_out, not_290_out, F2, not_291_out, not_292_out);
  and and_48 (and_48_out, not_293_out, not_294_out, not_295_out, not_296_out, not_297_out, not_298_out, F5, not_299_out, not_300_out, F2, not_301_out, F0);
  and and_49 (and_49_out, not_302_out, not_303_out, not_304_out, not_305_out, not_306_out, not_307_out, F5, not_308_out, not_309_out, F2, F1, F0);
  and and_50 (and_50_out, not_310_out, not_311_out, not_312_out, not_313_out, not_314_out, not_315_out, F5, not_316_out, F3, not_317_out, F1, not_318_out);
  and and_51 (and_51_out, not_319_out, not_320_out, not_321_out, not_322_out, not_323_out, not_324_out, F5, not_325_out, F3, not_326_out, F1, F0);
  and and_52 (and_52_out, not_327_out, not_328_out, not_329_out, not_330_out, not_331_out, not_332_out, F5, not_333_out, not_334_out, F2, F1, not_335_out);
  and and_53 (BEQ, not_336_out, not_337_out, not_338_out, OP2, not_339_out, not_340_out);
  and and_54 (BNE, not_341_out, not_342_out, not_343_out, OP2, not_344_out, OP0);
  and and_55 (JR, not_345_out, not_346_out, not_347_out, not_348_out, not_349_out, not_350_out, not_351_out, not_352_out, F3, not_353_out, not_354_out, not_355_out);
  and and_56 (and_56_out, not_356_out, not_357_out, not_358_out, not_359_out, OP1, not_360_out);
  and and_57 (and_57_out, not_361_out, not_362_out, not_363_out, not_364_out, OP1, OP0);
  and and_58 (JAL, not_365_out, not_366_out, not_367_out, not_368_out, OP1, OP0);
  or or_1 (MemToReg, and_1_out, and_2_out);
  or or_2 (ALU_SRCB_1, and_4_out, and_5_out, and_6_out, and_7_out, and_8_out, and_9_out, and_10_out, and_11_out, and_12_out);
  or or_3 (SignedExt, and_35_out, and_36_out, and_37_out, and_38_out, and_39_out, and_40_out);
  or or_4 (JMP, and_56_out, and_57_out);
  or or_5 (RegWrite, and_13_out, and_14_out, and_15_out, and_16_out, and_17_out, and_18_out, and_19_out, and_20_out, and_21_out, and_22_out, and_23_out, and_24_out, and_25_out, and_26_out, and_27_out, and_28_out, and_29_out, and_30_out, and_31_out, and_32_out, and_33_out);
  or or_6 (RegDst, and_41_out, and_42_out, and_43_out, and_44_out, and_45_out, and_46_out, and_47_out, and_48_out, and_49_out, and_50_out, and_51_out, and_52_out);
endmodule

// ALU
module MIPS_ALU (
  input  [4:0] shamt,
  input  [31:0] X,
  input  [31:0] Y,
  input  [3:0] AluOP,
  output Equal,
  output [31:0] Result,
  output [31:0] Result_2
);

  wire [0:0] comparator_1_lt, comparator_2_lt;
  wire [31:0] adder_1_out, AND_out, divider_1_out, divider_1_rem, multiplier_1_cout, multiplier_1_out,
       NOR_out, OR_out, shifter_1_out, shifter_2_out, shifter_3_out, subtractor_1_out, XOR_out;

  assign AND_out = X & Y;  // AND_Gate AND, 32 bits wide
  assign OR_out = X | Y;  // OR_Gate OR, 32 bits wide
  Shifter #(.width(32)) shifter_1 (.in(Y), .\dist (shamt), .out(shifter_1_out));
  Shifter #(.width(32), .shift("ar")) shifter_2 (.in(Y), .\dist (shamt), .out(shifter_2_out));
  Shifter #(.width(32), .shift("lr")) shifter_3 (.in(Y), .\dist (shamt), .out(shifter_3_out));
  Multiplier #(.width(32)) multiplier_1 (.a(X), .b(Y), .out(multiplier_1_out), .cout(multiplier_1_cout));  // open: cin
  Divider #(.width(32)) divider_1 (.a(X), .b(Y), .out(divider_1_out), .rem(divider_1_rem));  // open: upper
  Adder #(.width(32)) adder_1 (.a(X), .b(Y), .out(adder_1_out));  // open: cin, cout
  Subtractor #(.width(32)) subtractor_1 (.a(X), .b(Y), .out(subtractor_1_out));  // open: bin, bout
  assign XOR_out = X ^ Y;  // XOR_Gate XOR, 32 bits wide
  assign NOR_out = ~(X | Y);  // NOR_Gate NOR, 32 bits wide
  Comparator #(.width(32)) comparator_1 (.a(X), .b(Y), .eq(Equal), .lt(comparator_1_lt[0]));  // open: gt
  Comparator #(.width(32), .mode("unsigned")) comparator_2 (.a(X), .b(Y), .lt(comparator_2_lt[0]));  // open: gt, eq
  Multiplexer #(.select(4), .width(32), .enable("false")) multiplexer_1 (
    .in0(shifter_1_out), .in1(shifter_2_out), .in2(shifter_3_out), .in3(multiplier_1_out),
    .in4(divider_1_out), .in5(adder_1_out), .in6(subtractor_1_out), .in7(AND_out), .in8(OR_out),
    .in9(XOR_out), .in10(NOR_out), .in11({{31{1'b0}}, comparator_1_lt[0]}),
    .in12({{31{1'b0}}, comparator_2_lt[0]}), .in13({32{1'b0}}), .in14({32{1'b0}}), .in15({32{1'b0}}),
    .out(Result), .sel(AluOP));
  Multiplexer #(.select(4), .width(32), .enable("false")) multiplexer_2 (
    .in0({32{1'b0}}), .in1({32{1'b0}}), .in2({32{1'b0}}), .in3(multiplier_1_cout), .in4(divider_1_rem),
    .in5({32{1'b0}}), .in6({32{1'b0}}), .in7({32{1'b0}}), .in8({32{1'b0}}), .in9({32{1'b0}}),
    .in10({32{1'b0}}), .in11({32{1'b0}}), .in12({32{1'b0}}), .in13({32{1'b0}}), .in14({32{1'b0}}),
    .in15({32{1'b0}}), .out(Result_2), .sel(AluOP));

  // Other names for the same wires on the sheet: Result2[31:0] = Result_2; S[3:0] = AluOP

  // Notes on the sheet:
  //   不要改变此引脚区域内容，也不要改变ALU封装形式
  //   输入引脚
  //   输出引脚
endmodule

module MIPS_Regifile (
  input  [31:0] Din,
  input  Clk,
  input  WE,
  input  [4:0] R1_num,
  input  [4:0] W_num,
  input  [4:0] R2_num,
  output [31:0] R1,
  output [31:0] R2
);

  // RegisterFile registerfile_1: pin names not known; wires that end beside it: Din, Clk, WE, W_num, R1_num, R2_num, R1, R2
endmodule

module IF_ID (
  input  [31:0] PCin,
  input  [31:0] IRin,
  input  [31:0] PC_4in,
  input  [31:0] \预测in ,
  input  CLK,
  input  \同步清零 ,
  input  \使能端 ,
  output [31:0] PCout,
  output [31:0] IRout,
  output [31:0] PC_4out,
  output [31:0] \预测out 
);

  wire not_1_out;
  wire [31:0] multiplexer_1_out, multiplexer_2_out, multiplexer_3_out, multiplexer_4_out;

  Multiplexer #(.width(32), .enable("false")) multiplexer_1 (
    .in0(PCin), .in1({32{1'b0}}), .out(multiplexer_1_out), .sel(\同步清零 ));
  Multiplexer #(.width(32), .enable("false")) multiplexer_2 (
    .in0(IRin), .in1({32{1'b0}}), .out(multiplexer_2_out), .sel(\同步清零 ));
  Multiplexer #(.width(32), .enable("false")) multiplexer_3 (
    .in0(PC_4in), .in1({32{1'b0}}), .out(multiplexer_3_out), .sel(\同步清零 ));
  Multiplexer #(.width(32), .enable("false")) multiplexer_4 (
    .in0(\预测in ), .in1({32{1'b0}}), .out(multiplexer_4_out), .sel(\同步清零 ));
  not not_1 (not_1_out, \使能端 );
  Register #(.width(32)) register_1 (.D(multiplexer_1_out), .en(not_1_out), .Q(PCout), .clk(CLK));  // open: clr
  Register #(.width(32)) register_2 (.D(multiplexer_2_out), .en(not_1_out), .Q(IRout), .clk(CLK));  // open: clr
  Register #(.width(32)) register_3 (.D(multiplexer_3_out), .en(not_1_out), .Q(PC_4out), .clk(CLK));  // open: clr
  Register #(.width(32)) register_4 (.D(multiplexer_4_out), .en(not_1_out), .Q(\预测out ), .clk(CLK));  // open: clr
endmodule

module ID_EX (
  input  Beqin,
  input  Bnein,
  input  JMPin,
  input  JRin,
  input  [31:0] PC_4in,
  input  JALin,
  input  MemToRegin,
  input  MemWritein,
  input  [3:0] AluOPin,
  input  AluSrcin,
  input  RegWritein,
  input  [4:0] WriteRegin,
  input  [31:0] PCin,
  input  [31:0] IRin,
  input  [31:0] Ain,
  input  [31:0] Bin,
  input  [31:0] IMMin,
  input  [31:0] EIMMin,
  input  Systemcallin,
  input  [4:0] Shamtin,
  input  [1:0] ID_ChooseA,
  input  [1:0] ID_ChooseB,
  input  [31:0] \预测in ,
  input  ID_LHU,
  input  ID_BLEZ,
  input  CLK,
  input  \同步清零 ,
  input  \使能端 ,
  output Beqout,
  output Bneout,
  output JMPout,
  output JRout,
  output [31:0] PC_4out,
  output JALout,
  output MemToRegout,
  output MemWriteout,
  output [3:0] AluOPout,
  output AluSrcout,
  output RegWriteout,
  output [4:0] WriteRegout,
  output [31:0] PCout,
  output [31:0] IRout,
  output [31:0] Aout,
  output [31:0] Bout,
  output [31:0] IMMout,
  output [31:0] EIMMout,
  output Systemcallout,
  output [4:0] Shamtout,
  output [1:0] EX_ChooseA,
  output [1:0] EX_ChooseB,
  output [31:0] \预测out ,
  output EX_LHU,
  output EX_BLEZ
);

  wire multiplexer_2_out, multiplexer_3_out, multiplexer_4_out, multiplexer_5_out, multiplexer_7_out,
       multiplexer_8_out, multiplexer_9_out, multiplexer_11_out, multiplexer_12_out, multiplexer_20_out,
       multiplexer_24_out, multiplexer_25_out, not_1_out;
  wire [1:0] multiplexer_22_out, multiplexer_23_out;
  wire [3:0] multiplexer_10_out;
  wire [4:0] multiplexer_13_out, multiplexer_21_out;
  wire [31:0] multiplexer_1_out, multiplexer_6_out, multiplexer_14_out, multiplexer_15_out,
       multiplexer_16_out, multiplexer_17_out, multiplexer_18_out, multiplexer_19_out;

  Multiplexer #(.width(32), .enable("false")) multiplexer_1 (
    .in0(\预测in ), .in1({32{1'b0}}), .out(multiplexer_1_out), .sel(\同步清零 ));
  Multiplexer #(.enable("false")) multiplexer_2 (.in0(Beqin), .in1(1'b0), .out(multiplexer_2_out), .sel(\同步清零 ));
  Multiplexer #(.enable("false")) multiplexer_3 (.in0(Bnein), .in1(1'b0), .out(multiplexer_3_out), .sel(\同步清零 ));
  Multiplexer #(.enable("false")) multiplexer_4 (.in0(JMPin), .in1(1'b0), .out(multiplexer_4_out), .sel(\同步清零 ));
  Multiplexer #(.enable("false")) multiplexer_5 (.in0(JRin), .in1(1'b0), .out(multiplexer_5_out), .sel(\同步清零 ));
  Multiplexer #(.width(32), .enable("false")) multiplexer_6 (
    .in0(PC_4in), .in1({32{1'b0}}), .out(multiplexer_6_out), .sel(\同步清零 ));
  Multiplexer #(.enable("false")) multiplexer_7 (.in0(JALin), .in1(1'b0), .out(multiplexer_7_out), .sel(\同步清零 ));
  Multiplexer #(.enable("false")) multiplexer_8 (.in0(MemToRegin), .in1(1'b0), .out(multiplexer_8_out), .sel(\同步清零 ));
  Multiplexer #(.enable("false")) multiplexer_9 (.in0(MemWritein), .in1(1'b0), .out(multiplexer_9_out), .sel(\同步清零 ));
  Multiplexer #(.width(4), .enable("false")) multiplexer_10 (
    .in0(AluOPin), .in1(4'b0000), .out(multiplexer_10_out), .sel(\同步清零 ));
  Multiplexer #(.enable("false")) multiplexer_11 (.in0(AluSrcin), .in1(1'b0), .out(multiplexer_11_out), .sel(\同步清零 ));
  Multiplexer #(.enable("false")) multiplexer_12 (.in0(RegWritein), .in1(1'b0), .out(multiplexer_12_out), .sel(\同步清零 ));
  Multiplexer #(.width(5), .enable("false")) multiplexer_13 (
    .in0(WriteRegin), .in1({5{1'b0}}), .out(multiplexer_13_out), .sel(\同步清零 ));
  Multiplexer #(.width(32), .enable("false")) multiplexer_14 (
    .in0(PCin), .in1({32{1'b0}}), .out(multiplexer_14_out), .sel(\同步清零 ));
  Multiplexer #(.width(32), .enable("false")) multiplexer_15 (
    .in0(IRin), .in1({32{1'b0}}), .out(multiplexer_15_out), .sel(\同步清零 ));
  Multiplexer #(.width(32), .enable("false")) multiplexer_16 (
    .in0(Ain), .in1({32{1'b0}}), .out(multiplexer_16_out), .sel(\同步清零 ));
  Multiplexer #(.width(32), .enable("false")) multiplexer_17 (
    .in0(Bin), .in1({32{1'b0}}), .out(multiplexer_17_out), .sel(\同步清零 ));
  Multiplexer #(.width(32), .enable("false")) multiplexer_18 (
    .in0(IMMin), .in1({32{1'b0}}), .out(multiplexer_18_out), .sel(\同步清零 ));
  Multiplexer #(.width(32), .enable("false")) multiplexer_19 (
    .in0(EIMMin), .in1({32{1'b0}}), .out(multiplexer_19_out), .sel(\同步清零 ));
  Multiplexer #(.enable("false")) multiplexer_20 (
    .in0(Systemcallin), .in1(1'b0), .out(multiplexer_20_out), .sel(\同步清零 ));
  Multiplexer #(.width(5), .enable("false")) multiplexer_21 (
    .in0(Shamtin), .in1({5{1'b0}}), .out(multiplexer_21_out), .sel(\同步清零 ));
  Multiplexer #(.width(2), .enable("false")) multiplexer_22 (
    .in0(ID_ChooseA), .in1(2'b00), .out(multiplexer_22_out), .sel(\同步清零 ));
  Multiplexer #(.width(2), .enable("false")) multiplexer_23 (
    .in0(ID_ChooseB), .in1(2'b00), .out(multiplexer_23_out), .sel(\同步清零 ));
  Multiplexer #(.enable("false")) multiplexer_24 (.in0(ID_LHU), .in1(1'b0), .out(multiplexer_24_out), .sel(\同步清零 ));
  Multiplexer #(.enable("false")) multiplexer_25 (.in0(ID_BLEZ), .in1(1'b0), .out(multiplexer_25_out), .sel(\同步清零 ));
  not not_1 (not_1_out, \使能端 );
  Register #(.width(1)) register_1 (.D(multiplexer_2_out), .en(not_1_out), .Q(Beqout), .clk(CLK));  // open: clr
  Register #(.width(1)) register_2 (.D(multiplexer_3_out), .en(not_1_out), .Q(Bneout), .clk(CLK));  // open: clr
  Register #(.width(1)) register_3 (.D(multiplexer_4_out), .en(not_1_out), .Q(JMPout), .clk(CLK));  // open: clr
  Register #(.width(1)) register_4 (.D(multiplexer_5_out), .en(not_1_out), .Q(JRout), .clk(CLK));  // open: clr
  Register #(.width(32)) register_5 (.D(multiplexer_6_out), .en(not_1_out), .Q(PC_4out), .clk(CLK));  // open: clr
  Register #(.width(1)) register_6 (.D(multiplexer_7_out), .en(not_1_out), .Q(JALout), .clk(CLK));  // open: clr
  Register #(.width(1)) register_7 (.D(multiplexer_8_out), .en(not_1_out), .Q(MemToRegout), .clk(CLK));  // open: clr
  Register #(.width(1)) register_8 (.D(multiplexer_9_out), .en(not_1_out), .Q(MemWriteout), .clk(CLK));  // open: clr
  Register #(.width(4)) register_9 (.D(multiplexer_10_out), .en(not_1_out), .Q(AluOPout), .clk(CLK));  // open: clr
  Register #(.width(1)) register_10 (.D(multiplexer_11_out), .en(not_1_out), .Q(AluSrcout), .clk(CLK));  // open: clr
  Register #(.width(1)) register_11 (.D(multiplexer_12_out), .en(not_1_out), .Q(RegWriteout), .clk(CLK));  // open: clr
  Register #(.width(5)) register_12 (.D(multiplexer_13_out), .en(not_1_out), .Q(WriteRegout), .clk(CLK));  // open: clr
  Register #(.width(32)) register_13 (.D(multiplexer_14_out), .en(not_1_out), .Q(PCout), .clk(CLK));  // open: clr
  Register #(.width(32)) register_14 (.D(multiplexer_15_out), .en(not_1_out), .Q(IRout), .clk(CLK));  // open: clr
  Register #(.width(32)) register_15 (.D(multiplexer_16_out), .en(not_1_out), .Q(Aout), .clk(CLK));  // open: clr
  Register #(.width(32)) register_16 (.D(multiplexer_17_out), .en(not_1_out), .Q(Bout), .clk(CLK));  // open: clr
  Register #(.width(32)) register_17 (.D(multiplexer_18_out), .en(not_1_out), .Q(IMMout), .clk(CLK));  // open: clr
  Register #(.width(32)) register_18 (.D(multiplexer_19_out), .en(not_1_out), .Q(EIMMout), .clk(CLK));  // open: clr
  Register #(.width(1)) register_19 (
    .D(multiplexer_20_out), .en(not_1_out), .Q(Systemcallout), .clk(CLK));  // open: clr
  Register #(.width(5)) register_20 (.D(multiplexer_21_out), .en(not_1_out), .Q(Shamtout), .clk(CLK));  // open: clr
  Register #(.width(2)) register_21 (.D(multiplexer_22_out), .en(not_1_out), .Q(EX_ChooseA), .clk(CLK));  // open: clr
  Register #(.width(2)) register_22 (.D(multiplexer_23_out), .en(not_1_out), .Q(EX_ChooseB), .clk(CLK));  // open: clr
  Register #(.width(32)) register_23 (.D(multiplexer_1_out), .en(not_1_out), .Q(\预测out ), .clk(CLK));  // open: clr
  Register #(.width(1)) register_24 (.D(multiplexer_24_out), .en(not_1_out), .Q(EX_LHU), .clk(CLK));  // open: clr
  Register #(.width(1)) register_25 (.D(multiplexer_25_out), .en(not_1_out), .Q(EX_BLEZ), .clk(CLK));  // open: clr
endmodule

module EX_MEM (
  input  [31:0] PC_4in,
  input  JALin,
  input  Systemcallin,
  input  MemToRegin,
  input  MemWritein,
  input  RegWritein,
  input  [4:0] WriteRegin,
  input  [31:0] PCin,
  input  [31:0] IRin,
  input  [31:0] ALUin,
  input  [31:0] Bin,
  input  [31:0] Ain,
  input  EX_LHU,
  input  CLK,
  input  \同步清零 ,
  input  \使能端 ,
  output [31:0] PC_4out,
  output JALout,
  output Systemcallout,
  output MemToRegout,
  output MemWriteout,
  output RegWriteout,
  output [4:0] WriteRegout,
  output [31:0] PCout,
  output [31:0] IRout,
  output [31:0] ALUout,
  output [31:0] Bout,
  output [31:0] Aout,
  output MEM_LHU
);

  wire multiplexer_2_out, multiplexer_3_out, multiplexer_4_out, multiplexer_5_out, multiplexer_6_out,
       multiplexer_13_out, not_1_out;
  wire [4:0] multiplexer_7_out;
  wire [31:0] multiplexer_1_out, multiplexer_8_out, multiplexer_9_out, multiplexer_10_out,
       multiplexer_11_out, multiplexer_12_out;

  Multiplexer #(.width(32), .enable("false")) multiplexer_1 (
    .in0(PC_4in), .in1({32{1'b0}}), .out(multiplexer_1_out), .sel(\同步清零 ));
  Multiplexer #(.enable("false")) multiplexer_2 (.in0(JALin), .in1(1'b0), .out(multiplexer_2_out), .sel(\同步清零 ));
  Multiplexer #(.enable("false")) multiplexer_3 (.in0(Systemcallin), .in1(1'b0), .out(multiplexer_3_out), .sel(\同步清零 ));
  Multiplexer #(.enable("false")) multiplexer_4 (.in0(MemToRegin), .in1(1'b0), .out(multiplexer_4_out), .sel(\同步清零 ));
  Multiplexer #(.enable("false")) multiplexer_5 (.in0(MemWritein), .in1(1'b0), .out(multiplexer_5_out), .sel(\同步清零 ));
  Multiplexer #(.enable("false")) multiplexer_6 (.in0(RegWritein), .out(multiplexer_6_out), .sel(\同步清零 ));  // open: in1
  Multiplexer #(.width(5), .enable("false")) multiplexer_7 (
    .in0(WriteRegin), .in1({5{1'b0}}), .out(multiplexer_7_out), .sel(\同步清零 ));
  Multiplexer #(.width(32), .enable("false")) multiplexer_8 (
    .in0(PCin), .in1({32{1'b0}}), .out(multiplexer_8_out), .sel(\同步清零 ));
  Multiplexer #(.width(32), .enable("false")) multiplexer_9 (
    .in0(IRin), .in1({32{1'b0}}), .out(multiplexer_9_out), .sel(\同步清零 ));
  Multiplexer #(.width(32), .enable("false")) multiplexer_10 (
    .in0(ALUin), .in1({32{1'b0}}), .out(multiplexer_10_out), .sel(\同步清零 ));
  Multiplexer #(.width(32), .enable("false")) multiplexer_11 (
    .in0(Bin), .in1({32{1'b0}}), .out(multiplexer_11_out), .sel(\同步清零 ));
  Multiplexer #(.width(32), .enable("false")) multiplexer_12 (
    .in0(Ain), .in1({32{1'b0}}), .out(multiplexer_12_out), .sel(\同步清零 ));
  Multiplexer #(.enable("false")) multiplexer_13 (.in0(EX_LHU), .in1(1'b0), .out(multiplexer_13_out), .sel(\同步清零 ));
  not not_1 (not_1_out, \使能端 );
  Register #(.width(32)) register_1 (.D(multiplexer_1_out), .en(not_1_out), .Q(PC_4out), .clk(CLK));  // open: clr
  Register #(.width(1)) register_2 (.D(multiplexer_2_out), .en(not_1_out), .Q(JALout), .clk(CLK));  // open: clr
  Register #(.width(1)) register_3 (.D(multiplexer_3_out), .en(not_1_out), .Q(Systemcallout), .clk(CLK));  // open: clr
  Register #(.width(1)) register_4 (.D(multiplexer_4_out), .en(not_1_out), .Q(MemToRegout), .clk(CLK));  // open: clr
  Register #(.width(1)) register_5 (.D(multiplexer_5_out), .en(not_1_out), .Q(MemWriteout), .clk(CLK));  // open: clr
  Register #(.width(1)) register_6 (.D(multiplexer_6_out), .en(not_1_out), .Q(RegWriteout), .clk(CLK));  // open: clr
  Register #(.width(5)) register_7 (.D(multiplexer_7_out), .en(not_1_out), .Q(WriteRegout), .clk(CLK));  // open: clr
  Register #(.width(32)) register_8 (.D(multiplexer_8_out), .en(not_1_out), .Q(PCout), .clk(CLK));  // open: clr
  Register #(.width(32)) register_9 (.D(multiplexer_9_out), .en(not_1_out), .Q(IRout), .clk(CLK));  // open: clr
  Register #(.width(32)) register_10 (.D(multiplexer_10_out), .en(not_1_out), .Q(ALUout), .clk(CLK));  // open: clr
  Register #(.width(32)) register_11 (.D(multiplexer_11_out), .en(not_1_out), .Q(Bout), .clk(CLK));  // open: clr
  Register #(.width(32)) register_12 (.D(multiplexer_12_out), .en(not_1_out), .Q(Aout), .clk(CLK));  // open: clr
  Register #(.width(1)) register_13 (.D(multiplexer_13_out), .en(not_1_out), .Q(MEM_LHU), .clk(CLK));  // open: clr
endmodule

module MEM_WB (
  input  JALin,
  input  RegWritein,
  input  MemToRegin,
  input  Systemcallin,
  input  [31:0] IRin,
  input  [31:0] PCin,
  input  [4:0] WriteRegin,
  input  [31:0] ALUin,
  input  [31:0] MDin,
  input  [31:0] Ain,
  input  [31:0] Bin,
  input  [31:0] PC_4in,
  input  CLK,
  input  \同步清零 ,
  input  \使能端 ,
  output JALout,
  output RegWriteout,
  output MemToRegout,
  output Systemcallout,
  output [31:0] IRout,
  output [31:0] PCout,
  output [4:0] WriteRegout,
  output [31:0] ALUout,
  output [31:0] MDout,
  output [31:0] Aout,
  output [31:0] Bout,
  output [31:0] PC_4out
);

  wire multiplexer_1_out, multiplexer_2_out, multiplexer_3_out, multiplexer_4_out, not_1_out;
  wire [4:0] multiplexer_7_out;
  wire [31:0] multiplexer_5_out, multiplexer_6_out, multiplexer_8_out, multiplexer_9_out, multiplexer_10_out,
       multiplexer_11_out, multiplexer_12_out;

  Multiplexer #(.enable("false")) multiplexer_1 (.in0(JALin), .in1(1'b0), .out(multiplexer_1_out), .sel(\同步清零 ));
  Multiplexer #(.enable("false")) multiplexer_2 (.in0(RegWritein), .in1(1'b0), .out(multiplexer_2_out), .sel(\同步清零 ));
  Multiplexer #(.enable("false")) multiplexer_3 (.in0(MemToRegin), .in1(1'b0), .out(multiplexer_3_out), .sel(\同步清零 ));
  Multiplexer #(.enable("false")) multiplexer_4 (.in0(Systemcallin), .in1(1'b0), .out(multiplexer_4_out), .sel(\同步清零 ));
  Multiplexer #(.width(32), .enable("false")) multiplexer_5 (
    .in0(IRin), .in1({32{1'b0}}), .out(multiplexer_5_out), .sel(\同步清零 ));
  Multiplexer #(.width(32), .enable("false")) multiplexer_6 (
    .in0(PCin), .in1({32{1'b0}}), .out(multiplexer_6_out), .sel(\同步清零 ));
  Multiplexer #(.width(5), .enable("false")) multiplexer_7 (
    .in0(WriteRegin), .in1({5{1'b0}}), .out(multiplexer_7_out), .sel(\同步清零 ));
  Multiplexer #(.width(32), .enable("false")) multiplexer_8 (
    .in0(ALUin), .in1({32{1'b0}}), .out(multiplexer_8_out), .sel(\同步清零 ));
  Multiplexer #(.width(32), .enable("false")) multiplexer_9 (
    .in0(MDin), .in1({32{1'b0}}), .out(multiplexer_9_out), .sel(\同步清零 ));
  Multiplexer #(.width(32), .enable("false")) multiplexer_10 (
    .in0(Ain), .in1({32{1'b0}}), .out(multiplexer_10_out), .sel(\同步清零 ));
  Multiplexer #(.width(32), .enable("false")) multiplexer_11 (
    .in0(Bin), .in1({32{1'b0}}), .out(multiplexer_11_out), .sel(\同步清零 ));
  Multiplexer #(.width(32), .enable("false")) multiplexer_12 (
    .in0(PC_4in), .in1({32{1'b0}}), .out(multiplexer_12_out), .sel(\同步清零 ));
  not not_1 (not_1_out, \使能端 );
  Register #(.width(1)) register_1 (.D(multiplexer_1_out), .en(not_1_out), .Q(JALout), .clk(CLK));  // open: clr
  Register #(.width(1)) register_2 (.D(multiplexer_2_out), .en(not_1_out), .Q(RegWriteout), .clk(CLK));  // open: clr
  Register #(.width(1)) register_3 (.D(multiplexer_3_out), .en(not_1_out), .Q(MemToRegout), .clk(CLK));  // open: clr
  Register #(.width(1)) register_4 (.D(multiplexer_4_out), .en(not_1_out), .Q(Systemcallout), .clk(CLK));  // open: clr
  Register #(.width(32)) register_5 (.D(multiplexer_5_out), .en(not_1_out), .Q(IRout), .clk(CLK));  // open: clr
  Register #(.width(32)) register_6 (.D(multiplexer_6_out), .en(not_1_out), .Q(PCout), .clk(CLK));  // open: clr
  Register #(.width(5)) register_7 (.D(multiplexer_7_out), .en(not_1_out), .Q(WriteRegout), .clk(CLK));  // open: clr
  Register #(.width(32)) register_8 (.D(multiplexer_8_out), .en(not_1_out), .Q(ALUout), .clk(CLK));  // open: clr
  Register #(.width(32)) register_9 (.D(multiplexer_9_out), .en(not_1_out), .Q(MDout), .clk(CLK));  // open: clr
  Register #(.width(32)) register_10 (.D(multiplexer_10_out), .en(not_1_out), .Q(Aout), .clk(CLK));  // open: clr
  Register #(.width(32)) register_11 (.D(multiplexer_11_out), .en(not_1_out), .Q(Bout), .clk(CLK));  // open: clr
  Register #(.width(32)) register_12 (.D(multiplexer_12_out), .en(not_1_out), .Q(PC_4out), .clk(CLK));  // open: clr
endmodule
module \源寄存器使用情况  (
  input  OP0,
  input  OP1,
  input  OP2,
  input  OP3,
  input  OP4,
  input  OP5,
  input  F1,
  input  F2,
  input  F0,
  input  F3,
  input  F4,
  input  F5,
  output R1_Used,
  output R2_Used
);

  wire and_1_out, and_2_out, and_3_out, and_4_out, and_5_out, and_6_out, and_7_out, and_8_out, and_9_out,
       and_10_out, and_11_out, and_12_out, and_13_out, and_14_out, and_15_out, and_16_out, and_17_out,
       and_18_out, and_19_out, and_20_out, and_21_out, and_22_out, and_23_out, and_24_out, and_25_out,
       and_26_out, and_27_out, and_28_out, and_29_out, and_30_out, and_31_out, and_32_out, and_33_out,
       and_34_out, and_35_out, and_36_out, and_37_out, and_38_out, and_39_out, and_40_out, and_41_out,
       and_42_out, and_43_out, and_44_out, and_45_out, and_46_out, not_1_out, not_2_out, not_3_out,
       not_4_out, not_5_out, not_6_out, not_7_out, not_8_out, not_9_out, not_10_out, not_11_out, not_12_out,
       not_13_out, not_14_out, not_15_out, not_16_out, not_17_out, not_18_out, not_19_out, not_20_out,
       not_21_out, not_22_out, not_23_out, not_24_out, not_25_out, not_26_out, not_27_out, not_28_out,
       not_29_out, not_30_out, not_31_out, not_32_out, not_33_out, not_34_out, not_35_out, not_36_out,
       not_37_out, not_38_out, not_39_out, not_40_out, not_41_out, not_42_out, not_43_out, not_44_out,
       not_45_out, not_46_out, not_47_out, not_48_out, not_49_out, not_50_out, not_51_out, not_52_out,
       not_53_out, not_54_out, not_55_out, not_56_out, not_57_out, not_58_out, not_59_out, not_60_out,
       not_61_out, not_62_out, not_63_out, not_64_out, not_65_out, not_66_out, not_67_out, not_68_out,
       not_69_out, not_70_out, not_71_out, not_72_out, not_73_out, not_74_out, not_75_out, not_76_out,
       not_77_out, not_78_out, not_79_out, not_80_out, not_81_out, not_82_out, not_83_out, not_84_out,
       not_85_out, not_86_out, not_87_out, not_88_out, not_89_out, not_90_out, not_91_out, not_92_out,
       not_93_out, not_94_out, not_95_out, not_96_out, not_97_out, not_98_out, not_99_out, not_100_out,
       not_101_out, not_102_out, not_103_out, not_104_out, not_105_out, not_106_out, not_107_out,
       not_108_out, not_109_out, not_110_out, not_111_out, not_112_out, not_113_out, not_114_out,
       not_115_out, not_116_out, not_117_out, not_118_out, not_119_out, not_120_out, not_121_out,
       not_122_out, not_123_out, not_124_out, not_125_out, not_126_out, not_127_out, not_128_out,
       not_129_out, not_130_out, not_131_out, not_132_out, not_133_out, not_134_out, not_135_out,
       not_136_out, not_137_out, not_138_out, not_139_out, not_140_out, not_141_out, not_142_out,
       not_143_out, not_144_out, not_145_out, not_146_out, not_147_out, not_148_out, not_149_out,
       not_150_out, not_151_out, not_152_out, not_153_out, not_154_out, not_155_out, not_156_out,
       not_157_out, not_158_out, not_159_out, not_160_out, not_161_out, not_162_out, not_163_out,
       not_164_out, not_165_out, not_166_out, not_167_out, not_168_out, not_169_out, not_170_out,
       not_171_out, not_172_out, not_173_out, not_174_out, not_175_out, not_176_out, not_177_out,
       not_178_out, not_179_out, not_180_out, not_181_out, not_182_out, not_183_out, not_184_out,
       not_185_out, not_186_out, not_187_out, not_188_out, not_189_out, not_190_out, not_191_out,
       not_192_out, not_193_out, not_194_out, not_195_out, not_196_out, not_197_out, not_198_out,
       not_199_out, not_200_out, not_201_out, not_202_out, not_203_out, not_204_out, not_205_out,
       not_206_out, not_207_out, not_208_out, not_209_out, not_210_out, not_211_out, not_212_out,
       not_213_out, not_214_out, not_215_out, not_216_out, not_217_out, not_218_out, not_219_out,
       not_220_out, not_221_out, not_222_out, not_223_out, not_224_out, not_225_out, not_226_out,
       not_227_out, not_228_out, not_229_out, not_230_out, not_231_out, not_232_out, not_233_out,
       not_234_out, not_235_out, not_236_out, not_237_out, not_238_out, not_239_out, not_240_out,
       not_241_out, not_242_out, not_243_out, not_244_out, not_245_out, not_246_out, not_247_out,
       not_248_out, not_249_out, not_250_out, not_251_out, not_252_out, not_253_out, not_254_out,
       not_255_out, not_256_out, not_257_out, not_258_out, not_259_out, not_260_out, not_261_out,
       not_262_out, not_263_out, not_264_out, not_265_out, not_266_out, not_267_out, not_268_out,
       not_269_out, not_270_out, not_271_out, not_272_out, not_273_out, not_274_out, not_275_out,
       not_276_out, not_277_out, not_278_out, not_279_out, not_280_out, not_281_out, not_282_out,
       not_283_out, not_284_out, not_285_out, not_286_out, not_287_out, not_288_out, not_289_out,
       not_290_out, not_291_out, not_292_out, not_293_out, not_294_out, not_295_out, not_296_out,
       not_297_out, not_298_out, not_299_out, not_300_out, not_301_out, not_302_out, not_303_out,
       not_304_out, not_305_out, not_306_out, not_307_out, not_308_out, not_309_out, not_310_out,
       not_311_out, not_312_out, not_313_out, not_314_out, not_315_out, not_316_out, not_317_out,
       not_318_out, not_319_out, not_320_out, not_321_out, not_322_out, not_323_out, not_324_out,
       not_325_out, not_326_out, not_327_out, not_328_out, not_329_out, not_330_out, not_331_out,
       not_332_out, not_333_out, not_334_out, not_335_out, not_336_out, not_337_out, not_338_out,
       not_339_out, not_340_out, not_341_out, not_342_out, not_343_out, not_344_out, not_345_out,
       not_346_out, not_347_out, not_348_out;

  not not_1 (not_1_out, OP5);
  not not_2 (not_2_out, OP4);
  not not_3 (not_3_out, OP3);
  not not_4 (not_4_out, OP2);
  not not_5 (not_5_out, OP1);
  not not_6 (not_6_out, OP0);
  not not_7 (not_7_out, F5);
  not not_8 (not_8_out, F4);
  not not_9 (not_9_out, F3);
  not not_10 (not_10_out, F2);
  not not_11 (not_11_out, F1);
  not not_12 (not_12_out, F0);
  not not_13 (not_13_out, OP5);
  not not_14 (not_14_out, OP4);
  not not_15 (not_15_out, OP3);
  not not_16 (not_16_out, OP2);
  not not_17 (not_17_out, OP1);
  not not_18 (not_18_out, OP0);
  not not_19 (not_19_out, F5);
  not not_20 (not_20_out, F4);
  not not_21 (not_21_out, F3);
  not not_22 (not_22_out, F2);
  not not_23 (not_23_out, OP5);
  not not_24 (not_24_out, OP4);
  not not_25 (not_25_out, OP3);
  not not_26 (not_26_out, OP2);
  not not_27 (not_27_out, OP1);
  not not_28 (not_28_out, OP0);
  not not_29 (not_29_out, F5);
  not not_30 (not_30_out, F4);
  not not_31 (not_31_out, F3);
  not not_32 (not_32_out, F2);
  not not_33 (not_33_out, F0);
  not not_34 (not_34_out, OP5);
  not not_35 (not_35_out, OP4);
  not not_36 (not_36_out, OP3);
  not not_37 (not_37_out, OP2);
  not not_38 (not_38_out, OP1);
  not not_39 (not_39_out, OP0);
  not not_40 (not_40_out, F4);
  not not_41 (not_41_out, F3);
  not not_42 (not_42_out, F2);
  not not_43 (not_43_out, F1);
  not not_44 (not_44_out, F0);
  not not_45 (not_45_out, OP5);
  not not_46 (not_46_out, OP4);
  not not_47 (not_47_out, OP3);
  not not_48 (not_48_out, OP2);
  not not_49 (not_49_out, OP1);
  not not_50 (not_50_out, OP0);
  not not_51 (not_51_out, F4);
  not not_52 (not_52_out, F3);
  not not_53 (not_53_out, F2);
  not not_54 (not_54_out, F1);
  not not_55 (not_55_out, OP5);
  not not_56 (not_56_out, OP4);
  not not_57 (not_57_out, OP3);
  not not_58 (not_58_out, OP2);
  not not_59 (not_59_out, OP1);
  not not_60 (not_60_out, OP0);
  not not_61 (not_61_out, F4);
  not not_62 (not_62_out, F3);
  not not_63 (not_63_out, F2);
  not not_64 (not_64_out, F0);
  not not_65 (not_65_out, OP5);
  not not_66 (not_66_out, OP4);
  not not_67 (not_67_out, OP3);
  not not_68 (not_68_out, OP2);
  not not_69 (not_69_out, OP1);
  not not_70 (not_70_out, OP0);
  not not_71 (not_71_out, F4);
  not not_72 (not_72_out, F3);
  not not_73 (not_73_out, F1);
  not not_74 (not_74_out, F0);
  not not_75 (not_75_out, OP5);
  not not_76 (not_76_out, OP4);
  not not_77 (not_77_out, OP3);
  not not_78 (not_78_out, OP2);
  not not_79 (not_79_out, OP1);
  not not_80 (not_80_out, OP0);
  not not_81 (not_81_out, F4);
  not not_82 (not_82_out, F3);
  not not_83 (not_83_out, F1);
  not not_84 (not_84_out, OP5);
  not not_85 (not_85_out, OP4);
  not not_86 (not_86_out, OP3);
  not not_87 (not_87_out, OP2);
  not not_88 (not_88_out, OP1);
  not not_89 (not_89_out, OP0);
  not not_90 (not_90_out, F4);
  not not_91 (not_91_out, F3);
  not not_92 (not_92_out, OP5);
  not not_93 (not_93_out, OP4);
  not not_94 (not_94_out, OP3);
  not not_95 (not_95_out, OP2);
  not not_96 (not_96_out, OP1);
  not not_97 (not_97_out, OP0);
  not not_98 (not_98_out, F4);
  not not_99 (not_99_out, F2);
  not not_100 (not_100_out, F0);
  not not_101 (not_101_out, OP5);
  not not_102 (not_102_out, OP4);
  not not_103 (not_103_out, OP3);
  not not_104 (not_104_out, OP2);
  not not_105 (not_105_out, OP1);
  not not_106 (not_106_out, OP0);
  not not_107 (not_107_out, F4);
  not not_108 (not_108_out, F2);
  not not_109 (not_109_out, OP5);
  not not_110 (not_110_out, OP4);
  not not_111 (not_111_out, OP3);
  not not_112 (not_112_out, OP2);
  not not_113 (not_113_out, OP1);
  not not_114 (not_114_out, OP0);
  not not_115 (not_115_out, F5);
  not not_116 (not_116_out, F4);
  not not_117 (not_117_out, F2);
  not not_118 (not_118_out, F1);
  not not_119 (not_119_out, F0);
  not not_120 (not_120_out, OP5);
  not not_121 (not_121_out, OP4);
  not not_122 (not_122_out, OP3);
  not not_123 (not_123_out, OP2);
  not not_124 (not_124_out, OP1);
  not not_125 (not_125_out, OP0);
  not not_126 (not_126_out, F5);
  not not_127 (not_127_out, F4);
  not not_128 (not_128_out, F1);
  not not_129 (not_129_out, F0);
  not not_130 (not_130_out, OP5);
  not not_131 (not_131_out, OP4);
  not not_132 (not_132_out, OP3);
  not not_133 (not_133_out, OP1);
  not not_134 (not_134_out, OP0);
  not not_135 (not_135_out, OP5);
  not not_136 (not_136_out, OP4);
  not not_137 (not_137_out, OP3);
  not not_138 (not_138_out, OP1);
  not not_139 (not_139_out, OP5);
  not not_140 (not_140_out, OP4);
  not not_141 (not_141_out, OP2);
  not not_142 (not_142_out, OP1);
  not not_143 (not_143_out, OP0);
  not not_144 (not_144_out, OP5);
  not not_145 (not_145_out, OP4);
  not not_146 (not_146_out, OP1);
  not not_147 (not_147_out, OP0);
  not not_148 (not_148_out, OP5);
  not not_149 (not_149_out, OP4);
  not not_150 (not_150_out, OP2);
  not not_151 (not_151_out, OP1);
  not not_152 (not_152_out, OP5);
  not not_153 (not_153_out, OP4);
  not not_154 (not_154_out, OP2);
  not not_155 (not_155_out, OP0);
  not not_156 (not_156_out, OP5);
  not not_157 (not_157_out, OP4);
  not not_158 (not_158_out, OP1);
  not not_159 (not_159_out, OP4);
  not not_160 (not_160_out, OP3);
  not not_161 (not_161_out, OP2);
  not not_162 (not_162_out, OP4);
  not not_163 (not_163_out, OP2);
  not not_164 (not_164_out, OP5);
  not not_165 (not_165_out, OP4);
  not not_166 (not_166_out, OP3);
  not not_167 (not_167_out, OP2);
  not not_168 (not_168_out, OP1);
  not not_169 (not_169_out, OP0);
  not not_170 (not_170_out, F4);
  not not_171 (not_171_out, F3);
  not not_172 (not_172_out, F2);
  not not_173 (not_173_out, OP5);
  not not_174 (not_174_out, OP4);
  not not_175 (not_175_out, OP2);
  not not_176 (not_176_out, OP4);
  not not_177 (not_177_out, OP3);
  not not_178 (not_178_out, OP2);
  not not_179 (not_179_out, OP1);
  not not_180 (not_180_out, OP0);
  not not_181 (not_181_out, OP5);
  not not_182 (not_182_out, OP4);
  not not_183 (not_183_out, OP3);
  not not_184 (not_184_out, OP2);
  not not_185 (not_185_out, OP1);
  not not_186 (not_186_out, OP5);
  not not_187 (not_187_out, OP4);
  not not_188 (not_188_out, OP3);
  not not_189 (not_189_out, OP2);
  not not_190 (not_190_out, OP1);
  not not_191 (not_191_out, OP0);
  not not_192 (not_192_out, F4);
  not not_193 (not_193_out, F3);
  not not_194 (not_194_out, F0);
  not not_195 (not_195_out, OP4);
  not not_196 (not_196_out, OP3);
  not not_197 (not_197_out, OP1);
  not not_198 (not_198_out, OP5);
  not not_199 (not_199_out, OP4);
  not not_200 (not_200_out, OP3);
  not not_201 (not_201_out, OP0);
  not not_202 (not_202_out, OP5);
  not not_203 (not_203_out, OP4);
  not not_204 (not_204_out, OP3);
  not not_205 (not_205_out, OP2);
  not not_206 (not_206_out, OP1);
  not not_207 (not_207_out, OP0);
  not not_208 (not_208_out, F5);
  not not_209 (not_209_out, F4);
  not not_210 (not_210_out, F3);
  not not_211 (not_211_out, F2);
  not not_212 (not_212_out, F1);
  not not_213 (not_213_out, F0);
  not not_214 (not_214_out, OP5);
  not not_215 (not_215_out, OP4);
  not not_216 (not_216_out, OP3);
  not not_217 (not_217_out, OP2);
  not not_218 (not_218_out, OP1);
  not not_219 (not_219_out, OP0);
  not not_220 (not_220_out, F5);
  not not_221 (not_221_out, F4);
  not not_222 (not_222_out, F3);
  not not_223 (not_223_out, F2);
  not not_224 (not_224_out, OP5);
  not not_225 (not_225_out, OP4);
  not not_226 (not_226_out, OP3);
  not not_227 (not_227_out, OP2);
  not not_228 (not_228_out, OP1);
  not not_229 (not_229_out, OP0);
  not not_230 (not_230_out, F5);
  not not_231 (not_231_out, F4);
  not not_232 (not_232_out, F3);
  not not_233 (not_233_out, F2);
  not not_234 (not_234_out, F0);
  not not_235 (not_235_out, OP5);
  not not_236 (not_236_out, OP4);
  not not_237 (not_237_out, OP3);
  not not_238 (not_238_out, OP2);
  not not_239 (not_239_out, OP1);
  not not_240 (not_240_out, OP0);
  not not_241 (not_241_out, F4);
  not not_242 (not_242_out, F3);
  not not_243 (not_243_out, F2);
  not not_244 (not_244_out, F1);
  not not_245 (not_245_out, F0);
  not not_246 (not_246_out, OP5);
  not not_247 (not_247_out, OP4);
  not not_248 (not_248_out, OP3);
  not not_249 (not_249_out, OP2);
  not not_250 (not_250_out, OP1);
  not not_251 (not_251_out, OP0);
  not not_252 (not_252_out, F4);
  not not_253 (not_253_out, F3);
  not not_254 (not_254_out, F2);
  not not_255 (not_255_out, F1);
  not not_256 (not_256_out, OP5);
  not not_257 (not_257_out, OP4);
  not not_258 (not_258_out, OP3);
  not not_259 (not_259_out, OP2);
  not not_260 (not_260_out, OP1);
  not not_261 (not_261_out, OP0);
  not not_262 (not_262_out, F4);
  not not_263 (not_263_out, F3);
  not not_264 (not_264_out, F2);
  not not_265 (not_265_out, F0);
  not not_266 (not_266_out, OP5);
  not not_267 (not_267_out, OP4);
  not not_268 (not_268_out, OP3);
  not not_269 (not_269_out, OP2);
  not not_270 (not_270_out, OP1);
  not not_271 (not_271_out, OP0);
  not not_272 (not_272_out, F4);
  not not_273 (not_273_out, F3);
  not not_274 (not_274_out, F1);
  not not_275 (not_275_out, F0);
  not not_276 (not_276_out, OP5);
  not not_277 (not_277_out, OP4);
  not not_278 (not_278_out, OP3);
  not not_279 (not_279_out, OP2);
  not not_280 (not_280_out, OP1);
  not not_281 (not_281_out, OP0);
  not not_282 (not_282_out, F4);
  not not_283 (not_283_out, F3);
  not not_284 (not_284_out, F1);
  not not_285 (not_285_out, OP5);
  not not_286 (not_286_out, OP4);
  not not_287 (not_287_out, OP3);
  not not_288 (not_288_out, OP2);
  not not_289 (not_289_out, OP1);
  not not_290 (not_290_out, OP0);
  not not_291 (not_291_out, F4);
  not not_292 (not_292_out, F3);
  not not_293 (not_293_out, OP5);
  not not_294 (not_294_out, OP4);
  not not_295 (not_295_out, OP3);
  not not_296 (not_296_out, OP2);
  not not_297 (not_297_out, OP1);
  not not_298 (not_298_out, OP0);
  not not_299 (not_299_out, F4);
  not not_300 (not_300_out, F2);
  not not_301 (not_301_out, F0);
  not not_302 (not_302_out, OP5);
  not not_303 (not_303_out, OP4);
  not not_304 (not_304_out, OP3);
  not not_305 (not_305_out, OP2);
  not not_306 (not_306_out, OP1);
  not not_307 (not_307_out, OP0);
  not not_308 (not_308_out, F4);
  not not_309 (not_309_out, F2);
  not not_310 (not_310_out, OP5);
  not not_311 (not_311_out, OP4);
  not not_312 (not_312_out, OP3);
  not not_313 (not_313_out, OP2);
  not not_314 (not_314_out, OP1);
  not not_315 (not_315_out, OP0);
  not not_316 (not_316_out, F5);
  not not_317 (not_317_out, F4);
  not not_318 (not_318_out, F1);
  not not_319 (not_319_out, F0);
  not not_320 (not_320_out, OP5);
  not not_321 (not_321_out, OP4);
  not not_322 (not_322_out, OP3);
  not not_323 (not_323_out, OP1);
  not not_324 (not_324_out, OP0);
  not not_325 (not_325_out, OP5);
  not not_326 (not_326_out, OP4);
  not not_327 (not_327_out, OP3);
  not not_328 (not_328_out, OP1);
  not not_329 (not_329_out, OP4);
  not not_330 (not_330_out, OP2);
  not not_331 (not_331_out, OP5);
  not not_332 (not_332_out, OP4);
  not not_333 (not_333_out, OP3);
  not not_334 (not_334_out, OP2);
  not not_335 (not_335_out, OP1);
  not not_336 (not_336_out, OP0);
  not not_337 (not_337_out, F4);
  not not_338 (not_338_out, F3);
  not not_339 (not_339_out, F2);
  not not_340 (not_340_out, OP5);
  not not_341 (not_341_out, OP4);
  not not_342 (not_342_out, OP3);
  not not_343 (not_343_out, OP2);
  not not_344 (not_344_out, OP1);
  not not_345 (not_345_out, OP0);
  not not_346 (not_346_out, F4);
  not not_347 (not_347_out, F3);
  not not_348 (not_348_out, F0);
  and and_1 (and_1_out, not_1_out, not_2_out, not_3_out, not_4_out, not_5_out, not_6_out, not_7_out, not_8_out, not_9_out, not_10_out, not_11_out, not_12_out);
  and and_2 (and_2_out, not_13_out, not_14_out, not_15_out, not_16_out, not_17_out, not_18_out, not_19_out, not_20_out, not_21_out, not_22_out, F1, F0);
  and and_3 (and_3_out, not_23_out, not_24_out, not_25_out, not_26_out, not_27_out, not_28_out, not_29_out, not_30_out, not_31_out, not_32_out, F1, not_33_out);
  and and_4 (and_4_out, not_34_out, not_35_out, not_36_out, not_37_out, not_38_out, not_39_out, F5, not_40_out, not_41_out, not_42_out, not_43_out, not_44_out);
  and and_5 (and_5_out, not_45_out, not_46_out, not_47_out, not_48_out, not_49_out, not_50_out, F5, not_51_out, not_52_out, not_53_out, not_54_out, F0);
  and and_6 (and_6_out, not_55_out, not_56_out, not_57_out, not_58_out, not_59_out, not_60_out, F5, not_61_out, not_62_out, not_63_out, F1, not_64_out);
  and and_7 (and_7_out, not_65_out, not_66_out, not_67_out, not_68_out, not_69_out, not_70_out, F5, not_71_out, not_72_out, F2, not_73_out, not_74_out);
  and and_8 (and_8_out, not_75_out, not_76_out, not_77_out, not_78_out, not_79_out, not_80_out, F5, not_81_out, not_82_out, F2, not_83_out, F0);
  and and_9 (and_9_out, not_84_out, not_85_out, not_86_out, not_87_out, not_88_out, not_89_out, F5, not_90_out, not_91_out, F2, F1, F0);
  and and_10 (and_10_out, not_92_out, not_93_out, not_94_out, not_95_out, not_96_out, not_97_out, F5, not_98_out, F3, not_99_out, F1, not_100_out);
  and and_11 (and_11_out, not_101_out, not_102_out, not_103_out, not_104_out, not_105_out, not_106_out, F5, not_107_out, F3, not_108_out, F1, F0);
  and and_12 (and_12_out, not_109_out, not_110_out, not_111_out, not_112_out, not_113_out, not_114_out, not_115_out, not_116_out, F3, not_117_out, not_118_out, not_119_out);
  and and_13 (and_13_out, not_120_out, not_121_out, not_122_out, not_123_out, not_124_out, not_125_out, not_126_out, not_127_out, F3, F2, not_128_out, not_129_out);
  and and_14 (and_14_out, not_130_out, not_131_out, not_132_out, OP2, not_133_out, not_134_out);
  and and_15 (and_15_out, not_135_out, not_136_out, not_137_out, OP2, not_138_out, OP0);
  and and_16 (and_16_out, not_139_out, not_140_out, OP3, not_141_out, not_142_out, not_143_out);
  and and_17 (and_17_out, not_144_out, not_145_out, OP3, OP2, not_146_out, not_147_out);
  and and_18 (and_18_out, not_148_out, not_149_out, OP3, not_150_out, not_151_out, OP0);
  and and_19 (and_19_out, not_152_out, not_153_out, OP3, not_154_out, OP1, not_155_out);
  and and_20 (and_20_out, not_156_out, not_157_out, OP3, OP2, not_158_out, OP0);
  and and_21 (and_21_out, OP5, not_159_out, not_160_out, not_161_out, OP1, OP0);
  and and_22 (and_22_out, OP5, not_162_out, OP3, not_163_out, OP1, OP0);
  and and_23 (and_23_out, not_164_out, not_165_out, not_166_out, not_167_out, not_168_out, not_169_out, F5, not_170_out, not_171_out, not_172_out, F1, F0);
  and and_24 (and_24_out, not_173_out, not_174_out, OP3, not_175_out, OP1, OP0);
  and and_25 (and_25_out, OP5, not_176_out, not_177_out, not_178_out, not_179_out, not_180_out);
  and and_26 (and_26_out, not_181_out, not_182_out, not_183_out, not_184_out, not_185_out, OP0);
  and and_27 (and_27_out, not_186_out, not_187_out, not_188_out, not_189_out, not_190_out, not_191_out, F5, not_192_out, not_193_out, F2, F1, not_194_out);
  and and_28 (and_28_out, OP5, not_195_out, not_196_out, OP2, not_197_out, OP0);
  and and_29 (and_29_out, not_198_out, not_199_out, not_200_out, OP2, OP1, not_201_out);
  and and_30 (and_30_out, not_202_out, not_203_out, not_204_out, not_205_out, not_206_out, not_207_out, not_208_out, not_209_out, not_210_out, not_211_out, not_212_out, not_213_out);
  and and_31 (and_31_out, not_214_out, not_215_out, not_216_out, not_217_out, not_218_out, not_219_out, not_220_out, not_221_out, not_222_out, not_223_out, F1, F0);
  and and_32 (and_32_out, not_224_out, not_225_out, not_226_out, not_227_out, not_228_out, not_229_out, not_230_out, not_231_out, not_232_out, not_233_out, F1, not_234_out);
  and and_33 (and_33_out, not_235_out, not_236_out, not_237_out, not_238_out, not_239_out, not_240_out, F5, not_241_out, not_242_out, not_243_out, not_244_out, not_245_out);
  and and_34 (and_34_out, not_246_out, not_247_out, not_248_out, not_249_out, not_250_out, not_251_out, F5, not_252_out, not_253_out, not_254_out, not_255_out, F0);
  and and_35 (and_35_out, not_256_out, not_257_out, not_258_out, not_259_out, not_260_out, not_261_out, F5, not_262_out, not_263_out, not_264_out, F1, not_265_out);
  and and_36 (and_36_out, not_266_out, not_267_out, not_268_out, not_269_out, not_270_out, not_271_out, F5, not_272_out, not_273_out, F2, not_274_out, not_275_out);
  and and_37 (and_37_out, not_276_out, not_277_out, not_278_out, not_279_out, not_280_out, not_281_out, F5, not_282_out, not_283_out, F2, not_284_out, F0);
  and and_38 (and_38_out, not_285_out, not_286_out, not_287_out, not_288_out, not_289_out, not_290_out, F5, not_291_out, not_292_out, F2, F1, F0);
  and and_39 (and_39_out, not_293_out, not_294_out, not_295_out, not_296_out, not_297_out, not_298_out, F5, not_299_out, F3, not_300_out, F1, not_301_out);
  and and_40 (and_40_out, not_302_out, not_303_out, not_304_out, not_305_out, not_306_out, not_307_out, F5, not_308_out, F3, not_309_out, F1, F0);
  and and_41 (and_41_out, not_310_out, not_311_out, not_312_out, not_313_out, not_314_out, not_315_out, not_316_out, not_317_out, F3, F2, not_318_out, not_319_out);
  and and_42 (and_42_out, not_320_out, not_321_out, not_322_out, OP2, not_323_out, not_324_out);
  and and_43 (and_43_out, not_325_out, not_326_out, not_327_out, OP2, not_328_out, OP0);
  and and_44 (and_44_out, OP5, not_329_out, OP3, not_330_out, OP1, OP0);
  and and_45 (and_45_out, not_331_out, not_332_out, not_333_out, not_334_out, not_335_out, not_336_out, F5, not_337_out, not_338_out, not_339_out, F1, F0);
  and and_46 (and_46_out, not_340_out, not_341_out, not_342_out, not_343_out, not_344_out, not_345_out, F5, not_346_out, not_347_out, F2, F1, not_348_out);
  or or_1 (R2_Used, and_30_out, and_31_out, and_32_out, and_33_out, and_34_out, and_35_out, and_36_out, and_37_out, and_38_out, and_39_out, and_40_out, and_41_out, and_42_out, and_43_out, and_44_out, and_45_out, and_46_out);
  or or_2 (R1_Used, and_1_out, and_2_out, and_3_out, and_4_out, and_5_out, and_6_out, and_7_out, and_8_out, and_9_out, and_10_out, and_11_out, and_12_out, and_13_out, and_14_out, and_15_out, and_16_out, and_17_out, and_18_out, and_19_out, and_20_out, and_21_out, and_22_out, and_23_out, and_24_out, and_25_out, and_26_out, and_27_out, and_28_out, and_29_out);
endmodule

module \重定向选择  (
  input  [4:0] EX_WriteReg,
  input  [5:0] OP_CODE,
  input  [4:0] R1,
  input  [4:0] MEM_WriteReg,
  input  [5:0] FUNC,
  input  [4:0] R2,
  input  EX_RegWrite,
  input  [5:0] EX_OP,
  input  MEM_RegWrite,
  input  MEM_MemReg,
  output [1:0] chooseA,
  output [1:0] chooseB,
  output Loaduse
);

  wire and_1_out, and_2_out, and_3_out, and_4_out, and_5_out, and_6_out, and_8_out, and_9_out, and_10_out,
       and_11_out, comparator_1_eq, comparator_2_eq, comparator_3_eq, comparator_4_eq, comparator_5_eq,
       comparator_6_eq, comparator_7_eq, comparator_8_eq, multiplexer_1_out, multiplexer_2_out,
       multiplexer_3_out, multiplexer_4_out, multiplexer_5_out, multiplexer_6_out, multiplexer_7_out,
       multiplexer_8_out, or_1_out, or_2_out, R1Used, R2Used;

  \源寄存器使用情况  \u_源寄存器使用情况_1  (
    .OP0(OP_CODE[0]), .OP1(OP_CODE[1]), .OP2(OP_CODE[2]), .OP3(OP_CODE[3]), .OP4(OP_CODE[4]),
    .OP5(OP_CODE[5]), .F1(FUNC[1]), .F2(FUNC[2]), .F0(FUNC[0]), .F3(FUNC[3]), .F4(FUNC[4]), .F5(FUNC[5]),
    .R1_Used(R1Used), .R2_Used(R2Used));
  Comparator #(.width(5)) comparator_1 (.a(R1), .b({5{1'b0}}), .eq(comparator_1_eq));  // open: gt, lt
  Comparator #(.width(5)) comparator_2 (.a(R2), .b({5{1'b0}}), .eq(comparator_2_eq));  // open: gt, lt
  Comparator #(.width(5)) comparator_3 (.a(R1), .b(EX_WriteReg), .eq(comparator_3_eq));  // open: gt, lt
  Comparator #(.width(5)) comparator_4 (.a(R2), .b(EX_WriteReg), .eq(comparator_4_eq));  // open: gt, lt
  Comparator #(.width(5)) comparator_5 (.a(R1), .b(MEM_WriteReg), .eq(comparator_5_eq));  // open: gt, lt
  Comparator #(.width(5)) comparator_6 (.a(R2), .b(MEM_WriteReg), .eq(comparator_6_eq));  // open: gt, lt
  Multiplexer #(.enable("false")) multiplexer_1 (
    .in0(comparator_3_eq), .in1(1'b0), .out(multiplexer_1_out), .sel(comparator_1_eq));
  Multiplexer #(.enable("false")) multiplexer_2 (
    .in0(comparator_4_eq), .in1(1'b0), .out(multiplexer_2_out), .sel(comparator_2_eq));
  Multiplexer #(.enable("false")) multiplexer_3 (
    .in0(comparator_5_eq), .in1(1'b0), .out(multiplexer_3_out), .sel(comparator_1_eq));
  Multiplexer #(.enable("false")) multiplexer_4 (
    .in0(comparator_6_eq), .in1(1'b0), .out(multiplexer_4_out), .sel(comparator_2_eq));
  Multiplexer #(.enable("false")) multiplexer_5 (
    .in0(1'b0), .in1(multiplexer_1_out), .out(multiplexer_5_out), .sel(R1Used));
  Multiplexer #(.enable("false")) multiplexer_6 (
    .in0(1'b0), .in1(multiplexer_2_out), .out(multiplexer_6_out), .sel(R2Used));
  Multiplexer #(.enable("false")) multiplexer_7 (
    .in0(1'b0), .in1(multiplexer_3_out), .out(multiplexer_7_out), .sel(R1Used));
  Multiplexer #(.enable("false")) multiplexer_8 (
    .in0(1'b0), .in1(multiplexer_4_out), .out(multiplexer_8_out), .sel(R2Used));
  Comparator #(.width(6)) comparator_7 (.a(EX_OP), .b(6'b100011), .eq(comparator_7_eq));  // open: gt, lt
  Comparator #(.width(6)) comparator_8 (.a(EX_OP), .b(6'b100101), .eq(comparator_8_eq));  // open: gt, lt
  and and_1 (and_1_out, EX_RegWrite, multiplexer_5_out);
  and and_2 (and_2_out, EX_RegWrite, multiplexer_6_out);
  and and_3 (and_3_out, MEM_RegWrite, multiplexer_7_out);
  and and_4 (and_4_out, MEM_RegWrite, multiplexer_8_out);
  or or_1 (or_1_out, comparator_7_eq, comparator_8_eq);
  or or_2 (or_2_out, and_1_out, and_2_out);
  and and_5 (and_5_out, ~Loaduse, and_1_out);  // AND_Gate
  and and_6 (and_6_out, ~Loaduse, and_2_out);  // AND_Gate
  and and_7 (Loaduse, or_1_out, or_2_out);
  and and_8 (and_8_out, and_3_out, ~MEM_MemReg);  // AND_Gate
  and and_9 (and_9_out, and_3_out, MEM_MemReg);
  or or_3 (chooseA[1], and_8_out, and_5_out);
  or or_4 (chooseA[0], and_9_out, and_5_out);
  and and_10 (and_10_out, and_4_out, ~MEM_MemReg);  // AND_Gate
  or or_5 (chooseB[1], and_10_out, and_6_out);
  and and_11 (and_11_out, and_4_out, MEM_MemReg);
  or or_6 (chooseB[0], and_11_out, and_6_out);
endmodule

module \分支预测BHT  (
  input  [31:0] in_1,
  input  [31:0] \分支指令地址 ,
  input  [31:0] \分支目标地址 ,
  input  \跳转 ,
  input  CLK,
  input  \分支 ,
  input  Enable,
  output Miss,
  output [31:0] DataOut
);

  wire and_1_out, and_2_out, and_3_out, and_4_out, and_5_out, and_6_out, and_7_out, comparator_1_eq,
       comparator_2_eq, comparator_3_eq, comparator_4_eq, comparator_5_eq, comparator_6_eq, comparator_7_eq,
       comparator_8_eq, comparator_9_eq, comparator_10_eq, comparator_11_eq, comparator_12_eq,
       comparator_13_eq, comparator_14_eq, comparator_15_eq, comparator_16_eq, decoder_1_out0,
       decoder_1_out1, decoder_1_out2, decoder_1_out3, decoder_1_out4, decoder_1_out5, decoder_1_out6,
       decoder_1_out7, Eq0, Eq1, Eq2, Eq3, Eq4, Eq5, Eq6, Eq7, L0, L1, L2, L3, L4, L5, L6, L7,
       multiplexer_3_out, multiplexer_4_out, multiplexer_5_out, multiplexer_6_out, multiplexer_7_out,
       multiplexer_8_out, multiplexer_9_out, multiplexer_10_out, nand_1_out, nor_2_out, not_1_out, or_1_out,
       or_2_out, or_3_out, or_4_out, or_5_out, or_6_out, or_7_out, or_8_out, or_9_out, or_10_out, or_11_out,
       or_12_out, or_13_out, or_14_out, or_15_out, or_16_out, PCMiss, Set0, Set1, Set2, Set3, Set4, Set5,
       Set6, Set7, V0, V1, V2, V3, V4, V5, V6, V7;
  wire [1:0] \bht状态转换_1_nstate , \bht状态转换_2_nstate , \bht状态转换_3_nstate , \bht状态转换_4_nstate ,
       \bht状态转换_5_nstate , \bht状态转换_6_nstate , \bht状态转换_7_nstate , \bht状态转换_8_nstate , \分支预测历史 ,
       \分支预测历史_2_q , \分支预测历史_3_q , \分支预测历史_4_q , \分支预测历史_5_q , \分支预测历史_6_q , \分支预测历史_7_q , \分支预测历史_8_q ,
       \分支预测历史_q ;
  wire [2:0] max3_1_max_num, max3_2_max_num, max3_3_max_num, max3_4_max_num, max3_5_max_num, max3_6_max_num,
       max3_7_max_num;
  wire [15:0] C0, C1, C2, C3, C4, C5, C6, C7, max3_1_max, max3_2_max, max3_3_max, max3_4_max, max3_5_max,
       max3_6_max;
  wire [31:0] multiplexer_1_out, PC_4, SlotData, \分支指令地址0 , \分支指令地址1 , \分支指令地址2 , \分支指令地址3 , \分支指令地址4 ,
       \分支指令地址5 , \分支指令地址6 , \分支指令地址7 , \分支目标地址_q , \数据块副本_2_q , \数据块副本_3_q , \数据块副本_4_q , \数据块副本_5_q ,
       \数据块副本_6_q , \数据块副本_7_q , \数据块副本_q ;

  Register #(.width(1)) Valid (.D(1'b1), .en(Set0), .Q(V0), .clk(CLK));  // open: clr
  Register #(.width(1)) Valid_2 (.D(1'b1), .en(Set1), .Q(V1), .clk(CLK));  // open: clr
  Register #(.width(1)) Valid_3 (.D(1'b1), .en(Set2), .Q(V2), .clk(CLK));  // open: clr
  Register #(.width(1)) Valid_4 (.D(1'b1), .en(Set3), .Q(V3), .clk(CLK));  // open: clr
  Register #(.width(1)) Valid_5 (.D(1'b1), .en(Set4), .Q(V4), .clk(CLK));  // open: clr
  Register #(.width(1)) Valid_6 (.D(1'b1), .en(Set5), .Q(V5), .clk(CLK));  // open: clr
  Register #(.width(1)) Valid_7 (.D(1'b1), .en(Set6), .Q(V6), .clk(CLK));  // open: clr
  Register #(.width(1)) Valid_8 (.D(1'b1), .en(Set7), .Q(V7), .clk(CLK));  // open: clr
  Register #(.width(32)) \u_分支指令地址  (.D(\分支指令地址 ), .en(Set0), .Q(\分支指令地址0 ), .clk(CLK));  // open: clr
  Register #(.width(32)) \u_分支指令地址_2  (.D(\分支指令地址 ), .en(Set1), .Q(\分支指令地址1 ), .clk(CLK));  // open: clr
  Register #(.width(32)) \u_分支指令地址_3  (.D(\分支指令地址 ), .en(Set2), .Q(\分支指令地址2 ), .clk(CLK));  // open: clr
  Register #(.width(32)) \u_分支指令地址_4  (.D(\分支指令地址 ), .en(Set3), .Q(\分支指令地址3 ), .clk(CLK));  // open: clr
  Register #(.width(32)) \u_分支指令地址_5  (.D(\分支指令地址 ), .en(Set4), .Q(\分支指令地址4 ), .clk(CLK));  // open: clr
  Register #(.width(32)) \u_分支指令地址_6  (.D(\分支指令地址 ), .en(Set5), .Q(\分支指令地址5 ), .clk(CLK));  // open: clr
  Register #(.width(32)) \u_分支指令地址_7  (.D(\分支指令地址 ), .en(Set6), .Q(\分支指令地址6 ), .clk(CLK));  // open: clr
  Register #(.width(32)) \u_分支指令地址_8  (.D(\分支指令地址 ), .en(Set7), .Q(\分支指令地址7 ), .clk(CLK));  // open: clr
  // Probe on \bht状态转换_2_nstate 
  or or_1 (or_1_out, L6, Set6);
  or or_2 (or_2_out, L0, Set0);
  or or_3 (or_3_out, L1, Set1);
  or or_4 (or_4_out, L2, Set2);
  or or_5 (or_5_out, L3, Set3);
  or or_6 (or_6_out, L4, Set4);
  or or_7 (or_7_out, L5, Set5);
  or or_8 (or_8_out, L7, Set7);
  \BHT状态转换  \bht状态转换_1  (.state(\分支预测历史_q ), .\分支 (\分支 ), .nstate(\bht状态转换_1_nstate ), .Set(Set0));
  Register #(.width(2)) \u_分支预测历史  (.D(\bht状态转换_1_nstate ), .en(or_2_out), .Q(\分支预测历史_q ), .clk(CLK));  // open: clr
  assign \分支预测历史  = Eq0 ? \分支预测历史_q  : 2'bz;  // Controlled_Buffer controlled_buffer_1
  \BHT状态转换  \bht状态转换_2  (.state(\分支预测历史_2_q ), .\分支 (\分支 ), .nstate(\bht状态转换_2_nstate ), .Set(Set1));
  assign \分支预测历史  = Eq1 ? \分支预测历史_2_q  : 2'bz;  // Controlled_Buffer controlled_buffer_2
  Register #(.width(2)) \u_分支预测历史_2  (.D(\bht状态转换_2_nstate ), .en(or_3_out), .Q(\分支预测历史_2_q ), .clk(CLK));  // open: clr
  \BHT状态转换  \bht状态转换_3  (.state(\分支预测历史_3_q ), .\分支 (\分支 ), .nstate(\bht状态转换_3_nstate ), .Set(Set2));
  assign \分支预测历史  = Eq2 ? \分支预测历史_3_q  : 2'bz;  // Controlled_Buffer controlled_buffer_3
  Register #(.width(2)) \u_分支预测历史_3  (.D(\bht状态转换_3_nstate ), .en(or_4_out), .Q(\分支预测历史_3_q ), .clk(CLK));  // open: clr
  \BHT状态转换  \bht状态转换_4  (.state(\分支预测历史_4_q ), .\分支 (\分支 ), .nstate(\bht状态转换_4_nstate ), .Set(Set3));
  assign \分支预测历史  = Eq3 ? \分支预测历史_4_q  : 2'bz;  // Controlled_Buffer controlled_buffer_4
  Register #(.width(2)) \u_分支预测历史_4  (.D(\bht状态转换_4_nstate ), .en(or_5_out), .Q(\分支预测历史_4_q ), .clk(CLK));  // open: clr
  \BHT状态转换  \bht状态转换_5  (.state(\分支预测历史_5_q ), .\分支 (\分支 ), .nstate(\bht状态转换_5_nstate ), .Set(Set4));
  Register #(.width(2)) \u_分支预测历史_5  (.D(\bht状态转换_5_nstate ), .en(or_6_out), .Q(\分支预测历史_5_q ), .clk(CLK));  // open: clr
  assign \分支预测历史  = Eq4 ? \分支预测历史_5_q  : 2'bz;  // Controlled_Buffer controlled_buffer_5
  \BHT状态转换  \bht状态转换_6  (.state(\分支预测历史_6_q ), .\分支 (\分支 ), .nstate(\bht状态转换_6_nstate ), .Set(Set5));
  assign \分支预测历史  = Eq5 ? \分支预测历史_6_q  : 2'bz;  // Controlled_Buffer controlled_buffer_6
  Register #(.width(2)) \u_分支预测历史_6  (.D(\bht状态转换_6_nstate ), .en(or_7_out), .Q(\分支预测历史_6_q ), .clk(CLK));  // open: clr
  \BHT状态转换  \bht状态转换_7  (.state(\分支预测历史_7_q ), .\分支 (\分支 ), .nstate(\bht状态转换_7_nstate ), .Set(Set6));
  assign \分支预测历史  = Eq6 ? \分支预测历史_7_q  : 2'bz;  // Controlled_Buffer controlled_buffer_7
  Register #(.width(2)) \u_分支预测历史_7  (.D(\bht状态转换_7_nstate ), .en(or_1_out), .Q(\分支预测历史_7_q ), .clk(CLK));  // open: clr
  \BHT状态转换  \bht状态转换_8  (.state(\分支预测历史_8_q ), .\分支 (\分支 ), .nstate(\bht状态转换_8_nstate ), .Set(Set7));
  Register #(.width(2)) \u_分支预测历史_8  (.D(\bht状态转换_8_nstate ), .en(or_8_out), .Q(\分支预测历史_8_q ), .clk(CLK));  // open: clr
  assign \分支预测历史  = Eq7 ? \分支预测历史_8_q  : 2'bz;  // Controlled_Buffer controlled_buffer_8
  counter counter_1 (.add1(1'b1), .clk(CLK), .clr(or_9_out), .Counter_out(C0));
  counter counter_2 (.add1(1'b1), .clk(CLK), .clr(or_10_out), .Counter_out(C1));
  counter counter_3 (.add1(1'b1), .clk(CLK), .clr(or_11_out), .Counter_out(C2));
  counter counter_4 (.add1(1'b1), .clk(CLK), .clr(or_12_out), .Counter_out(C3));
  counter counter_5 (.add1(1'b1), .clk(CLK), .clr(or_13_out), .Counter_out(C4));
  counter counter_6 (.add1(1'b1), .clk(CLK), .clr(or_14_out), .Counter_out(C5));
  counter counter_7 (.add1(1'b1), .clk(CLK), .clr(or_15_out), .Counter_out(C6));
  counter counter_8 (.add1(1'b1), .clk(CLK), .clr(or_16_out), .Counter_out(C7));
  Adder #(.width(32)) adder_1 (.a(in_1), .b(32'h4), .out(PC_4));  // open: cin, cout
  or or_9 (or_9_out, L0, Set0);
  or or_10 (or_10_out, L1, Set1);
  or or_11 (or_11_out, L2, Set2);
  or or_12 (or_12_out, L3, Set3);
  or or_13 (or_13_out, L4, Set4);
  or or_14 (or_14_out, L5, Set5);
  or or_15 (or_15_out, L6, Set6);
  or or_16 (or_16_out, L7, Set7);
  assign SlotData = Eq0 ? \分支目标地址_q  : 32'bz;  // Controlled_Buffer controlled_buffer_9
  Register #(.width(32)) \u_分支目标地址  (.D(\分支目标地址 ), .en(Set0), .Q(\分支目标地址_q ), .clk(CLK));  // open: clr
  assign SlotData = Eq1 ? \数据块副本_q  : 32'bz;  // Controlled_Buffer controlled_buffer_10
  Register #(.width(32)) \u_数据块副本  (.D(\分支目标地址 ), .en(Set1), .Q(\数据块副本_q ), .clk(CLK));  // open: clr
  Register #(.width(32)) \u_数据块副本_2  (.D(\分支目标地址 ), .en(Set2), .Q(\数据块副本_2_q ), .clk(CLK));  // open: clr
  assign SlotData = Eq2 ? \数据块副本_2_q  : 32'bz;  // Controlled_Buffer controlled_buffer_11
  Register #(.width(32)) \u_数据块副本_3  (.D(\分支目标地址 ), .en(Set3), .Q(\数据块副本_3_q ), .clk(CLK));  // open: clr
  assign SlotData = Eq3 ? \数据块副本_3_q  : 32'bz;  // Controlled_Buffer controlled_buffer_12
  Register #(.width(32)) \u_数据块副本_4  (.D(\分支目标地址 ), .en(Set4), .Q(\数据块副本_4_q ), .clk(CLK));  // open: clr
  assign SlotData = Eq4 ? \数据块副本_4_q  : 32'bz;  // Controlled_Buffer controlled_buffer_13
  assign SlotData = Eq5 ? \数据块副本_5_q  : 32'bz;  // Controlled_Buffer controlled_buffer_14
  Register #(.width(32)) \u_数据块副本_5  (.D(\分支目标地址 ), .en(Set5), .Q(\数据块副本_5_q ), .clk(CLK));  // open: clr
  Register #(.width(32)) \u_数据块副本_6  (.D(\分支目标地址 ), .en(Set6), .Q(\数据块副本_6_q ), .clk(CLK));  // open: clr
  assign SlotData = Eq6 ? \数据块副本_6_q  : 32'bz;  // Controlled_Buffer controlled_buffer_15
  assign SlotData = Eq7 ? \数据块副本_7_q  : 32'bz;  // Controlled_Buffer controlled_buffer_16
  Register #(.width(32)) \u_数据块副本_7  (.D(\分支目标地址 ), .en(Set7), .Q(\数据块副本_7_q ), .clk(CLK));  // open: clr
  Multiplexer #(.select(2), .width(32), .enable("false")) multiplexer_1 (
    .in0(PC_4), .in1(PC_4), .in2(SlotData), .in3(SlotData), .out(multiplexer_1_out), .sel(\分支预测历史 ));
  Multiplexer #(.width(32), .enable("false")) multiplexer_2 (
    .in0(multiplexer_1_out), .in1(PC_4), .out(DataOut), .sel(PCMiss));
  Max3 max3_1 (.Y(C1), .X(C0), .Y_num(3'b001), .X_num(3'b000), .MAX(max3_1_max), .Max_num(max3_1_max_num));
  Max3 max3_2 (.Y(C3), .X(C2), .Y_num(3'b011), .X_num(3'b010), .MAX(max3_2_max), .Max_num(max3_2_max_num));
  Max3 max3_3 (.Y(C5), .X(C4), .Y_num(3'b101), .X_num(3'b100), .MAX(max3_3_max), .Max_num(max3_3_max_num));
  Max3 max3_4 (.Y(C7), .X(C6), .Y_num(3'b111), .X_num(3'b110), .MAX(max3_4_max), .Max_num(max3_4_max_num));
  Decoder #(.select(3), .enable("false")) decoder_1 (
    .out0(decoder_1_out0), .out1(decoder_1_out1), .out2(decoder_1_out2), .out3(decoder_1_out3),
    .out4(decoder_1_out4), .out5(decoder_1_out5), .out6(decoder_1_out6), .out7(decoder_1_out7),
    .sel(max3_7_max_num));
  Max3 max3_5 (
    .Y(max3_2_max), .X(max3_1_max), .Y_num(max3_2_max_num), .X_num(max3_1_max_num), .MAX(max3_5_max),
    .Max_num(max3_5_max_num));
  Max3 max3_6 (
    .Y(max3_4_max), .X(max3_3_max), .Y_num(max3_4_max_num), .X_num(max3_3_max_num), .MAX(max3_6_max),
    .Max_num(max3_6_max_num));
  Multiplexer #(.enable("false")) multiplexer_3 (
    .in0(decoder_1_out0), .in1(not_1_out), .out(multiplexer_3_out), .sel(nand_1_out));
  not not_1 (not_1_out, V0);
  and and_1 (and_1_out, V0, ~V1);  // AND_Gate
  and and_2 (and_2_out, V0, V1, ~V2);  // AND_Gate
  and and_3 (and_3_out, V0, V1, V2, ~V3);  // AND_Gate
  and and_4 (and_4_out, V0, V1, V2, V3, ~V4);  // AND_Gate
  and and_5 (and_5_out, V0, V1, V2, V3, V4, ~V5);  // AND_Gate
  and and_6 (and_6_out, V0, V1, V2, V3, V4, V5, ~V6);  // AND_Gate
  and and_7 (and_7_out, V0, V1, V2, V3, V4, V5, V6, ~V7);  // AND_Gate
  nand nand_1 (nand_1_out, V0, V1, V2, V3, V4, V5, V6, V7);
  Max3 max3_7 (
    .Y(max3_6_max), .X(max3_5_max), .Y_num(max3_6_max_num), .X_num(max3_5_max_num), .Max_num(max3_7_max_num));  // open: MAX
  Comparator #(.width(32)) comparator_1 (.a(in_1), .b(\分支指令地址0 ), .eq(comparator_1_eq));  // open: gt, lt
  Comparator #(.width(32)) comparator_2 (.a(in_1), .b(\分支指令地址1 ), .eq(comparator_2_eq));  // open: gt, lt
  Comparator #(.width(32)) comparator_3 (.a(in_1), .b(\分支指令地址2 ), .eq(comparator_3_eq));  // open: gt, lt
  Comparator #(.width(32)) comparator_4 (.a(in_1), .b(\分支指令地址3 ), .eq(comparator_4_eq));  // open: gt, lt
  Comparator #(.width(32)) comparator_5 (.a(in_1), .b(\分支指令地址4 ), .eq(comparator_5_eq));  // open: gt, lt
  Comparator #(.width(32)) comparator_6 (.a(in_1), .b(\分支指令地址5 ), .eq(comparator_6_eq));  // open: gt, lt
  Comparator #(.width(32)) comparator_7 (.a(in_1), .b(\分支指令地址6 ), .eq(comparator_7_eq));  // open: gt, lt
  Comparator #(.width(32)) comparator_8 (.a(in_1), .b(\分支指令地址7 ), .eq(comparator_8_eq));  // open: gt, lt
  Multiplexer #(.enable("false")) multiplexer_4 (
    .in0(decoder_1_out1), .in1(and_1_out), .out(multiplexer_4_out), .sel(nand_1_out));
  Multiplexer #(.enable("false")) multiplexer_5 (
    .in0(decoder_1_out2), .in1(and_2_out), .out(multiplexer_5_out), .sel(nand_1_out));
  and and_8 (Eq0, V0, comparator_1_eq);
  and and_9 (Eq1, V1, comparator_2_eq);
  and and_10 (Eq2, V2, comparator_3_eq);
  and and_11 (Eq3, V3, comparator_4_eq);
  and and_12 (Eq4, V4, comparator_5_eq);
  and and_13 (Eq5, V5, comparator_6_eq);
  and and_14 (Eq6, V6, comparator_7_eq);
  and and_15 (Eq7, V7, comparator_8_eq);
  Multiplexer #(.enable("false")) multiplexer_6 (
    .in0(decoder_1_out3), .in1(and_3_out), .out(multiplexer_6_out), .sel(nand_1_out));
  Multiplexer #(.enable("false")) multiplexer_7 (
    .in0(decoder_1_out4), .in1(and_4_out), .out(multiplexer_7_out), .sel(nand_1_out));
  Multiplexer #(.enable("false")) multiplexer_8 (
    .in0(decoder_1_out5), .in1(and_5_out), .out(multiplexer_8_out), .sel(nand_1_out));
  Multiplexer #(.enable("false")) multiplexer_9 (
    .in0(decoder_1_out6), .in1(and_6_out), .out(multiplexer_9_out), .sel(nand_1_out));
  Multiplexer #(.enable("false")) multiplexer_10 (
    .in0(decoder_1_out7), .in1(and_7_out), .out(multiplexer_10_out), .sel(nand_1_out));
  and and_16 (Set0, Miss, Enable, multiplexer_3_out);
  and and_17 (Set1, Miss, Enable, multiplexer_4_out);
  and and_18 (Set2, Miss, Enable, multiplexer_5_out);
  and and_19 (Set3, Miss, Enable, multiplexer_6_out);
  and and_20 (Set4, Miss, Enable, multiplexer_7_out);
  and and_21 (Set5, Miss, Enable, multiplexer_8_out);
  and and_22 (Set6, Miss, Enable, multiplexer_9_out);
  and and_23 (Set7, Miss, Enable, multiplexer_10_out);
  nor nor_1 (PCMiss, Eq0, Eq1, Eq2, Eq3, Eq4, Eq5, Eq6, Eq7);
  Comparator #(.width(32)) comparator_9 (.a(\分支指令地址 ), .b(\分支指令地址0 ), .eq(comparator_9_eq));  // open: gt, lt
  Comparator #(.width(32)) comparator_10 (.a(\分支指令地址 ), .b(\分支指令地址1 ), .eq(comparator_10_eq));  // open: gt, lt
  Comparator #(.width(32)) comparator_11 (.a(\分支指令地址 ), .b(\分支指令地址2 ), .eq(comparator_11_eq));  // open: gt, lt
  Comparator #(.width(32)) comparator_12 (.a(\分支指令地址 ), .b(\分支指令地址3 ), .eq(comparator_12_eq));  // open: gt, lt
  Comparator #(.width(32)) comparator_13 (.a(\分支指令地址 ), .b(\分支指令地址4 ), .eq(comparator_13_eq));  // open: gt, lt
  Comparator #(.width(32)) comparator_14 (.a(\分支指令地址 ), .b(\分支指令地址5 ), .eq(comparator_14_eq));  // open: gt, lt
  Comparator #(.width(32)) comparator_15 (.a(\分支指令地址 ), .b(\分支指令地址6 ), .eq(comparator_15_eq));  // open: gt, lt
  Comparator #(.width(32)) comparator_16 (.a(\分支指令地址 ), .b(\分支指令地址7 ), .eq(comparator_16_eq));  // open: gt, lt
  and and_24 (L0, V0, comparator_9_eq);
  and and_25 (L1, V1, comparator_10_eq);
  and and_26 (L2, V2, comparator_11_eq);
  and and_27 (L3, V3, comparator_12_eq);
  and and_28 (L4, V4, comparator_13_eq);
  and and_29 (L5, V5, comparator_14_eq);
  and and_30 (L6, V6, comparator_15_eq);
  and and_31 (L7, V7, comparator_16_eq);
  nor nor_2 (nor_2_out, L0, L1, L2, L3, L4, L5, L6, L7);
  and and_32 (Miss, \跳转 , nor_2_out);

  // Other names for the same wires on the sheet: En = Enable; PC[31:0] = in_1
endmodule

module Max3 (
  input  [15:0] Y,
  input  [15:0] X,
  input  [2:0] Y_num,
  input  [2:0] X_num,
  output [15:0] MAX,
  output [2:0] Max_num
);

  wire comparator_1_eq, comparator_1_gt, or_1_out;

  Multiplexer #(.width(16), .enable("false")) multiplexer_1 (.in0(Y), .in1(X), .out(MAX), .sel(or_1_out));
  Comparator #(.width(16), .mode("unsigned")) comparator_1 (
    .a(X), .b(Y), .gt(comparator_1_gt), .eq(comparator_1_eq));  // open: lt
  or or_1 (or_1_out, comparator_1_gt, comparator_1_eq);
  Multiplexer #(.width(3), .enable("false")) multiplexer_2 (.in0(Y_num), .in1(X_num), .out(Max_num), .sel(or_1_out));

  // Notes on the sheet:
  //   输出两个输入中的较大值，并输出较大值的3位编号
endmodule

module \BHT状态转换  (
  input  [1:0] state,
  input  \分支 ,
  input  Set,
  output [1:0] nstate
);

  wire and_1_out, and_2_out, and_3_out, and_4_out, and_5_out, and_6_out, and_7_out, and_8_out, and_9_out,
       and_10_out, or_1_out, or_2_out, or_3_out;
  wire [1:0] multiplexer_1_out, multiplexer_2_out, multiplexer_3_out;

  and and_1 (and_1_out, ~\分支 , state[0], state[1]);  // AND_Gate
  and and_2 (and_2_out, ~\分支 , state[0], ~state[1]);  // AND_Gate
  and and_3 (and_3_out, ~\分支 , ~state[0], ~state[1]);  // AND_Gate
  and and_4 (and_4_out, \分支 , ~state[0], ~state[1]);  // AND_Gate
  and and_5 (and_5_out, \分支 , state[0], ~state[1]);  // AND_Gate
  and and_6 (and_6_out, \分支 , ~state[0], state[1]);  // AND_Gate
  and and_7 (and_7_out, \分支 , state[0], state[1]);
  and and_8 (and_8_out, ~\分支 , ~state[0], state[1]);  // AND_Gate
  or or_1 (or_1_out, and_1_out, and_2_out, and_3_out);
  or or_2 (or_2_out, and_5_out, and_6_out, and_7_out);
  and and_9 (and_9_out, and_8_out, ~or_2_out);  // AND_Gate
  Multiplexer #(.width(2), .enable("false")) multiplexer_1 (
    .in0(2'b10), .in1(2'b11), .out(multiplexer_1_out), .sel(and_9_out));
  and and_10 (and_10_out, and_4_out, ~or_1_out);  // AND_Gate
  Multiplexer #(.width(2), .enable("false")) multiplexer_2 (
    .in0(2'b00), .in1(2'b01), .out(multiplexer_2_out), .sel(and_10_out));
  or or_3 (or_3_out, or_2_out, and_8_out);
  Multiplexer #(.width(2), .enable("false")) multiplexer_3 (
    .in0(multiplexer_2_out), .in1(multiplexer_1_out), .out(multiplexer_3_out), .sel(or_3_out));
  Multiplexer #(.width(2), .enable("false")) multiplexer_4 (
    .in0(multiplexer_3_out), .in1(2'b10), .out(nstate), .sel(Set));
endmodule

module \控制信号生成2  (
  input  OP0,
  input  OP1,
  input  OP2,
  input  OP3,
  input  OP4,
  input  OP5,
  input  F0,
  input  F1,
  input  F2,
  input  F3,
  input  F4,
  input  F5,
  output Shift,
  output MemtoPC,
  output LUH
);

  wire not_1_out, not_2_out, not_3_out, not_4_out, not_5_out, not_6_out, not_7_out, not_8_out, not_9_out;

  not not_1 (not_1_out, OP5);
  not not_2 (not_2_out, OP4);
  not not_3 (not_3_out, OP5);
  not not_4 (not_4_out, OP4);
  not not_5 (not_5_out, OP3);
  not not_6 (not_6_out, OP0);
  not not_7 (not_7_out, OP4);
  not not_8 (not_8_out, OP3);
  not not_9 (not_9_out, OP1);
  and and_1 (Shift, not_1_out, not_2_out, OP3, OP2, OP1, OP0);
  and and_2 (MemtoPC, not_3_out, not_4_out, not_5_out, OP2, OP1, not_6_out);
  and and_3 (LUH, OP5, not_7_out, not_8_out, OP2, not_9_out, OP0);
endmodule

module counter (
  input  add1,
  input  clk,
  input  clr,
  output [15:0] Counter_out
);

  wire [15:0] adder_1_out, multiplexer_1_out, multiplexer_2_out;

  Adder #(.width(16)) adder_1 (.a(Counter_out), .b(16'h1), .out(adder_1_out));  // open: cin, cout
  Multiplexer #(.width(16), .enable("false")) multiplexer_1 (
    .in0(Counter_out), .in1(adder_1_out), .out(multiplexer_1_out), .sel(add1));
  Multiplexer #(.width(16), .enable("false")) multiplexer_2 (
    .in0(multiplexer_1_out), .in1({16{1'b0}}), .out(multiplexer_2_out), .sel(clr));
  Register #(.width(16)) register_1 (.D(multiplexer_2_out), .Q(Counter_out), .clk(clk));  // open: en, clr
endmodule
