// Logisim project 气泡流水线.circ as structural Verilog: 12 circuits, main circuit ◇单周期MIPS
module \单周期MIPS  (
);

  wire and_1_out, and_2_out, and_3_out, and_4_out, and_5_out, and_6_out, Bub, CLK, comparator_1_eq,
       ex_mem_1_jalout, ex_mem_1_memtoregout, ex_mem_1_memwriteout, ex_mem_1_systemcallout, EX_RegWrite, Go,
       id_ex_1_alusrcout, id_ex_1_beqout, id_ex_1_bneout, id_ex_1_memtoregout, id_ex_1_memwriteout,
       id_ex_1_systemcallout, JAL, JMP, JR, MEM_RegWrite, mem_wb_1_jalout, mem_wb_1_memtoregout,
       mips_alu_1_equal, not_1_out, not_2_out, or_2_out, or_3_out, or_4_out, PCen, RegWrite, Relevant, RST,
       SignedExt, syscall, \硬布线控制器_1_alu_src , \硬布线控制器_1_beq , \硬布线控制器_1_bne , \硬布线控制器_1_jal ,
       \硬布线控制器_1_jmp , \硬布线控制器_1_jr , \硬布线控制器_1_memtoreg , \硬布线控制器_1_memwrite , \硬布线控制器_1_regdst ,
       \硬布线控制器_1_regwrite , \硬布线控制器_1_syscall ;
  wire [2:2] or_5_out;
  wire [3:0] id_ex_1_aluopout, \硬布线控制器_1_alu_op ;
  wire [4:0] EX_WriteReg, id_ex_1_shamtout, MEM_WriteReg, multiplexer_4_out, multiplexer_6_out, R1_num,
       R2_num, shamt, WriteRegSign;
  wire [5:0] FUNC, OP;
  wire [15:0] \总周期数 , \插入气泡数 , \无条件分支数 , \条件分支成功数 ;
  wire [25:11] if_id_1_irout;
  wire [31:0] adder_1_out, adder_2_out, Aout, bit_extender_1_out, bit_extender_2_out, Din, ex_mem_1_aluout,
       ex_mem_1_aout, ex_mem_1_bout, ex_mem_1_irout, ex_mem_1_pc_4out, ex_mem_1_pcout, id_ex_1_bout,
       id_ex_1_eimmout, id_ex_1_immout, id_ex_1_pc_4out, id_ex_1_pcout, if_id_1_pc_4out, if_id_1_pcout, IR,
       IRI, LedData, mem_wb_1_aluout, mem_wb_1_mdout, mem_wb_1_pc_4out, mips_alu_1_result,
       mips_regifile_1_r1, mips_regifile_1_r2, multiplexer_1_out, multiplexer_5_out, multiplexer_7_out,
       multiplexer_8_out, PC, PC_q, R1, R2, ram_1_data, rom_1_data, shifter_1_out;

  Button \u_总复位  (.out(RST));
  Button u_Go (.out(Go));
  Clock clock_1 (.out(CLK));
  Multiplexer #(.select(3), .width(32), .enable("false")) multiplexer_1 (
    .in0(adder_1_out), .in1(Aout), .in2({adder_2_out[31:28], IRI[25:0], 2'b00}), .in3(Aout),
    .in4(adder_2_out), .in5(Aout), .in6({adder_2_out[31:28], IRI[25:0], 2'b00}), .in7(Aout),
    .out(multiplexer_1_out), .sel({or_5_out[2], JMP, JR}));
  and and_1 (and_1_out, PCen, not_1_out);
  Hex_Digit_Display hex_digit_display_1 (.value(LedData[27:24]));  // open: dp
  Hex_Digit_Display hex_digit_display_2 (.value(LedData[31:28]));  // open: dp
  Register #(.width(32)) u_PC (.D(multiplexer_1_out), .en(and_1_out), .Q(PC_q), .clk(CLK), .clr(RST));
  not not_1 (not_1_out, Relevant);
  Hex_Digit_Display hex_digit_display_3 (.value(LedData[23:20]));  // open: dp
  Hex_Digit_Display hex_digit_display_4 (.value(LedData[19:16]));  // open: dp
  or or_1 (Bub, or_5_out[2], JMP);
  not not_2 (not_2_out, PCen);
  Hex_Digit_Display hex_digit_display_5 (.value(LedData[11:8]));  // open: dp
  Hex_Digit_Display hex_digit_display_6 (.value(LedData[15:12]));  // open: dp
  Counter #(.width(16), .max('hffff)) counter_1 (
    .count(or_2_out), .Q(\无条件分支数 ), .clk(CLK), .clr(RST));  // open: load, D, carry
  or or_2 (or_2_out, JR, JMP, JAL);
  Adder #(.width(32)) adder_1 (.a(PC_q), .b(32'h4), .out(adder_1_out));  // open: cin, cout
  or or_3 (or_3_out, Relevant, not_2_out);
  \数据相关检测  \u_数据相关检测_1  (
    .EX_WriteReg(EX_WriteReg), .OP_CODE(OP), .R1(R1_num), .MEM_WriteReg(MEM_WriteReg), .FUNC(FUNC),
    .R2(R2_num), .EX_RegWrite(EX_RegWrite), .Relevant(Relevant), .MEM_RegWrite(MEM_RegWrite));
  Hex_Digit_Display hex_digit_display_7 (.value(LedData[7:4]));  // open: dp
  Hex_Digit_Display hex_digit_display_8 (.value(LedData[3:0]));  // open: dp
  ROM #(.addrWidth(10), .dataWidth(32)) rom_1 (.addr(PC_q[11:2]), .data(rom_1_data));  // open: sel
  IF_ID if_id_1 (
    .PCin(PC_q), .IRin(rom_1_data), .CLK(CLK), .PCout(if_id_1_pcout),
    .IRout({OP, if_id_1_irout, shamt, FUNC}), .\同步清零 (Bub), .\使能端 (or_3_out), .PC_4in(adder_1_out),
    .PC_4out(if_id_1_pc_4out));
  Multiplexer #(.width(5), .enable("false")) multiplexer_2 (
    .in0(if_id_1_irout[25:21]), .in1(5'b00010), .out(R1_num), .sel(\硬布线控制器_1_syscall ));
  assign bit_extender_1_out = {{16{1'b0}}, {if_id_1_irout[15:11], shamt, FUNC}};  // Bit_Extender bit_extender_1
  assign bit_extender_2_out = {{16{if_id_1_irout[15]}}, {if_id_1_irout[15:11], shamt, FUNC}};  // Bit_Extender bit_extender_2
  // Probe on \总周期数 
  // Probe on \无条件分支数 
  // Probe on \条件分支成功数 
  // Probe on \插入气泡数 
  \硬布线控制器  \u_硬布线控制器_1  (
    .Func(FUNC), .OP(OP), .ALU_OP(\硬布线控制器_1_alu_op ), .MemToReg(\硬布线控制器_1_memtoreg ),
    .MemWrite(\硬布线控制器_1_memwrite ), .ALU_SRC(\硬布线控制器_1_alu_src ), .RegWrite(\硬布线控制器_1_regwrite ),
    .SysCALL(\硬布线控制器_1_syscall ), .SignedExt(SignedExt), .RegDst(\硬布线控制器_1_regdst ), .JR(\硬布线控制器_1_jr ),
    .JMP(\硬布线控制器_1_jmp ), .Beq(\硬布线控制器_1_beq ), .JAL(\硬布线控制器_1_jal ), .Bne(\硬布线控制器_1_bne ));
  Multiplexer #(.width(5), .enable("false")) multiplexer_3 (
    .in0(if_id_1_irout[20:16]), .in1(5'b00100), .out(R2_num), .sel(\硬布线控制器_1_syscall ));
  Multiplexer #(.width(5), .enable("false")) multiplexer_4 (
    .in0(if_id_1_irout[20:16]), .in1(if_id_1_irout[15:11]), .out(multiplexer_4_out), .sel(\硬布线控制器_1_regdst ));
  Multiplexer #(.width(32), .enable("false")) multiplexer_5 (
    .in0(bit_extender_1_out), .in1(bit_extender_2_out), .out(multiplexer_5_out), .sel(SignedExt));
  Multiplexer #(.width(5), .enable("false")) multiplexer_6 (
    .in0(multiplexer_4_out), .in1({5{1'b1}}), .out(multiplexer_6_out), .sel(\硬布线控制器_1_jal ));
  Counter #(.width(16), .max('hffff)) counter_2 (
    .count(and_2_out), .Q(\插入气泡数 ), .clk(CLK), .clr(RST));  // open: load, D, carry
  and and_2 (and_2_out, PCen, Relevant);
  Comparator #(.width(32)) comparator_1 (.a(R1), .b(32'h22), .eq(comparator_1_eq));  // open: gt, lt
  MIPS_Regifile mips_regifile_1 (
    .Din(Din), .Clk(CLK), .R1(mips_regifile_1_r1), .R2(mips_regifile_1_r2), .WE(RegWrite),
    .W_num(WriteRegSign), .R1_num(R1_num), .R2_num(R2_num));
  or or_4 (or_4_out, Relevant, Bub);
  ID_EX id_ex_1 (
    .PCin(if_id_1_pcout), .IRin({OP, if_id_1_irout, shamt, FUNC}), .Ain(mips_regifile_1_r1),
    .Bin(mips_regifile_1_r2), .IMMin(multiplexer_5_out), .CLK(CLK), .PCout(id_ex_1_pcout), .IRout(IRI),
    .Aout(Aout), .Bout(id_ex_1_bout), .IMMout(id_ex_1_immout), .\同步清零 (or_4_out), .\使能端 (not_2_out),
    .MemToRegin(\硬布线控制器_1_memtoreg ), .MemToRegout(id_ex_1_memtoregout), .MemWritein(\硬布线控制器_1_memwrite ),
    .MemWriteout(id_ex_1_memwriteout), .AluOPin(\硬布线控制器_1_alu_op ), .AluOPout(id_ex_1_aluopout),
    .AluSrcin(\硬布线控制器_1_alu_src ), .AluSrcout(id_ex_1_alusrcout), .RegWritein(\硬布线控制器_1_regwrite ),
    .RegWriteout(EX_RegWrite), .WriteRegin(multiplexer_6_out), .WriteRegout(EX_WriteReg),
    .JALin(\硬布线控制器_1_jal ), .JALout(JAL), .PC_4in(if_id_1_pc_4out), .PC_4out(id_ex_1_pc_4out),
    .EIMMin(bit_extender_2_out), .EIMMout(id_ex_1_eimmout), .Bnein(\硬布线控制器_1_bne ), .Bneout(id_ex_1_bneout),
    .Beqin(\硬布线控制器_1_beq ), .Beqout(id_ex_1_beqout), .JMPin(\硬布线控制器_1_jmp ), .JMPout(JMP), .JRout(JR),
    .JRin(\硬布线控制器_1_jr ), .Systemcallin(\硬布线控制器_1_syscall ), .Systemcallout(id_ex_1_systemcallout),
    .Shamtin(shamt), .Shamtout(id_ex_1_shamtout));
  and and_3 (and_3_out, comparator_1_eq, syscall);
  // Probe on multiplexer_7_out
  Multiplexer #(.width(32), .enable("false")) multiplexer_7 (
    .in0(id_ex_1_bout), .in1(id_ex_1_immout), .out(multiplexer_7_out), .sel(id_ex_1_alusrcout));
  Register #(.width(32)) register_1 (.D(R2), .en(and_3_out), .Q(LedData), .clk(CLK), .clr(RST));
  and and_4 (and_4_out, ~comparator_1_eq, syscall);  // AND_Gate
  MIPS_ALU mips_alu_1 (
    .X(Aout), .Y(multiplexer_7_out), .AluOP(id_ex_1_aluopout), .Equal(mips_alu_1_equal),
    .Result(mips_alu_1_result), .shamt(id_ex_1_shamtout));  // open: Result_2
  Shifter #(.width(32)) shifter_1 (.in(id_ex_1_eimmout), .\dist (5'b00010), .out(shifter_1_out));
  and and_5 (and_5_out, mips_alu_1_equal, id_ex_1_beqout);
  and and_6 (and_6_out, ~mips_alu_1_equal, id_ex_1_bneout);  // AND_Gate
  EX_MEM ex_mem_1 (
    .MemToRegin(id_ex_1_memtoregout), .MemToRegout(ex_mem_1_memtoregout), .MemWritein(id_ex_1_memwriteout),
    .MemWriteout(ex_mem_1_memwriteout), .RegWritein(EX_RegWrite), .RegWriteout(MEM_RegWrite),
    .PCin(id_ex_1_pcout), .PCout(ex_mem_1_pcout), .IRin(IRI), .IRout(ex_mem_1_irout), .Bin(id_ex_1_bout),
    .Bout(ex_mem_1_bout), .CLK(CLK), .\同步清零 (RST), .\使能端 (not_2_out), .ALUin(mips_alu_1_result),
    .ALUout(ex_mem_1_aluout), .WriteRegin(EX_WriteReg), .WriteRegout(MEM_WriteReg), .JALin(JAL),
    .JALout(ex_mem_1_jalout), .PC_4in(id_ex_1_pc_4out), .PC_4out(ex_mem_1_pc_4out),
    .Systemcallin(id_ex_1_systemcallout), .Systemcallout(ex_mem_1_systemcallout), .Ain(Aout),
    .Aout(ex_mem_1_aout));
  Adder #(.width(32)) adder_2 (.a(shifter_1_out), .b(id_ex_1_pc_4out), .out(adder_2_out));  // open: cin, cout
  not not_3 (PCen, and_4_out);
  or or_5 (or_5_out[2], and_5_out, and_6_out);
  Counter #(.width(16), .max('hffff)) counter_3 (
    .count(PCen), .Q(\总周期数 ), .clk(CLK), .clr(RST));  // open: load, D, carry
  Counter #(.width(16), .max('hffff)) counter_4 (
    .count(or_5_out[2]), .Q(\条件分支成功数 ), .clk(CLK), .clr(RST));  // open: load, D, carry
  // Probe on nothing
  RAM #(.addrWidth(10), .dataWidth(32), .bus("separate")) ram_1 (
    .addr(ex_mem_1_aluout[11:2]), .din(ex_mem_1_bout), .data(ram_1_data), .str(ex_mem_1_memwriteout),
    .sel(1'b1), .clk(CLK), .ld(ex_mem_1_memtoregout), .clr(RST));
  MEM_WB mem_wb_1 (
    .RegWritein(MEM_RegWrite), .IRin(ex_mem_1_irout), .PCin(ex_mem_1_pcout), .ALUin(ex_mem_1_aluout),
    .MDin(ram_1_data), .CLK(CLK), .RegWriteout(RegWrite), .IRout(IR), .PCout(PC), .ALUout(mem_wb_1_aluout),
    .MDout(mem_wb_1_mdout), .\同步清零 (RST), .\使能端 (not_2_out), .MemToRegin(ex_mem_1_memtoregout),
    .MemToRegout(mem_wb_1_memtoregout), .WriteRegin(MEM_WriteReg), .WriteRegout(WriteRegSign),
    .JALin(ex_mem_1_jalout), .JALout(mem_wb_1_jalout), .PC_4in(ex_mem_1_pc_4out), .PC_4out(mem_wb_1_pc_4out),
    .Systemcallin(ex_mem_1_systemcallout), .Systemcallout(syscall), .Ain(ex_mem_1_aout), .Aout(R1),
    .Bin(ex_mem_1_bout), .Bout(R2));
  Multiplexer #(.width(32), .enable("false")) multiplexer_8 (
    .in0(mem_wb_1_aluout), .in1(mem_wb_1_mdout), .out(multiplexer_8_out), .sel(mem_wb_1_memtoregout));
  Multiplexer #(.width(32), .enable("false")) multiplexer_9 (
    .in0(multiplexer_8_out), .in1(mem_wb_1_pc_4out), .out(Din), .sel(mem_wb_1_jalout));

  // Notes on the sheet:
  //   数码管输出应该用寄存器锁存，否则显示数据只能一闪而过
  //   可以通过项目增加Logisim库的方式将前几次实验完成的电路作为子电路引入到本电路中使用
  //   指令存储器
  //   数码管输出
  //   contents of rom_1 (hex, n*v repeats v):
  //   20110001 8000c05 20110001 20120002 20130003 8000c09 20110001 20120002 20130003 8000c0d 20110001
  //   20120002 20130003 8000c11 20110001 20120002 20130003 c000cb8 20100001 20110001 118fc0 112020
  //   20020022 c 118882 12200001 8000c15 112020 20020022 c 20110001 118880 112020 20020022 c 12200001
  //   8000c1f 20110001 118fc0 112020 20020022 c 1188c3 112020 20020022 c 118903 112020 20020022 c 118903
  //   112020 20020022 c 118903 112020 20020022 c 118903 112020 20020022 c 118903 112020 20020022 c 118903
  //   112020 20020022 c 118903 112020 20020022 c 20100001 109fc0 139fc3 8021 2012000c 24160003 26100001
  //   3210000f 20080008 20090001 139900 2709825 132020 20020022 c 1094022 1500fff9 22100001 2018000f
  //   2188024 108700 20080008 20090001 139902 2709825 132021 20020022 c 1094022 1500fff9 108702 2c9b022
  //   12c00001 8000c50 4020 1084027 84400 3508ffff 82021 20020022 c 2010ffff 20110000 ae300000 22100001
  //   22310004 ae300000 22100001 22310004 ae300000 22100001 22310004 ae300000 22100001 22310004 ae300000
  //   22100001 22310004 ae300000 22100001 22310004 ae300000 22100001 22310004 ae300000 22100001 22310004
  //   ae300000 22100001 22310004 ae300000 22100001 22310004 ae300000 22100001 22310004 ae300000 22100001
  //   22310004 ae300000 22100001 22310004 ae300000 22100001 22310004 ae300000 22100001 22310004 ae300000
  //   22100001 22310004 22100001 8020 2011003c 8e130000 8e340000 274402a 11000002 ae330000 ae140000
  //   2231fffc 1611fff8 102020 20020022 c 22100004 2011003c 1611fff2 20020032 c 20100000 22100001 102020
  //   20020022 c 22100002 102020 20020022 c 22100003 102020 20020022 c 22100004 102020 20020022 c 22100005
  //   102020 20020022 c 22100006 102020 20020022 c 22100007 102020 20020022 c 22100008 102020 20020022
  //   20020022 c 3e00008
  //   OP
  //   rs
  //   指令字
  //   rt
  //   rd
  //   OP
  //   Func
  //   Func
  //   总复位信号应将除ROM以外所有存储组件全部清零
  //   JR
  //   MemToReg
  //   MemWrite
  //   AluOP
  //   AluSrcB
  //   RegWrite
  //   JAL
  //   RegDst
  //   Syscall
endmodule

// 单周期硬布线控制器
module \硬布线控制器  (
  input  [5:0] OP,
  input  [5:0] Func,
  output [3:0] ALU_OP,
  output MemToReg,
  output MemWrite,
  output ALU_SRC,
  output RegWrite,
  output SysCALL,
  output SignedExt,
  output RegDst,
  output Beq,
  output Bne,
  output JR,
  output JMP,
  output JAL
);

  \运算控制器  \u_运算控制器_1  (
    .OP_CODEq0pm(OP[0]), .OP_CODEq1pm(OP[1]), .OP_CODEq2pm(OP[2]), .OP_CODEq3pm(OP[3]), .OP_CODEq4pm(OP[4]),
    .OP_CODEq5pm(OP[5]), .FUNCq0pm(Func[0]), .FUNCq1pm(Func[1]), .FUNCq2pm(Func[2]), .FUNCq3pm(Func[3]),
    .FUNCq4pm(Func[4]), .FUNCq5pm(Func[5]), .S0(ALU_OP[0]), .S1(ALU_OP[1]), .S2(ALU_OP[2]), .S3(ALU_OP[3]));
  \控制信号生成  \u_控制信号生成_1  (
    .OP_CODEq0pm(OP[0]), .OP_CODEq1pm(OP[1]), .OP_CODEq2pm(OP[2]), .OP_CODEq3pm(OP[3]), .OP_CODEq4pm(OP[4]),
    .OP_CODEq5pm(OP[5]), .FUNCq0pm(Func[0]), .FUNCq1pm(Func[1]), .FUNCq2pm(Func[2]), .FUNCq3pm(Func[3]),
    .FUNCq4pm(Func[4]), .FUNCq5pm(Func[5]), .MemToReg(MemToReg), .MemWrite(MemWrite), .ALU_SRC(ALU_SRC),
    .RegWrite(RegWrite), .SysCALL(SysCALL), .SignedExt(SignedExt), .RegDst(RegDst), .BEQ(Beq), .BNE(Bne),
    .JR(JR), .JMP(JMP), .JAL(JAL));

  // Other names for the same wires on the sheet: OP_CODE[5:0] = OP

  // Notes on the sheet:
  //   运算器控制器，根据指令生成运算器功能选择信号
  //   控制信号生成，产生数据通路需要的其他控制信号
endmodule

// 运算器控制器
module \运算控制器  (
  input  OP_CODEq0pm,
  input  OP_CODEq1pm,
  input  OP_CODEq2pm,
  input  OP_CODEq3pm,
  input  OP_CODEq4pm,
  input  OP_CODEq5pm,
  input  FUNCq0pm,
  input  FUNCq1pm,
  input  FUNCq2pm,
  input  FUNCq3pm,
  input  FUNCq4pm,
  input  FUNCq5pm,
  output S0,
  output S1,
  output S2,
  output S3
);

  wire and_1_out, and_2_out, and_3_out, and_4_out, and_5_out, and_6_out, and_7_out, and_8_out, and_9_out,
       and_10_out, and_11_out, and_12_out, and_13_out, and_14_out, and_15_out, and_16_out, and_17_out,
       and_18_out, and_19_out, and_20_out, and_21_out, and_22_out, and_23_out, and_24_out, and_25_out,
       and_26_out, and_27_out, and_28_out, and_29_out, and_30_out, and_31_out, and_32_out, and_33_out,
       and_34_out, not_1_out, not_2_out, not_3_out, not_4_out, not_5_out, not_6_out, not_7_out, not_8_out,
       not_9_out, not_10_out, not_11_out, not_12_out, not_13_out, not_14_out, not_15_out, not_16_out,
       not_17_out, not_18_out, not_19_out, not_20_out, not_21_out, not_22_out, not_23_out, not_24_out,
       not_25_out, not_26_out, not_27_out, not_28_out, not_29_out, not_30_out, not_31_out, not_32_out,
       not_33_out, not_34_out, not_35_out, not_36_out, not_37_out, not_38_out, not_39_out, not_40_out,
       not_41_out, not_42_out, not_43_out, not_44_out, not_45_out, not_46_out, not_47_out, not_48_out,
       not_49_out, not_50_out, not_51_out, not_52_out, not_53_out, not_54_out, not_55_out, not_56_out,
       not_57_out, not_58_out, not_59_out, not_60_out, not_61_out, not_62_out, not_63_out, not_64_out,
       not_65_out, not_66_out, not_67_out, not_68_out, not_69_out, not_70_out, not_71_out, not_72_out,
       not_73_out, not_74_out, not_75_out, not_76_out, not_77_out, not_78_out, not_79_out, not_80_out,
       not_81_out, not_82_out, not_83_out, not_84_out, not_85_out, not_86_out, not_87_out, not_88_out,
       not_89_out, not_90_out, not_91_out, not_92_out, not_93_out, not_94_out, not_95_out, not_96_out,
       not_97_out, not_98_out, not_99_out, not_100_out, not_101_out, not_102_out, not_103_out, not_104_out,
       not_105_out, not_106_out, not_107_out, not_108_out, not_109_out, not_110_out, not_111_out,
       not_112_out, not_113_out, not_114_out, not_115_out, not_116_out, not_117_out, not_118_out,
       not_119_out, not_120_out, not_121_out, not_122_out, not_123_out, not_124_out, not_125_out,
       not_126_out, not_127_out, not_128_out, not_129_out, not_130_out, not_131_out, not_132_out,
       not_133_out, not_134_out, not_135_out, not_136_out, not_137_out, not_138_out, not_139_out,
       not_140_out, not_141_out, not_142_out, not_143_out, not_144_out, not_145_out, not_146_out,
       not_147_out, not_148_out, not_149_out, not_150_out, not_151_out, not_152_out, not_153_out,
       not_154_out, not_155_out, not_156_out, not_157_out, not_158_out, not_159_out, not_160_out,
       not_161_out, not_162_out, not_163_out, not_164_out, not_165_out, not_166_out, not_167_out,
       not_168_out, not_169_out, not_170_out, not_171_out, not_172_out, not_173_out, not_174_out,
       not_175_out, not_176_out, not_177_out, not_178_out, not_179_out, not_180_out, not_181_out,
       not_182_out, not_183_out, not_184_out, not_185_out, not_186_out, not_187_out, not_188_out,
       not_189_out, not_190_out, not_191_out, not_192_out, not_193_out, not_194_out, not_195_out,
       not_196_out, not_197_out, not_198_out, not_199_out, not_200_out, not_201_out, not_202_out,
       not_203_out, not_204_out, not_205_out, not_206_out, not_207_out, not_208_out, not_209_out,
       not_210_out, not_211_out, not_212_out, not_213_out, not_214_out, not_215_out, not_216_out,
       not_217_out, not_218_out, not_219_out, not_220_out, not_221_out, not_222_out, not_223_out,
       not_224_out, not_225_out, not_226_out, not_227_out, not_228_out, not_229_out, not_230_out,
       not_231_out, not_232_out, not_233_out, not_234_out, not_235_out, not_236_out;

  not not_1 (not_1_out, OP_CODEq5pm);
  not not_2 (not_2_out, OP_CODEq4pm);
  not not_3 (not_3_out, OP_CODEq3pm);
  not not_4 (not_4_out, OP_CODEq2pm);
  not not_5 (not_5_out, OP_CODEq1pm);
  not not_6 (not_6_out, OP_CODEq0pm);
  not not_7 (not_7_out, FUNCq5pm);
  not not_8 (not_8_out, FUNCq4pm);
  not not_9 (not_9_out, FUNCq3pm);
  not not_10 (not_10_out, FUNCq2pm);
  not not_11 (not_11_out, OP_CODEq5pm);
  not not_12 (not_12_out, OP_CODEq4pm);
  not not_13 (not_13_out, OP_CODEq3pm);
  not not_14 (not_14_out, OP_CODEq2pm);
  not not_15 (not_15_out, OP_CODEq1pm);
  not not_16 (not_16_out, OP_CODEq0pm);
  not not_17 (not_17_out, FUNCq4pm);
  not not_18 (not_18_out, FUNCq3pm);
  not not_19 (not_19_out, FUNCq2pm);
  not not_20 (not_20_out, FUNCq1pm);
  not not_21 (not_21_out, FUNCq0pm);
  not not_22 (not_22_out, OP_CODEq5pm);
  not not_23 (not_23_out, OP_CODEq4pm);
  not not_24 (not_24_out, OP_CODEq3pm);
  not not_25 (not_25_out, OP_CODEq2pm);
  not not_26 (not_26_out, OP_CODEq1pm);
  not not_27 (not_27_out, OP_CODEq0pm);
  not not_28 (not_28_out, FUNCq4pm);
  not not_29 (not_29_out, FUNCq3pm);
  not not_30 (not_30_out, FUNCq2pm);
  not not_31 (not_31_out, FUNCq1pm);
  not not_32 (not_32_out, OP_CODEq5pm);
  not not_33 (not_33_out, OP_CODEq4pm);
  not not_34 (not_34_out, OP_CODEq3pm);
  not not_35 (not_35_out, OP_CODEq2pm);
  not not_36 (not_36_out, OP_CODEq1pm);
  not not_37 (not_37_out, OP_CODEq0pm);
  not not_38 (not_38_out, FUNCq4pm);
  not not_39 (not_39_out, FUNCq3pm);
  not not_40 (not_40_out, FUNCq1pm);
  not not_41 (not_41_out, FUNCq0pm);
  not not_42 (not_42_out, OP_CODEq5pm);
  not not_43 (not_43_out, OP_CODEq4pm);
  not not_44 (not_44_out, OP_CODEq3pm);
  not not_45 (not_45_out, OP_CODEq2pm);
  not not_46 (not_46_out, OP_CODEq1pm);
  not not_47 (not_47_out, OP_CODEq0pm);
  not not_48 (not_48_out, FUNCq4pm);
  not not_49 (not_49_out, FUNCq2pm);
  not not_50 (not_50_out, FUNCq0pm);
  not not_51 (not_51_out, OP_CODEq5pm);
  not not_52 (not_52_out, OP_CODEq4pm);
  not not_53 (not_53_out, OP_CODEq2pm);
  not not_54 (not_54_out, OP_CODEq1pm);
  not not_55 (not_55_out, OP_CODEq0pm);
  not not_56 (not_56_out, OP_CODEq5pm);
  not not_57 (not_57_out, OP_CODEq4pm);
  not not_58 (not_58_out, OP_CODEq1pm);
  not not_59 (not_59_out, OP_CODEq0pm);
  not not_60 (not_60_out, OP_CODEq5pm);
  not not_61 (not_61_out, OP_CODEq4pm);
  not not_62 (not_62_out, OP_CODEq2pm);
  not not_63 (not_63_out, OP_CODEq1pm);
  not not_64 (not_64_out, OP_CODEq5pm);
  not not_65 (not_65_out, OP_CODEq4pm);
  not not_66 (not_66_out, OP_CODEq2pm);
  not not_67 (not_67_out, OP_CODEq0pm);
  not not_68 (not_68_out, OP_CODEq4pm);
  not not_69 (not_69_out, OP_CODEq3pm);
  not not_70 (not_70_out, OP_CODEq2pm);
  not not_71 (not_71_out, OP_CODEq4pm);
  not not_72 (not_72_out, OP_CODEq2pm);
  not not_73 (not_73_out, OP_CODEq5pm);
  not not_74 (not_74_out, OP_CODEq4pm);
  not not_75 (not_75_out, OP_CODEq3pm);
  not not_76 (not_76_out, OP_CODEq2pm);
  not not_77 (not_77_out, OP_CODEq1pm);
  not not_78 (not_78_out, OP_CODEq0pm);
  not not_79 (not_79_out, FUNCq5pm);
  not not_80 (not_80_out, FUNCq4pm);
  not not_81 (not_81_out, FUNCq3pm);
  not not_82 (not_82_out, FUNCq2pm);
  not not_83 (not_83_out, FUNCq0pm);
  not not_84 (not_84_out, OP_CODEq5pm);
  not not_85 (not_85_out, OP_CODEq4pm);
  not not_86 (not_86_out, OP_CODEq3pm);
  not not_87 (not_87_out, OP_CODEq2pm);
  not not_88 (not_88_out, OP_CODEq1pm);
  not not_89 (not_89_out, OP_CODEq0pm);
  not not_90 (not_90_out, FUNCq4pm);
  not not_91 (not_91_out, FUNCq3pm);
  not not_92 (not_92_out, FUNCq2pm);
  not not_93 (not_93_out, FUNCq0pm);
  not not_94 (not_94_out, OP_CODEq5pm);
  not not_95 (not_95_out, OP_CODEq4pm);
  not not_96 (not_96_out, OP_CODEq3pm);
  not not_97 (not_97_out, OP_CODEq2pm);
  not not_98 (not_98_out, OP_CODEq1pm);
  not not_99 (not_99_out, OP_CODEq0pm);
  not not_100 (not_100_out, FUNCq4pm);
  not not_101 (not_101_out, FUNCq3pm);
  not not_102 (not_102_out, FUNCq1pm);
  not not_103 (not_103_out, FUNCq0pm);
  not not_104 (not_104_out, OP_CODEq5pm);
  not not_105 (not_105_out, OP_CODEq4pm);
  not not_106 (not_106_out, OP_CODEq3pm);
  not not_107 (not_107_out, OP_CODEq2pm);
  not not_108 (not_108_out, OP_CODEq1pm);
  not not_109 (not_109_out, OP_CODEq0pm);
  not not_110 (not_110_out, FUNCq4pm);
  not not_111 (not_111_out, FUNCq3pm);
  not not_112 (not_112_out, OP_CODEq5pm);
  not not_113 (not_113_out, OP_CODEq4pm);
  not not_114 (not_114_out, OP_CODEq3pm);
  not not_115 (not_115_out, OP_CODEq2pm);
  not not_116 (not_116_out, OP_CODEq1pm);
  not not_117 (not_117_out, OP_CODEq0pm);
  not not_118 (not_118_out, FUNCq4pm);
  not not_119 (not_119_out, FUNCq2pm);
  not not_120 (not_120_out, FUNCq0pm);
  not not_121 (not_121_out, OP_CODEq5pm);
  not not_122 (not_122_out, OP_CODEq4pm);
  not not_123 (not_123_out, OP_CODEq1pm);
  not not_124 (not_124_out, OP_CODEq0pm);
  not not_125 (not_125_out, OP_CODEq5pm);
  not not_126 (not_126_out, OP_CODEq4pm);
  not not_127 (not_127_out, OP_CODEq2pm);
  not not_128 (not_128_out, OP_CODEq0pm);
  not not_129 (not_129_out, OP_CODEq5pm);
  not not_130 (not_130_out, OP_CODEq4pm);
  not not_131 (not_131_out, OP_CODEq3pm);
  not not_132 (not_132_out, OP_CODEq2pm);
  not not_133 (not_133_out, OP_CODEq1pm);
  not not_134 (not_134_out, OP_CODEq0pm);
  not not_135 (not_135_out, FUNCq4pm);
  not not_136 (not_136_out, FUNCq3pm);
  not not_137 (not_137_out, FUNCq2pm);
  not not_138 (not_138_out, FUNCq1pm);
  not not_139 (not_139_out, FUNCq0pm);
  not not_140 (not_140_out, OP_CODEq5pm);
  not not_141 (not_141_out, OP_CODEq4pm);
  not not_142 (not_142_out, OP_CODEq3pm);
  not not_143 (not_143_out, OP_CODEq2pm);
  not not_144 (not_144_out, OP_CODEq1pm);
  not not_145 (not_145_out, OP_CODEq0pm);
  not not_146 (not_146_out, FUNCq4pm);
  not not_147 (not_147_out, FUNCq3pm);
  not not_148 (not_148_out, FUNCq2pm);
  not not_149 (not_149_out, FUNCq1pm);
  not not_150 (not_150_out, OP_CODEq5pm);
  not not_151 (not_151_out, OP_CODEq4pm);
  not not_152 (not_152_out, OP_CODEq3pm);
  not not_153 (not_153_out, OP_CODEq2pm);
  not not_154 (not_154_out, OP_CODEq1pm);
  not not_155 (not_155_out, OP_CODEq0pm);
  not not_156 (not_156_out, FUNCq4pm);
  not not_157 (not_157_out, FUNCq3pm);
  not not_158 (not_158_out, FUNCq2pm);
  not not_159 (not_159_out, FUNCq0pm);
  not not_160 (not_160_out, OP_CODEq5pm);
  not not_161 (not_161_out, OP_CODEq4pm);
  not not_162 (not_162_out, OP_CODEq3pm);
  not not_163 (not_163_out, OP_CODEq2pm);
  not not_164 (not_164_out, OP_CODEq1pm);
  not not_165 (not_165_out, OP_CODEq0pm);
  not not_166 (not_166_out, FUNCq4pm);
  not not_167 (not_167_out, FUNCq3pm);
  not not_168 (not_168_out, FUNCq1pm);
  not not_169 (not_169_out, FUNCq0pm);
  not not_170 (not_170_out, OP_CODEq5pm);
  not not_171 (not_171_out, OP_CODEq4pm);
  not not_172 (not_172_out, OP_CODEq3pm);
  not not_173 (not_173_out, OP_CODEq2pm);
  not not_174 (not_174_out, OP_CODEq1pm);
  not not_175 (not_175_out, OP_CODEq0pm);
  not not_176 (not_176_out, FUNCq4pm);
  not not_177 (not_177_out, FUNCq2pm);
  not not_178 (not_178_out, OP_CODEq5pm);
  not not_179 (not_179_out, OP_CODEq4pm);
  not not_180 (not_180_out, OP_CODEq2pm);
  not not_181 (not_181_out, OP_CODEq1pm);
  not not_182 (not_182_out, OP_CODEq0pm);
  not not_183 (not_183_out, OP_CODEq5pm);
  not not_184 (not_184_out, OP_CODEq4pm);
  not not_185 (not_185_out, OP_CODEq1pm);
  not not_186 (not_186_out, OP_CODEq0pm);
  not not_187 (not_187_out, OP_CODEq5pm);
  not not_188 (not_188_out, OP_CODEq4pm);
  not not_189 (not_189_out, OP_CODEq2pm);
  not not_190 (not_190_out, OP_CODEq1pm);
  not not_191 (not_191_out, OP_CODEq4pm);
  not not_192 (not_192_out, OP_CODEq3pm);
  not not_193 (not_193_out, OP_CODEq2pm);
  not not_194 (not_194_out, OP_CODEq4pm);
  not not_195 (not_195_out, OP_CODEq2pm);
  not not_196 (not_196_out, OP_CODEq5pm);
  not not_197 (not_197_out, OP_CODEq4pm);
  not not_198 (not_198_out, OP_CODEq3pm);
  not not_199 (not_199_out, OP_CODEq2pm);
  not not_200 (not_200_out, OP_CODEq1pm);
  not not_201 (not_201_out, OP_CODEq0pm);
  not not_202 (not_202_out, FUNCq4pm);
  not not_203 (not_203_out, FUNCq3pm);
  not not_204 (not_204_out, FUNCq1pm);
  not not_205 (not_205_out, OP_CODEq5pm);
  not not_206 (not_206_out, OP_CODEq4pm);
  not not_207 (not_207_out, OP_CODEq3pm);
  not not_208 (not_208_out, OP_CODEq2pm);
  not not_209 (not_209_out, OP_CODEq1pm);
  not not_210 (not_210_out, OP_CODEq0pm);
  not not_211 (not_211_out, FUNCq4pm);
  not not_212 (not_212_out, FUNCq3pm);
  not not_213 (not_213_out, OP_CODEq5pm);
  not not_214 (not_214_out, OP_CODEq4pm);
  not not_215 (not_215_out, OP_CODEq3pm);
  not not_216 (not_216_out, OP_CODEq2pm);
  not not_217 (not_217_out, OP_CODEq1pm);
  not not_218 (not_218_out, OP_CODEq0pm);
  not not_219 (not_219_out, FUNCq4pm);
  not not_220 (not_220_out, FUNCq2pm);
  not not_221 (not_221_out, FUNCq0pm);
  not not_222 (not_222_out, OP_CODEq5pm);
  not not_223 (not_223_out, OP_CODEq4pm);
  not not_224 (not_224_out, OP_CODEq3pm);
  not not_225 (not_225_out, OP_CODEq2pm);
  not not_226 (not_226_out, OP_CODEq1pm);
  not not_227 (not_227_out, OP_CODEq0pm);
  not not_228 (not_228_out, FUNCq4pm);
  not not_229 (not_229_out, FUNCq2pm);
  not not_230 (not_230_out, OP_CODEq5pm);
  not not_231 (not_231_out, OP_CODEq4pm);
  not not_232 (not_232_out, OP_CODEq2pm);
  not not_233 (not_233_out, OP_CODEq0pm);
  not not_234 (not_234_out, OP_CODEq5pm);
  not not_235 (not_235_out, OP_CODEq4pm);
  not not_236 (not_236_out, OP_CODEq1pm);
  and and_1 (and_1_out, not_1_out, not_2_out, not_3_out, not_4_out, not_5_out, not_6_out, not_7_out, not_8_out, not_9_out, not_10_out, FUNCq1pm, FUNCq0pm);
  and and_2 (and_2_out, not_11_out, not_12_out, not_13_out, not_14_out, not_15_out, not_16_out, FUNCq5pm, not_17_out, not_18_out, not_19_out, not_20_out, not_21_out);
  and and_3 (and_3_out, not_22_out, not_23_out, not_24_out, not_25_out, not_26_out, not_27_out, FUNCq5pm, not_28_out, not_29_out, not_30_out, not_31_out, FUNCq0pm);
  and and_4 (and_4_out, not_32_out, not_33_out, not_34_out, not_35_out, not_36_out, not_37_out, FUNCq5pm, not_38_out, not_39_out, FUNCq2pm, not_40_out, not_41_out);
  and and_5 (and_5_out, not_42_out, not_43_out, not_44_out, not_45_out, not_46_out, not_47_out, FUNCq5pm, not_48_out, FUNCq3pm, not_49_out, FUNCq1pm, not_50_out);
  and and_6 (and_6_out, not_51_out, not_52_out, OP_CODEq3pm, not_53_out, not_54_out, not_55_out);
  and and_7 (and_7_out, not_56_out, not_57_out, OP_CODEq3pm, OP_CODEq2pm, not_58_out, not_59_out);
  and and_8 (and_8_out, not_60_out, not_61_out, OP_CODEq3pm, not_62_out, not_63_out, OP_CODEq0pm);
  and and_9 (and_9_out, not_64_out, not_65_out, OP_CODEq3pm, not_66_out, OP_CODEq1pm, not_67_out);
  and and_10 (and_10_out, OP_CODEq5pm, not_68_out, not_69_out, not_70_out, OP_CODEq1pm, OP_CODEq0pm);
  and and_11 (and_11_out, OP_CODEq5pm, not_71_out, OP_CODEq3pm, not_72_out, OP_CODEq1pm, OP_CODEq0pm);
  and and_12 (and_12_out, not_73_out, not_74_out, not_75_out, not_76_out, not_77_out, not_78_out, not_79_out, not_80_out, not_81_out, not_82_out, FUNCq1pm, not_83_out);
  and and_13 (and_13_out, not_84_out, not_85_out, not_86_out, not_87_out, not_88_out, not_89_out, FUNCq5pm, not_90_out, not_91_out, not_92_out, FUNCq1pm, not_93_out);
  and and_14 (and_14_out, not_94_out, not_95_out, not_96_out, not_97_out, not_98_out, not_99_out, FUNCq5pm, not_100_out, not_101_out, FUNCq2pm, not_102_out, not_103_out);
  and and_15 (and_15_out, not_104_out, not_105_out, not_106_out, not_107_out, not_108_out, not_109_out, FUNCq5pm, not_110_out, not_111_out, FUNCq2pm, FUNCq1pm, FUNCq0pm);
  and and_16 (and_16_out, not_112_out, not_113_out, not_114_out, not_115_out, not_116_out, not_117_out, FUNCq5pm, not_118_out, FUNCq3pm, not_119_out, FUNCq1pm, not_120_out);
  and and_17 (and_17_out, not_121_out, not_122_out, OP_CODEq3pm, OP_CODEq2pm, not_123_out, not_124_out);
  and and_18 (and_18_out, not_125_out, not_126_out, OP_CODEq3pm, not_127_out, OP_CODEq1pm, not_128_out);
  and and_19 (and_19_out, not_129_out, not_130_out, not_131_out, not_132_out, not_133_out, not_134_out, FUNCq5pm, not_135_out, not_136_out, not_137_out, not_138_out, not_139_out);
  and and_20 (and_20_out, not_140_out, not_141_out, not_142_out, not_143_out, not_144_out, not_145_out, FUNCq5pm, not_146_out, not_147_out, not_148_out, not_149_out, FUNCq0pm);
  and and_21 (and_21_out, not_150_out, not_151_out, not_152_out, not_153_out, not_154_out, not_155_out, FUNCq5pm, not_156_out, not_157_out, not_158_out, FUNCq1pm, not_159_out);
  and and_22 (and_22_out, not_160_out, not_161_out, not_162_out, not_163_out, not_164_out, not_165_out, FUNCq5pm, not_166_out, not_167_out, FUNCq2pm, not_168_out, not_169_out);
  and and_23 (and_23_out, not_170_out, not_171_out, not_172_out, not_173_out, not_174_out, not_175_out, FUNCq5pm, not_176_out, FUNCq3pm, not_177_out, FUNCq1pm, FUNCq0pm);
  and and_24 (and_24_out, not_178_out, not_179_out, OP_CODEq3pm, not_180_out, not_181_out, not_182_out);
  and and_25 (and_25_out, not_183_out, not_184_out, OP_CODEq3pm, OP_CODEq2pm, not_185_out, not_186_out);
  and and_26 (and_26_out, not_187_out, not_188_out, OP_CODEq3pm, not_189_out, not_190_out, OP_CODEq0pm);
  and and_27 (and_27_out, OP_CODEq5pm, not_191_out, not_192_out, not_193_out, OP_CODEq1pm, OP_CODEq0pm);
  and and_28 (and_28_out, OP_CODEq5pm, not_194_out, OP_CODEq3pm, not_195_out, OP_CODEq1pm, OP_CODEq0pm);
  and and_29 (and_29_out, not_196_out, not_197_out, not_198_out, not_199_out, not_200_out, not_201_out, FUNCq5pm, not_202_out, not_203_out, FUNCq2pm, not_204_out, FUNCq0pm);
  and and_30 (and_30_out, not_205_out, not_206_out, not_207_out, not_208_out, not_209_out, not_210_out, FUNCq5pm, not_211_out, not_212_out, FUNCq2pm, FUNCq1pm, FUNCq0pm);
  and and_31 (and_31_out, not_213_out, not_214_out, not_215_out, not_216_out, not_217_out, not_218_out, FUNCq5pm, not_219_out, FUNCq3pm, not_220_out, FUNCq1pm, not_221_out);
  and and_32 (and_32_out, not_222_out, not_223_out, not_224_out, not_225_out, not_226_out, not_227_out, FUNCq5pm, not_228_out, FUNCq3pm, not_229_out, FUNCq1pm, FUNCq0pm);
  and and_33 (and_33_out, not_230_out, not_231_out, OP_CODEq3pm, not_232_out, OP_CODEq1pm, not_233_out);
  and and_34 (and_34_out, not_234_out, not_235_out, OP_CODEq3pm, OP_CODEq2pm, not_236_out, OP_CODEq0pm);
  or or_1 (S0, and_1_out, and_2_out, and_3_out, and_4_out, and_5_out, and_6_out, and_7_out, and_8_out, and_9_out, and_10_out, and_11_out);
  or or_2 (S1, and_12_out, and_13_out, and_14_out, and_15_out, and_16_out, and_17_out, and_18_out);
  or or_3 (S2, and_19_out, and_20_out, and_21_out, and_22_out, and_23_out, and_24_out, and_25_out, and_26_out, and_27_out, and_28_out);
  or or_4 (S3, and_29_out, and_30_out, and_31_out, and_32_out, and_33_out, and_34_out);
endmodule

// 控制信号生成
module \控制信号生成  (
  input  OP_CODEq0pm,
  input  OP_CODEq1pm,
  input  OP_CODEq2pm,
  input  OP_CODEq3pm,
  input  OP_CODEq4pm,
  input  OP_CODEq5pm,
  input  FUNCq0pm,
  input  FUNCq1pm,
  input  FUNCq2pm,
  input  FUNCq3pm,
  input  FUNCq4pm,
  input  FUNCq5pm,
  output MemToReg,
  output MemWrite,
  output ALU_SRC,
  output RegWrite,
  output SysCALL,
  output SignedExt,
  output RegDst,
  output BEQ,
  output BNE,
  output JR,
  output JMP,
  output JAL
);

  wire and_3_out, and_4_out, and_5_out, and_6_out, and_7_out, and_8_out, and_9_out, and_10_out, and_11_out,
       and_12_out, and_13_out, and_14_out, and_15_out, and_16_out, and_17_out, and_18_out, and_19_out,
       and_20_out, and_21_out, and_22_out, and_23_out, and_24_out, and_25_out, and_26_out, and_27_out,
       and_29_out, and_30_out, and_31_out, and_32_out, and_33_out, and_34_out, and_35_out, and_36_out,
       and_37_out, and_38_out, and_39_out, and_40_out, and_41_out, and_42_out, and_43_out, and_44_out,
       and_48_out, and_49_out, not_1_out, not_2_out, not_3_out, not_4_out, not_5_out, not_6_out, not_7_out,
       not_8_out, not_9_out, not_10_out, not_11_out, not_12_out, not_13_out, not_14_out, not_15_out,
       not_16_out, not_17_out, not_18_out, not_19_out, not_20_out, not_21_out, not_22_out, not_23_out,
       not_24_out, not_25_out, not_26_out, not_27_out, not_28_out, not_29_out, not_30_out, not_31_out,
       not_32_out, not_33_out, not_34_out, not_35_out, not_36_out, not_37_out, not_38_out, not_39_out,
       not_40_out, not_41_out, not_42_out, not_43_out, not_44_out, not_45_out, not_46_out, not_47_out,
       not_48_out, not_49_out, not_50_out, not_51_out, not_52_out, not_53_out, not_54_out, not_55_out,
       not_56_out, not_57_out, not_58_out, not_59_out, not_60_out, not_61_out, not_62_out, not_63_out,
       not_64_out, not_65_out, not_66_out, not_67_out, not_68_out, not_69_out, not_70_out, not_71_out,
       not_72_out, not_73_out, not_74_out, not_75_out, not_76_out, not_77_out, not_78_out, not_79_out,
       not_80_out, not_81_out, not_82_out, not_83_out, not_84_out, not_85_out, not_86_out, not_87_out,
       not_88_out, not_89_out, not_90_out, not_91_out, not_92_out, not_93_out, not_94_out, not_95_out,
       not_96_out, not_97_out, not_98_out, not_99_out, not_100_out, not_101_out, not_102_out, not_103_out,
       not_104_out, not_105_out, not_106_out, not_107_out, not_108_out, not_109_out, not_110_out,
       not_111_out, not_112_out, not_113_out, not_114_out, not_115_out, not_116_out, not_117_out,
       not_118_out, not_119_out, not_120_out, not_121_out, not_122_out, not_123_out, not_124_out,
       not_125_out, not_126_out, not_127_out, not_128_out, not_129_out, not_130_out, not_131_out,
       not_132_out, not_133_out, not_134_out, not_135_out, not_136_out, not_137_out, not_138_out,
       not_139_out, not_140_out, not_141_out, not_142_out, not_143_out, not_144_out, not_145_out,
       not_146_out, not_147_out, not_148_out, not_149_out, not_150_out, not_151_out, not_152_out,
       not_153_out, not_154_out, not_155_out, not_156_out, not_157_out, not_158_out, not_159_out,
       not_160_out, not_161_out, not_162_out, not_163_out, not_164_out, not_165_out, not_166_out,
       not_167_out, not_168_out, not_169_out, not_170_out, not_171_out, not_172_out, not_173_out,
       not_174_out, not_175_out, not_176_out, not_177_out, not_178_out, not_179_out, not_180_out,
       not_181_out, not_182_out, not_183_out, not_184_out, not_185_out, not_186_out, not_187_out,
       not_188_out, not_189_out, not_190_out, not_191_out, not_192_out, not_193_out, not_194_out,
       not_195_out, not_196_out, not_197_out, not_198_out, not_199_out, not_200_out, not_201_out,
       not_202_out, not_203_out, not_204_out, not_205_out, not_206_out, not_207_out, not_208_out,
       not_209_out, not_210_out, not_211_out, not_212_out, not_213_out, not_214_out, not_215_out,
       not_216_out, not_217_out, not_218_out, not_219_out, not_220_out, not_221_out, not_222_out,
       not_223_out, not_224_out, not_225_out, not_226_out, not_227_out, not_228_out, not_229_out,
       not_230_out, not_231_out, not_232_out, not_233_out, not_234_out, not_235_out, not_236_out,
       not_237_out, not_238_out, not_239_out, not_240_out, not_241_out, not_242_out, not_243_out,
       not_244_out, not_245_out, not_246_out, not_247_out, not_248_out, not_249_out, not_250_out,
       not_251_out, not_252_out, not_253_out, not_254_out, not_255_out, not_256_out, not_257_out,
       not_258_out, not_259_out, not_260_out, not_261_out, not_262_out, not_263_out, not_264_out,
       not_265_out, not_266_out, not_267_out, not_268_out, not_269_out, not_270_out, not_271_out,
       not_272_out, not_273_out, not_274_out, not_275_out, not_276_out, not_277_out, not_278_out,
       not_279_out, not_280_out, not_281_out, not_282_out, not_283_out, not_284_out, not_285_out,
       not_286_out, not_287_out, not_288_out, not_289_out, not_290_out, not_291_out, not_292_out,
       not_293_out, not_294_out, not_295_out, not_296_out, not_297_out, not_298_out, not_299_out,
       not_300_out, not_301_out, not_302_out, not_303_out, not_304_out, not_305_out, not_306_out,
       not_307_out, not_308_out, not_309_out, not_310_out, not_311_out, not_312_out, not_313_out,
       not_314_out, not_315_out, not_316_out, not_317_out, not_318_out, not_319_out, not_320_out,
       not_321_out, not_322_out, not_323_out, not_324_out, not_325_out, not_326_out, not_327_out,
       not_328_out, not_329_out, not_330_out, not_331_out, not_332_out, not_333_out, not_334_out;

  not not_1 (not_1_out, OP_CODEq4pm);
  not not_2 (not_2_out, OP_CODEq3pm);
  not not_3 (not_3_out, OP_CODEq2pm);
  not not_4 (not_4_out, OP_CODEq4pm);
  not not_5 (not_5_out, OP_CODEq2pm);
  not not_6 (not_6_out, OP_CODEq5pm);
  not not_7 (not_7_out, OP_CODEq4pm);
  not not_8 (not_8_out, OP_CODEq2pm);
  not not_9 (not_9_out, OP_CODEq1pm);
  not not_10 (not_10_out, OP_CODEq0pm);
  not not_11 (not_11_out, OP_CODEq5pm);
  not not_12 (not_12_out, OP_CODEq4pm);
  not not_13 (not_13_out, OP_CODEq1pm);
  not not_14 (not_14_out, OP_CODEq0pm);
  not not_15 (not_15_out, OP_CODEq5pm);
  not not_16 (not_16_out, OP_CODEq4pm);
  not not_17 (not_17_out, OP_CODEq2pm);
  not not_18 (not_18_out, OP_CODEq1pm);
  not not_19 (not_19_out, OP_CODEq5pm);
  not not_20 (not_20_out, OP_CODEq4pm);
  not not_21 (not_21_out, OP_CODEq2pm);
  not not_22 (not_22_out, OP_CODEq0pm);
  not not_23 (not_23_out, OP_CODEq5pm);
  not not_24 (not_24_out, OP_CODEq4pm);
  not not_25 (not_25_out, OP_CODEq1pm);
  not not_26 (not_26_out, OP_CODEq4pm);
  not not_27 (not_27_out, OP_CODEq3pm);
  not not_28 (not_28_out, OP_CODEq2pm);
  not not_29 (not_29_out, OP_CODEq4pm);
  not not_30 (not_30_out, OP_CODEq2pm);
  not not_31 (not_31_out, OP_CODEq5pm);
  not not_32 (not_32_out, OP_CODEq4pm);
  not not_33 (not_33_out, OP_CODEq3pm);
  not not_34 (not_34_out, OP_CODEq2pm);
  not not_35 (not_35_out, OP_CODEq1pm);
  not not_36 (not_36_out, OP_CODEq0pm);
  not not_37 (not_37_out, FUNCq5pm);
  not not_38 (not_38_out, FUNCq4pm);
  not not_39 (not_39_out, FUNCq3pm);
  not not_40 (not_40_out, FUNCq2pm);
  not not_41 (not_41_out, FUNCq1pm);
  not not_42 (not_42_out, FUNCq0pm);
  not not_43 (not_43_out, OP_CODEq5pm);
  not not_44 (not_44_out, OP_CODEq4pm);
  not not_45 (not_45_out, OP_CODEq3pm);
  not not_46 (not_46_out, OP_CODEq2pm);
  not not_47 (not_47_out, OP_CODEq1pm);
  not not_48 (not_48_out, OP_CODEq0pm);
  not not_49 (not_49_out, FUNCq5pm);
  not not_50 (not_50_out, FUNCq4pm);
  not not_51 (not_51_out, FUNCq3pm);
  not not_52 (not_52_out, FUNCq2pm);
  not not_53 (not_53_out, OP_CODEq5pm);
  not not_54 (not_54_out, OP_CODEq4pm);
  not not_55 (not_55_out, OP_CODEq3pm);
  not not_56 (not_56_out, OP_CODEq2pm);
  not not_57 (not_57_out, OP_CODEq1pm);
  not not_58 (not_58_out, OP_CODEq0pm);
  not not_59 (not_59_out, FUNCq5pm);
  not not_60 (not_60_out, FUNCq4pm);
  not not_61 (not_61_out, FUNCq3pm);
  not not_62 (not_62_out, FUNCq2pm);
  not not_63 (not_63_out, FUNCq0pm);
  not not_64 (not_64_out, OP_CODEq5pm);
  not not_65 (not_65_out, OP_CODEq4pm);
  not not_66 (not_66_out, OP_CODEq3pm);
  not not_67 (not_67_out, OP_CODEq2pm);
  not not_68 (not_68_out, OP_CODEq1pm);
  not not_69 (not_69_out, OP_CODEq0pm);
  not not_70 (not_70_out, FUNCq4pm);
  not not_71 (not_71_out, FUNCq3pm);
  not not_72 (not_72_out, FUNCq2pm);
  not not_73 (not_73_out, FUNCq1pm);
  not not_74 (not_74_out, FUNCq0pm);
  not not_75 (not_75_out, OP_CODEq5pm);
  not not_76 (not_76_out, OP_CODEq4pm);
  not not_77 (not_77_out, OP_CODEq3pm);
  not not_78 (not_78_out, OP_CODEq2pm);
  not not_79 (not_79_out, OP_CODEq1pm);
  not not_80 (not_80_out, OP_CODEq0pm);
  not not_81 (not_81_out, FUNCq4pm);
  not not_82 (not_82_out, FUNCq3pm);
  not not_83 (not_83_out, FUNCq2pm);
  not not_84 (not_84_out, FUNCq1pm);
  not not_85 (not_85_out, OP_CODEq5pm);
  not not_86 (not_86_out, OP_CODEq4pm);
  not not_87 (not_87_out, OP_CODEq3pm);
  not not_88 (not_88_out, OP_CODEq2pm);
  not not_89 (not_89_out, OP_CODEq1pm);
  not not_90 (not_90_out, OP_CODEq0pm);
  not not_91 (not_91_out, FUNCq4pm);
  not not_92 (not_92_out, FUNCq3pm);
  not not_93 (not_93_out, FUNCq2pm);
  not not_94 (not_94_out, FUNCq0pm);
  not not_95 (not_95_out, OP_CODEq5pm);
  not not_96 (not_96_out, OP_CODEq4pm);
  not not_97 (not_97_out, OP_CODEq3pm);
  not not_98 (not_98_out, OP_CODEq2pm);
  not not_99 (not_99_out, OP_CODEq1pm);
  not not_100 (not_100_out, OP_CODEq0pm);
  not not_101 (not_101_out, FUNCq4pm);
  not not_102 (not_102_out, FUNCq3pm);
  not not_103 (not_103_out, FUNCq1pm);
  not not_104 (not_104_out, FUNCq0pm);
  not not_105 (not_105_out, OP_CODEq5pm);
  not not_106 (not_106_out, OP_CODEq4pm);
  not not_107 (not_107_out, OP_CODEq3pm);
  not not_108 (not_108_out, OP_CODEq2pm);
  not not_109 (not_109_out, OP_CODEq1pm);
  not not_110 (not_110_out, OP_CODEq0pm);
  not not_111 (not_111_out, FUNCq4pm);
  not not_112 (not_112_out, FUNCq3pm);
  not not_113 (not_113_out, FUNCq1pm);
  not not_114 (not_114_out, OP_CODEq5pm);
  not not_115 (not_115_out, OP_CODEq4pm);
  not not_116 (not_116_out, OP_CODEq3pm);
  not not_117 (not_117_out, OP_CODEq2pm);
  not not_118 (not_118_out, OP_CODEq1pm);
  not not_119 (not_119_out, OP_CODEq0pm);
  not not_120 (not_120_out, FUNCq4pm);
  not not_121 (not_121_out, FUNCq3pm);
  not not_122 (not_122_out, OP_CODEq5pm);
  not not_123 (not_123_out, OP_CODEq4pm);
  not not_124 (not_124_out, OP_CODEq3pm);
  not not_125 (not_125_out, OP_CODEq2pm);
  not not_126 (not_126_out, OP_CODEq1pm);
  not not_127 (not_127_out, OP_CODEq0pm);
  not not_128 (not_128_out, FUNCq4pm);
  not not_129 (not_129_out, FUNCq2pm);
  not not_130 (not_130_out, FUNCq0pm);
  not not_131 (not_131_out, OP_CODEq5pm);
  not not_132 (not_132_out, OP_CODEq4pm);
  not not_133 (not_133_out, OP_CODEq3pm);
  not not_134 (not_134_out, OP_CODEq2pm);
  not not_135 (not_135_out, OP_CODEq1pm);
  not not_136 (not_136_out, OP_CODEq0pm);
  not not_137 (not_137_out, FUNCq4pm);
  not not_138 (not_138_out, FUNCq2pm);
  not not_139 (not_139_out, OP_CODEq5pm);
  not not_140 (not_140_out, OP_CODEq4pm);
  not not_141 (not_141_out, OP_CODEq3pm);
  not not_142 (not_142_out, OP_CODEq2pm);
  not not_143 (not_143_out, OP_CODEq5pm);
  not not_144 (not_144_out, OP_CODEq4pm);
  not not_145 (not_145_out, OP_CODEq2pm);
  not not_146 (not_146_out, OP_CODEq1pm);
  not not_147 (not_147_out, OP_CODEq0pm);
  not not_148 (not_148_out, OP_CODEq5pm);
  not not_149 (not_149_out, OP_CODEq4pm);
  not not_150 (not_150_out, OP_CODEq1pm);
  not not_151 (not_151_out, OP_CODEq0pm);
  not not_152 (not_152_out, OP_CODEq5pm);
  not not_153 (not_153_out, OP_CODEq4pm);
  not not_154 (not_154_out, OP_CODEq2pm);
  not not_155 (not_155_out, OP_CODEq1pm);
  not not_156 (not_156_out, OP_CODEq5pm);
  not not_157 (not_157_out, OP_CODEq4pm);
  not not_158 (not_158_out, OP_CODEq2pm);
  not not_159 (not_159_out, OP_CODEq0pm);
  not not_160 (not_160_out, OP_CODEq5pm);
  not not_161 (not_161_out, OP_CODEq4pm);
  not not_162 (not_162_out, OP_CODEq1pm);
  not not_163 (not_163_out, OP_CODEq4pm);
  not not_164 (not_164_out, OP_CODEq3pm);
  not not_165 (not_165_out, OP_CODEq2pm);
  not not_166 (not_166_out, OP_CODEq5pm);
  not not_167 (not_167_out, OP_CODEq4pm);
  not not_168 (not_168_out, OP_CODEq3pm);
  not not_169 (not_169_out, OP_CODEq2pm);
  not not_170 (not_170_out, OP_CODEq1pm);
  not not_171 (not_171_out, OP_CODEq0pm);
  not not_172 (not_172_out, FUNCq5pm);
  not not_173 (not_173_out, FUNCq4pm);
  not not_174 (not_174_out, FUNCq1pm);
  not not_175 (not_175_out, FUNCq0pm);
  not not_176 (not_176_out, OP_CODEq5pm);
  not not_177 (not_177_out, OP_CODEq4pm);
  not not_178 (not_178_out, OP_CODEq2pm);
  not not_179 (not_179_out, OP_CODEq1pm);
  not not_180 (not_180_out, OP_CODEq0pm);
  not not_181 (not_181_out, OP_CODEq5pm);
  not not_182 (not_182_out, OP_CODEq4pm);
  not not_183 (not_183_out, OP_CODEq2pm);
  not not_184 (not_184_out, OP_CODEq1pm);
  not not_185 (not_185_out, OP_CODEq5pm);
  not not_186 (not_186_out, OP_CODEq4pm);
  not not_187 (not_187_out, OP_CODEq2pm);
  not not_188 (not_188_out, OP_CODEq0pm);
  not not_189 (not_189_out, OP_CODEq4pm);
  not not_190 (not_190_out, OP_CODEq3pm);
  not not_191 (not_191_out, OP_CODEq2pm);
  not not_192 (not_192_out, OP_CODEq4pm);
  not not_193 (not_193_out, OP_CODEq2pm);
  not not_194 (not_194_out, OP_CODEq5pm);
  not not_195 (not_195_out, OP_CODEq4pm);
  not not_196 (not_196_out, OP_CODEq3pm);
  not not_197 (not_197_out, OP_CODEq2pm);
  not not_198 (not_198_out, OP_CODEq1pm);
  not not_199 (not_199_out, OP_CODEq0pm);
  not not_200 (not_200_out, FUNCq5pm);
  not not_201 (not_201_out, FUNCq4pm);
  not not_202 (not_202_out, FUNCq3pm);
  not not_203 (not_203_out, FUNCq2pm);
  not not_204 (not_204_out, FUNCq1pm);
  not not_205 (not_205_out, FUNCq0pm);
  not not_206 (not_206_out, OP_CODEq5pm);
  not not_207 (not_207_out, OP_CODEq4pm);
  not not_208 (not_208_out, OP_CODEq3pm);
  not not_209 (not_209_out, OP_CODEq2pm);
  not not_210 (not_210_out, OP_CODEq1pm);
  not not_211 (not_211_out, OP_CODEq0pm);
  not not_212 (not_212_out, FUNCq5pm);
  not not_213 (not_213_out, FUNCq4pm);
  not not_214 (not_214_out, FUNCq3pm);
  not not_215 (not_215_out, FUNCq2pm);
  not not_216 (not_216_out, OP_CODEq5pm);
  not not_217 (not_217_out, OP_CODEq4pm);
  not not_218 (not_218_out, OP_CODEq3pm);
  not not_219 (not_219_out, OP_CODEq2pm);
  not not_220 (not_220_out, OP_CODEq1pm);
  not not_221 (not_221_out, OP_CODEq0pm);
  not not_222 (not_222_out, FUNCq5pm);
  not not_223 (not_223_out, FUNCq4pm);
  not not_224 (not_224_out, FUNCq3pm);
  not not_225 (not_225_out, FUNCq2pm);
  not not_226 (not_226_out, FUNCq0pm);
  not not_227 (not_227_out, OP_CODEq5pm);
  not not_228 (not_228_out, OP_CODEq4pm);
  not not_229 (not_229_out, OP_CODEq3pm);
  not not_230 (not_230_out, OP_CODEq2pm);
  not not_231 (not_231_out, OP_CODEq1pm);
  not not_232 (not_232_out, OP_CODEq0pm);
  not not_233 (not_233_out, FUNCq4pm);
  not not_234 (not_234_out, FUNCq3pm);
  not not_235 (not_235_out, FUNCq2pm);
  not not_236 (not_236_out, FUNCq1pm);
  not not_237 (not_237_out, FUNCq0pm);
  not not_238 (not_238_out, OP_CODEq5pm);
  not not_239 (not_239_out, OP_CODEq4pm);
  not not_240 (not_240_out, OP_CODEq3pm);
  not not_241 (not_241_out, OP_CODEq2pm);
  not not_242 (not_242_out, OP_CODEq1pm);
  not not_243 (not_243_out, OP_CODEq0pm);
  not not_244 (not_244_out, FUNCq4pm);
  not not_245 (not_245_out, FUNCq3pm);
  not not_246 (not_246_out, FUNCq2pm);
  not not_247 (not_247_out, FUNCq1pm);
  not not_248 (not_248_out, OP_CODEq5pm);
  not not_249 (not_249_out, OP_CODEq4pm);
  not not_250 (not_250_out, OP_CODEq3pm);
  not not_251 (not_251_out, OP_CODEq2pm);
  not not_252 (not_252_out, OP_CODEq1pm);
  not not_253 (not_253_out, OP_CODEq0pm);
  not not_254 (not_254_out, FUNCq4pm);
  not not_255 (not_255_out, FUNCq3pm);
  not not_256 (not_256_out, FUNCq2pm);
  not not_257 (not_257_out, FUNCq0pm);
  not not_258 (not_258_out, OP_CODEq5pm);
  not not_259 (not_259_out, OP_CODEq4pm);
  not not_260 (not_260_out, OP_CODEq3pm);
  not not_261 (not_261_out, OP_CODEq2pm);
  not not_262 (not_262_out, OP_CODEq1pm);
  not not_263 (not_263_out, OP_CODEq0pm);
  not not_264 (not_264_out, FUNCq4pm);
  not not_265 (not_265_out, FUNCq3pm);
  not not_266 (not_266_out, FUNCq1pm);
  not not_267 (not_267_out, FUNCq0pm);
  not not_268 (not_268_out, OP_CODEq5pm);
  not not_269 (not_269_out, OP_CODEq4pm);
  not not_270 (not_270_out, OP_CODEq3pm);
  not not_271 (not_271_out, OP_CODEq2pm);
  not not_272 (not_272_out, OP_CODEq1pm);
  not not_273 (not_273_out, OP_CODEq0pm);
  not not_274 (not_274_out, FUNCq4pm);
  not not_275 (not_275_out, FUNCq3pm);
  not not_276 (not_276_out, FUNCq1pm);
  not not_277 (not_277_out, OP_CODEq5pm);
  not not_278 (not_278_out, OP_CODEq4pm);
  not not_279 (not_279_out, OP_CODEq3pm);
  not not_280 (not_280_out, OP_CODEq2pm);
  not not_281 (not_281_out, OP_CODEq1pm);
  not not_282 (not_282_out, OP_CODEq0pm);
  not not_283 (not_283_out, FUNCq4pm);
  not not_284 (not_284_out, FUNCq3pm);
  not not_285 (not_285_out, OP_CODEq5pm);
  not not_286 (not_286_out, OP_CODEq4pm);
  not not_287 (not_287_out, OP_CODEq3pm);
  not not_288 (not_288_out, OP_CODEq2pm);
  not not_289 (not_289_out, OP_CODEq1pm);
  not not_290 (not_290_out, OP_CODEq0pm);
  not not_291 (not_291_out, FUNCq4pm);
  not not_292 (not_292_out, FUNCq2pm);
  not not_293 (not_293_out, FUNCq0pm);
  not not_294 (not_294_out, OP_CODEq5pm);
  not not_295 (not_295_out, OP_CODEq4pm);
  not not_296 (not_296_out, OP_CODEq3pm);
  not not_297 (not_297_out, OP_CODEq2pm);
  not not_298 (not_298_out, OP_CODEq1pm);
  not not_299 (not_299_out, OP_CODEq0pm);
  not not_300 (not_300_out, FUNCq4pm);
  not not_301 (not_301_out, FUNCq2pm);
  not not_302 (not_302_out, OP_CODEq5pm);
  not not_303 (not_303_out, OP_CODEq4pm);
  not not_304 (not_304_out, OP_CODEq3pm);
  not not_305 (not_305_out, OP_CODEq1pm);
  not not_306 (not_306_out, OP_CODEq0pm);
  not not_307 (not_307_out, OP_CODEq5pm);
  not not_308 (not_308_out, OP_CODEq4pm);
  not not_309 (not_309_out, OP_CODEq3pm);
  not not_310 (not_310_out, OP_CODEq1pm);
  not not_311 (not_311_out, OP_CODEq5pm);
  not not_312 (not_312_out, OP_CODEq4pm);
  not not_313 (not_313_out, OP_CODEq3pm);
  not not_314 (not_314_out, OP_CODEq2pm);
  not not_315 (not_315_out, OP_CODEq1pm);
  not not_316 (not_316_out, OP_CODEq0pm);
  not not_317 (not_317_out, FUNCq5pm);
  not not_318 (not_318_out, FUNCq4pm);
  not not_319 (not_319_out, FUNCq2pm);
  not not_320 (not_320_out, FUNCq1pm);
  not not_321 (not_321_out, FUNCq0pm);
  not not_322 (not_322_out, OP_CODEq5pm);
  not not_323 (not_323_out, OP_CODEq4pm);
  not not_324 (not_324_out, OP_CODEq3pm);
  not not_325 (not_325_out, OP_CODEq2pm);
  not not_326 (not_326_out, OP_CODEq0pm);
  not not_327 (not_327_out, OP_CODEq5pm);
  not not_328 (not_328_out, OP_CODEq4pm);
  not not_329 (not_329_out, OP_CODEq3pm);
  not not_330 (not_330_out, OP_CODEq2pm);
  not not_331 (not_331_out, OP_CODEq5pm);
  not not_332 (not_332_out, OP_CODEq4pm);
  not not_333 (not_333_out, OP_CODEq3pm);
  not not_334 (not_334_out, OP_CODEq2pm);
  and and_1 (MemToReg, OP_CODEq5pm, not_1_out, not_2_out, not_3_out, OP_CODEq1pm, OP_CODEq0pm);
  and and_2 (MemWrite, OP_CODEq5pm, not_4_out, OP_CODEq3pm, not_5_out, OP_CODEq1pm, OP_CODEq0pm);
  and and_3 (and_3_out, not_6_out, not_7_out, OP_CODEq3pm, not_8_out, not_9_out, not_10_out);
  and and_4 (and_4_out, not_11_out, not_12_out, OP_CODEq3pm, OP_CODEq2pm, not_13_out, not_14_out);
  and and_5 (and_5_out, not_15_out, not_16_out, OP_CODEq3pm, not_17_out, not_18_out, OP_CODEq0pm);
  and and_6 (and_6_out, not_19_out, not_20_out, OP_CODEq3pm, not_21_out, OP_CODEq1pm, not_22_out);
  and and_7 (and_7_out, not_23_out, not_24_out, OP_CODEq3pm, OP_CODEq2pm, not_25_out, OP_CODEq0pm);
  and and_8 (and_8_out, OP_CODEq5pm, not_26_out, not_27_out, not_28_out, OP_CODEq1pm, OP_CODEq0pm);
  and and_9 (and_9_out, OP_CODEq5pm, not_29_out, OP_CODEq3pm, not_30_out, OP_CODEq1pm, OP_CODEq0pm);
  and and_10 (and_10_out, not_31_out, not_32_out, not_33_out, not_34_out, not_35_out, not_36_out, not_37_out, not_38_out, not_39_out, not_40_out, not_41_out, not_42_out);
  and and_11 (and_11_out, not_43_out, not_44_out, not_45_out, not_46_out, not_47_out, not_48_out, not_49_out, not_50_out, not_51_out, not_52_out, FUNCq1pm, FUNCq0pm);
  and and_12 (and_12_out, not_53_out, not_54_out, not_55_out, not_56_out, not_57_out, not_58_out, not_59_out, not_60_out, not_61_out, not_62_out, FUNCq1pm, not_63_out);
  and and_13 (and_13_out, not_64_out, not_65_out, not_66_out, not_67_out, not_68_out, not_69_out, FUNCq5pm, not_70_out, not_71_out, not_72_out, not_73_out, not_74_out);
  and and_14 (and_14_out, not_75_out, not_76_out, not_77_out, not_78_out, not_79_out, not_80_out, FUNCq5pm, not_81_out, not_82_out, not_83_out, not_84_out, FUNCq0pm);
  and and_15 (and_15_out, not_85_out, not_86_out, not_87_out, not_88_out, not_89_out, not_90_out, FUNCq5pm, not_91_out, not_92_out, not_93_out, FUNCq1pm, not_94_out);
  and and_16 (and_16_out, not_95_out, not_96_out, not_97_out, not_98_out, not_99_out, not_100_out, FUNCq5pm, not_101_out, not_102_out, FUNCq2pm, not_103_out, not_104_out);
  and and_17 (and_17_out, not_105_out, not_106_out, not_107_out, not_108_out, not_109_out, not_110_out, FUNCq5pm, not_111_out, not_112_out, FUNCq2pm, not_113_out, FUNCq0pm);
  and and_18 (and_18_out, not_114_out, not_115_out, not_116_out, not_117_out, not_118_out, not_119_out, FUNCq5pm, not_120_out, not_121_out, FUNCq2pm, FUNCq1pm, FUNCq0pm);
  and and_19 (and_19_out, not_122_out, not_123_out, not_124_out, not_125_out, not_126_out, not_127_out, FUNCq5pm, not_128_out, FUNCq3pm, not_129_out, FUNCq1pm, not_130_out);
  and and_20 (and_20_out, not_131_out, not_132_out, not_133_out, not_134_out, not_135_out, not_136_out, FUNCq5pm, not_137_out, FUNCq3pm, not_138_out, FUNCq1pm, FUNCq0pm);
  and and_21 (and_21_out, not_139_out, not_140_out, not_141_out, not_142_out, OP_CODEq1pm, OP_CODEq0pm);
  and and_22 (and_22_out, not_143_out, not_144_out, OP_CODEq3pm, not_145_out, not_146_out, not_147_out);
  and and_23 (and_23_out, not_148_out, not_149_out, OP_CODEq3pm, OP_CODEq2pm, not_150_out, not_151_out);
  and and_24 (and_24_out, not_152_out, not_153_out, OP_CODEq3pm, not_154_out, not_155_out, OP_CODEq0pm);
  and and_25 (and_25_out, not_156_out, not_157_out, OP_CODEq3pm, not_158_out, OP_CODEq1pm, not_159_out);
  and and_26 (and_26_out, not_160_out, not_161_out, OP_CODEq3pm, OP_CODEq2pm, not_162_out, OP_CODEq0pm);
  and and_27 (and_27_out, OP_CODEq5pm, not_163_out, not_164_out, not_165_out, OP_CODEq1pm, OP_CODEq0pm);
  and and_28 (SysCALL, not_166_out, not_167_out, not_168_out, not_169_out, not_170_out, not_171_out, not_172_out, not_173_out, FUNCq3pm, FUNCq2pm, not_174_out, not_175_out);
  and and_29 (and_29_out, not_176_out, not_177_out, OP_CODEq3pm, not_178_out, not_179_out, not_180_out);
  and and_30 (and_30_out, not_181_out, not_182_out, OP_CODEq3pm, not_183_out, not_184_out, OP_CODEq0pm);
  and and_31 (and_31_out, not_185_out, not_186_out, OP_CODEq3pm, not_187_out, OP_CODEq1pm, not_188_out);
  and and_32 (and_32_out, OP_CODEq5pm, not_189_out, not_190_out, not_191_out, OP_CODEq1pm, OP_CODEq0pm);
  and and_33 (and_33_out, OP_CODEq5pm, not_192_out, OP_CODEq3pm, not_193_out, OP_CODEq1pm, OP_CODEq0pm);
  and and_34 (and_34_out, not_194_out, not_195_out, not_196_out, not_197_out, not_198_out, not_199_out, not_200_out, not_201_out, not_202_out, not_203_out, not_204_out, not_205_out);
  and and_35 (and_35_out, not_206_out, not_207_out, not_208_out, not_209_out, not_210_out, not_211_out, not_212_out, not_213_out, not_214_out, not_215_out, FUNCq1pm, FUNCq0pm);
  and and_36 (and_36_out, not_216_out, not_217_out, not_218_out, not_219_out, not_220_out, not_221_out, not_222_out, not_223_out, not_224_out, not_225_out, FUNCq1pm, not_226_out);
  and and_37 (and_37_out, not_227_out, not_228_out, not_229_out, not_230_out, not_231_out, not_232_out, FUNCq5pm, not_233_out, not_234_out, not_235_out, not_236_out, not_237_out);
  and and_38 (and_38_out, not_238_out, not_239_out, not_240_out, not_241_out, not_242_out, not_243_out, FUNCq5pm, not_244_out, not_245_out, not_246_out, not_247_out, FUNCq0pm);
  and and_39 (and_39_out, not_248_out, not_249_out, not_250_out, not_251_out, not_252_out, not_253_out, FUNCq5pm, not_254_out, not_255_out, not_256_out, FUNCq1pm, not_257_out);
  and and_40 (and_40_out, not_258_out, not_259_out, not_260_out, not_261_out, not_262_out, not_263_out, FUNCq5pm, not_264_out, not_265_out, FUNCq2pm, not_266_out, not_267_out);
  and and_41 (and_41_out, not_268_out, not_269_out, not_270_out, not_271_out, not_272_out, not_273_out, FUNCq5pm, not_274_out, not_275_out, FUNCq2pm, not_276_out, FUNCq0pm);
  and and_42 (and_42_out, not_277_out, not_278_out, not_279_out, not_280_out, not_281_out, not_282_out, FUNCq5pm, not_283_out, not_284_out, FUNCq2pm, FUNCq1pm, FUNCq0pm);
  and and_43 (and_43_out, not_285_out, not_286_out, not_287_out, not_288_out, not_289_out, not_290_out, FUNCq5pm, not_291_out, FUNCq3pm, not_292_out, FUNCq1pm, not_293_out);
  and and_44 (and_44_out, not_294_out, not_295_out, not_296_out, not_297_out, not_298_out, not_299_out, FUNCq5pm, not_300_out, FUNCq3pm, not_301_out, FUNCq1pm, FUNCq0pm);
  and and_45 (BEQ, not_302_out, not_303_out, not_304_out, OP_CODEq2pm, not_305_out, not_306_out);
  and and_46 (BNE, not_307_out, not_308_out, not_309_out, OP_CODEq2pm, not_310_out, OP_CODEq0pm);
  and and_47 (JR, not_311_out, not_312_out, not_313_out, not_314_out, not_315_out, not_316_out, not_317_out, not_318_out, FUNCq3pm, not_319_out, not_320_out, not_321_out);
  and and_48 (and_48_out, not_322_out, not_323_out, not_324_out, not_325_out, OP_CODEq1pm, not_326_out);
  and and_49 (and_49_out, not_327_out, not_328_out, not_329_out, not_330_out, OP_CODEq1pm, OP_CODEq0pm);
  and and_50 (JAL, not_331_out, not_332_out, not_333_out, not_334_out, OP_CODEq1pm, OP_CODEq0pm);
  or or_1 (ALU_SRC, and_3_out, and_4_out, and_5_out, and_6_out, and_7_out, and_8_out, and_9_out);
  or or_2 (SignedExt, and_29_out, and_30_out, and_31_out, and_32_out, and_33_out);
  or or_3 (RegDst, and_34_out, and_35_out, and_36_out, and_37_out, and_38_out, and_39_out, and_40_out, and_41_out, and_42_out, and_43_out, and_44_out);
  or or_4 (JMP, and_48_out, and_49_out);
  or or_5 (RegWrite, and_10_out, and_11_out, and_12_out, and_13_out, and_14_out, and_15_out, and_16_out, and_17_out, and_18_out, and_19_out, and_20_out, and_21_out, and_22_out, and_23_out, and_24_out, and_25_out, and_26_out, and_27_out);
endmodule

// ALU
module MIPS_ALU (
  input  [4:0] shamt,
  input  [31:0] X,
  input  [31:0] Y,
  input  [3:0] AluOP,
  output Equal,
  output [31:0] Result,
  output [31:0] Result_2
);

  wire [0:0] comparator_1_lt, comparator_2_lt;
  wire [31:0] adder_1_out, AND_out, divider_1_out, divider_1_rem, multiplier_1_cout, multiplier_1_out,
       NOR_out, OR_out, shifter_1_out, shifter_2_out, shifter_3_out, subtractor_1_out, XOR_out;

  assign AND_out = X & Y;  // AND_Gate AND, 32 bits wide
  assign OR_out = X | Y;  // OR_Gate OR, 32 bits wide
  Shifter #(.width(32)) shifter_1 (.in(Y), .\dist (shamt), .out(shifter_1_out));
  Shifter #(.width(32), .shift("ar")) shifter_2 (.in(Y), .\dist (shamt), .out(shifter_2_out));
  Shifter #(.width(32), .shift("lr")) shifter_3 (.in(Y), .\dist (shamt), .out(shifter_3_out));
  Multiplier #(.width(32)) multiplier_1 (.a(X), .b(Y), .out(multiplier_1_out), .cout(multiplier_1_cout));  // open: cin
  Divider #(.width(32)) divider_1 (.a(X), .b(Y), .out(divider_1_out), .rem(divider_1_rem));  // open: upper
  Adder #(.width(32)) adder_1 (.a(X), .b(Y), .out(adder_1_out));  // open: cin, cout
  Subtractor #(.width(32)) subtractor_1 (.a(X), .b(Y), .out(subtractor_1_out));  // open: bin, bout
  assign XOR_out = X ^ Y;  // XOR_Gate XOR, 32 bits wide
  assign NOR_out = ~(X | Y);  // NOR_Gate NOR, 32 bits wide
  Comparator #(.width(32)) comparator_1 (.a(X), .b(Y), .eq(Equal), .lt(comparator_1_lt[0]));  // open: gt
  Comparator #(.width(32), .mode("unsigned")) comparator_2 (.a(X), .b(Y), .lt(comparator_2_lt[0]));  // open: gt, eq
  Multiplexer #(.select(4), .width(32), .enable("false")) multiplexer_1 (
    .in0(shifter_1_out), .in1(shifter_2_out), .in2(shifter_3_out), .in3(multiplier_1_out),
    .in4(divider_1_out), .in5(adder_1_out), .in6(subtractor_1_out), .in7(AND_out), .in8(OR_out),
    .in9(XOR_out), .in10(NOR_out), .in11({{31{1'b0}}, comparator_1_lt[0]}),
    .in12({{31{1'b0}}, comparator_2_lt[0]}), .in13({32{1'b0}}), .in14({32{1'b0}}), .in15({32{1'b0}}),
    .out(Result), .sel(AluOP));
  Multiplexer #(.select(4), .width(32), .enable("false")) multiplexer_2 (
    .in0({32{1'b0}}), .in1({32{1'b0}}), .in2({32{1'b0}}), .in3(multiplier_1_cout), .in4(divider_1_rem),
    .in5({32{1'b0}}), .in6({32{1'b0}}), .in7({32{1'b0}}), .in8({32{1'b0}}), .in9({32{1'b0}}),
    .in10({32{1'b0}}), .in11({32{1'b0}}), .in12({32{1'b0}}), .in13({32{1'b0}}), .in14({32{1'b0}}),
    .in15({32{1'b0}}), .out(Result_2), .sel(AluOP));

  // Other names for the same wires on the sheet: Result2[31:0] = Result_2; S[3:0] = AluOP

  // Notes on the sheet:
  //   不要改变此引脚区域内容，也不要改变ALU封装形式
  //   输入引脚
  //   输出引脚
endmodule

module MIPS_Regifile (
  input  [31:0] Din,
  input  Clk,
  input  WE,
  input  [4:0] R1_num,
  input  [4:0] W_num,
  input  [4:0] R2_num,
  output [31:0] R1,
  output [31:0] R2
);

  // RegisterFile registerfile_1: pin names not known; wires that end beside it: Din, Clk, WE, W_num, R1_num, R2_num, R1, R2
endmodule

module IF_ID (
  input  [31:0] PCin,
  input  [31:0] IRin,
  input  [31:0] PC_4in,
  input  CLK,
  input  \同步清零 ,
  input  \使能端 ,
  output [31:0] PCout,
  output [31:0] IRout,
  output [31:0] PC_4out
);

  wire not_1_out;
  wire [31:0] multiplexer_1_out, multiplexer_2_out, multiplexer_3_out;

  Multiplexer #(.width(32), .enable("false")) multiplexer_1 (
    .in0(PCin), .in1({32{1'b0}}), .out(multiplexer_1_out), .sel(\同步清零 ));
  Multiplexer #(.width(32), .enable("false")) multiplexer_2 (
    .in0(IRin), .in1({32{1'b0}}), .out(multiplexer_2_out), .sel(\同步清零 ));
  Multiplexer #(.width(32), .enable("false")) multiplexer_3 (
    .in0(PC_4in), .in1({32{1'b0}}), .out(multiplexer_3_out), .sel(\同步清零 ));
  not not_1 (not_1_out, \使能端 );
  Register #(.width(32)) register_1 (.D(multiplexer_1_out), .en(not_1_out), .Q(PCout), .clk(CLK));  // open: clr
  Register #(.width(32)) register_2 (.D(multiplexer_2_out), .en(not_1_out), .Q(IRout), .clk(CLK));  // open: clr
  Register #(.width(32)) register_3 (.D(multiplexer_3_out), .en(not_1_out), .Q(PC_4out), .clk(CLK));  // open: clr
endmodule

module ID_EX (
  input  Beqin,
  input  Bnein,
  input  JMPin,
  input  JRin,
  input  [31:0] PC_4in,
  input  JALin,
  input  MemToRegin,
  input  MemWritein,
  input  [3:0] AluOPin,
  input  AluSrcin,
  input  RegWritein,
  input  [4:0] WriteRegin,
  input  [31:0] PCin,
  input  [31:0] IRin,
  input  [31:0] Ain,
  input  [31:0] Bin,
  input  [31:0] IMMin,
  input  [31:0] EIMMin,
  input  Systemcallin,
  input  [4:0] Shamtin,
  input  CLK,
  input  \同步清零 ,
  input  \使能端 ,
  output Beqout,
  output Bneout,
  output JMPout,
  output JRout,
  output [31:0] PC_4out,
  output JALout,
  output MemToRegout,
  output MemWriteout,
  output [3:0] AluOPout,
  output AluSrcout,
  output RegWriteout,
  output [4:0] WriteRegout,
  output [31:0] PCout,
  output [31:0] IRout,
  output [31:0] Aout,
  output [31:0] Bout,
  output [31:0] IMMout,
  output [31:0] EIMMout,
  output Systemcallout,
  output [4:0] Shamtout
);

  wire multiplexer_1_out, multiplexer_2_out, multiplexer_3_out, multiplexer_4_out, multiplexer_6_out,
       multiplexer_7_out, multiplexer_8_out, multiplexer_10_out, multiplexer_11_out, multiplexer_19_out,
       not_1_out;
  wire [3:0] multiplexer_9_out;
  wire [4:0] multiplexer_12_out, multiplexer_20_out;
  wire [31:0] multiplexer_5_out, multiplexer_13_out, multiplexer_14_out, multiplexer_15_out,
       multiplexer_16_out, multiplexer_17_out, multiplexer_18_out;

  Multiplexer #(.enable("false")) multiplexer_1 (.in0(Beqin), .in1(1'b0), .out(multiplexer_1_out), .sel(\同步清零 ));
  Multiplexer #(.enable("false")) multiplexer_2 (.in0(Bnein), .in1(1'b0), .out(multiplexer_2_out), .sel(\同步清零 ));
  Multiplexer #(.enable("false")) multiplexer_3 (.in0(JMPin), .in1(1'b0), .out(multiplexer_3_out), .sel(\同步清零 ));
  Multiplexer #(.enable("false")) multiplexer_4 (.in0(JRin), .in1(1'b0), .out(multiplexer_4_out), .sel(\同步清零 ));
  Multiplexer #(.width(32), .enable("false")) multiplexer_5 (
    .in0(PC_4in), .in1({32{1'b0}}), .out(multiplexer_5_out), .sel(\同步清零 ));
  Multiplexer #(.enable("false")) multiplexer_6 (.in0(JALin), .in1(1'b0), .out(multiplexer_6_out), .sel(\同步清零 ));
  Multiplexer #(.enable("false")) multiplexer_7 (.in0(MemToRegin), .in1(1'b0), .out(multiplexer_7_out), .sel(\同步清零 ));
  Multiplexer #(.enable("false")) multiplexer_8 (.in0(MemWritein), .in1(1'b0), .out(multiplexer_8_out), .sel(\同步清零 ));
  Multiplexer #(.width(4), .enable("false")) multiplexer_9 (
    .in0(AluOPin), .in1(4'b0000), .out(multiplexer_9_out), .sel(\同步清零 ));
  Multiplexer #(.enable("false")) multiplexer_10 (.in0(AluSrcin), .in1(1'b0), .out(multiplexer_10_out), .sel(\同步清零 ));
  Multiplexer #(.enable("false")) multiplexer_11 (.in0(RegWritein), .in1(1'b0), .out(multiplexer_11_out), .sel(\同步清零 ));
  Multiplexer #(.width(5), .enable("false")) multiplexer_12 (
    .in0(WriteRegin), .in1({5{1'b0}}), .out(multiplexer_12_out), .sel(\同步清零 ));
  Multiplexer #(.width(32), .enable("false")) multiplexer_13 (
    .in0(PCin), .in1({32{1'b0}}), .out(multiplexer_13_out), .sel(\同步清零 ));
  Multiplexer #(.width(32), .enable("false")) multiplexer_14 (
    .in0(IRin), .in1({32{1'b0}}), .out(multiplexer_14_out), .sel(\同步清零 ));
  Multiplexer #(.width(32), .enable("false")) multiplexer_15 (
    .in0(Ain), .in1({32{1'b0}}), .out(multiplexer_15_out), .sel(\同步清零 ));
  Multiplexer #(.width(32), .enable("false")) multiplexer_16 (
    .in0(Bin), .in1({32{1'b0}}), .out(multiplexer_16_out), .sel(\同步清零 ));
  Multiplexer #(.width(32), .enable("false")) multiplexer_17 (
    .in0(IMMin), .in1({32{1'b0}}), .out(multiplexer_17_out), .sel(\同步清零 ));
  Multiplexer #(.width(32), .enable("false")) multiplexer_18 (
    .in0(EIMMin), .in1({32{1'b0}}), .out(multiplexer_18_out), .sel(\同步清零 ));
  Multiplexer #(.enable("false")) multiplexer_19 (
    .in0(Systemcallin), .in1(1'b0), .out(multiplexer_19_out), .sel(\同步清零 ));
  Multiplexer #(.width(5), .enable("false")) multiplexer_20 (
    .in0(Shamtin), .in1({5{1'b0}}), .out(multiplexer_20_out), .sel(\同步清零 ));
  not not_1 (not_1_out, \使能端 );
  Register #(.width(1)) register_1 (.D(multiplexer_1_out), .en(not_1_out), .Q(Beqout), .clk(CLK));  // open: clr
  Register #(.width(1)) register_2 (.D(multiplexer_2_out), .en(not_1_out), .Q(Bneout), .clk(CLK));  // open: clr
  Register #(.width(1)) register_3 (.D(multiplexer_3_out), .en(not_1_out), .Q(JMPout), .clk(CLK));  // open: clr
  Register #(.width(1)) register_4 (.D(multiplexer_4_out), .en(not_1_out), .Q(JRout), .clk(CLK));  // open: clr
  Register #(.width(32)) register_5 (.D(multiplexer_5_out), .en(not_1_out), .Q(PC_4out), .clk(CLK));  // open: clr
  Register #(.width(1)) register_6 (.D(multiplexer_6_out), .en(not_1_out), .Q(JALout), .clk(CLK));  // open: clr
  Register #(.width(1)) register_7 (.D(multiplexer_7_out), .en(not_1_out), .Q(MemToRegout), .clk(CLK));  // open: clr
  Register #(.width(1)) register_8 (.D(multiplexer_8_out), .en(not_1_out), .Q(MemWriteout), .clk(CLK));  // open: clr
  Register #(.width(4)) register_9 (.D(multiplexer_9_out), .en(not_1_out), .Q(AluOPout), .clk(CLK));  // open: clr
  Register #(.width(1)) register_10 (.D(multiplexer_10_out), .en(not_1_out), .Q(AluSrcout), .clk(CLK));  // open: clr
  Register #(.width(1)) register_11 (.D(multiplexer_11_out), .en(not_1_out), .Q(RegWriteout), .clk(CLK));  // open: clr
  Register #(.width(5)) register_12 (.D(multiplexer_12_out), .en(not_1_out), .Q(WriteRegout), .clk(CLK));  // open: clr
  Register #(.width(32)) register_13 (.D(multiplexer_13_out), .en(not_1_out), .Q(PCout), .clk(CLK));  // open: clr
  Register #(.width(32)) register_14 (.D(multiplexer_14_out), .en(not_1_out), .Q(IRout), .clk(CLK));  // open: clr
  Register #(.width(32)) register_15 (.D(multiplexer_15_out), .en(not_1_out), .Q(Aout), .clk(CLK));  // open: clr
  Register #(.width(32)) register_16 (.D(multiplexer_16_out), .en(not_1_out), .Q(Bout), .clk(CLK));  // open: clr
  Register #(.width(32)) register_17 (.D(multiplexer_17_out), .en(not_1_out), .Q(IMMout), .clk(CLK));  // open: clr
  Register #(.width(32)) register_18 (.D(multiplexer_18_out), .en(not_1_out), .Q(EIMMout), .clk(CLK));  // open: clr
  Register #(.width(1)) register_19 (
    .D(multiplexer_19_out), .en(not_1_out), .Q(Systemcallout), .clk(CLK));  // open: clr
  Register #(.width(5)) register_20 (.D(multiplexer_20_out), .en(not_1_out), .Q(Shamtout), .clk(CLK));  // open: clr
endmodule

module EX_MEM (
  input  [31:0] PC_4in,
  input  JALin,
  input  Systemcallin,
  input  MemToRegin,
  input  MemWritein,
  input  RegWritein,
  input  [4:0] WriteRegin,
  input  [31:0] PCin,
  input  [31:0] IRin,
  input  [31:0] ALUin,
  input  [31:0] Bin,
  input  [31:0] Ain,
  input  CLK,
  input  \同步清零 ,
  input  \使能端 ,
  output [31:0] PC_4out,
  output JALout,
  output Systemcallout,
  output MemToRegout,
  output MemWriteout,
  output RegWriteout,
  output [4:0] WriteRegout,
  output [31:0] PCout,
  output [31:0] IRout,
  output [31:0] ALUout,
  output [31:0] Bout,
  output [31:0] Aout
);

  wire multiplexer_2_out, multiplexer_3_out, multiplexer_4_out, multiplexer_5_out, multiplexer_6_out,
       not_1_out;
  wire [4:0] multiplexer_7_out;
  wire [31:0] multiplexer_1_out, multiplexer_8_out, multiplexer_9_out, multiplexer_10_out,
       multiplexer_11_out, multiplexer_12_out;

  Multiplexer #(.width(32), .enable("false")) multiplexer_1 (
    .in0(PC_4in), .in1({32{1'b0}}), .out(multiplexer_1_out), .sel(\同步清零 ));
  Multiplexer #(.enable("false")) multiplexer_2 (.in0(JALin), .in1(1'b0), .out(multiplexer_2_out), .sel(\同步清零 ));
  Multiplexer #(.enable("false")) multiplexer_3 (.in0(Systemcallin), .in1(1'b0), .out(multiplexer_3_out), .sel(\同步清零 ));
  Multiplexer #(.enable("false")) multiplexer_4 (.in0(MemToRegin), .in1(1'b0), .out(multiplexer_4_out), .sel(\同步清零 ));
  Multiplexer #(.enable("false")) multiplexer_5 (.in0(MemWritein), .in1(1'b0), .out(multiplexer_5_out), .sel(\同步清零 ));
  Multiplexer #(.enable("false")) multiplexer_6 (.in0(RegWritein), .out(multiplexer_6_out), .sel(\同步清零 ));  // open: in1
  Multiplexer #(.width(5), .enable("false")) multiplexer_7 (
    .in0(WriteRegin), .in1({5{1'b0}}), .out(multiplexer_7_out), .sel(\同步清零 ));
  Multiplexer #(.width(32), .enable("false")) multiplexer_8 (
    .in0(PCin), .in1({32{1'b0}}), .out(multiplexer_8_out), .sel(\同步清零 ));
  Multiplexer #(.width(32), .enable("false")) multiplexer_9 (
    .in0(IRin), .in1({32{1'b0}}), .out(multiplexer_9_out), .sel(\同步清零 ));
  Multiplexer #(.width(32), .enable("false")) multiplexer_10 (
    .in0(ALUin), .in1({32{1'b0}}), .out(multiplexer_10_out), .sel(\同步清零 ));
  Multiplexer #(.width(32), .enable("false")) multiplexer_11 (
    .in0(Bin), .in1({32{1'b0}}), .out(multiplexer_11_out), .sel(\同步清零 ));
  Multiplexer #(.width(32), .enable("false")) multiplexer_12 (
    .in0(Ain), .in1({32{1'b0}}), .out(multiplexer_12_out), .sel(\同步清零 ));
  not not_1 (not_1_out, \使能端 );
  Register #(.width(32)) register_1 (.D(multiplexer_1_out), .en(not_1_out), .Q(PC_4out), .clk(CLK));  // open: clr
  Register #(.width(1)) register_2 (.D(multiplexer_2_out), .en(not_1_out), .Q(JALout), .clk(CLK));  // open: clr
  Register #(.width(1)) register_3 (.D(multiplexer_3_out), .en(not_1_out), .Q(Systemcallout), .clk(CLK));  // open: clr
  Register #(.width(1)) register_4 (.D(multiplexer_4_out), .en(not_1_out), .Q(MemToRegout), .clk(CLK));  // open: clr
  Register #(.width(1)) register_5 (.D(multiplexer_5_out), .en(not_1_out), .Q(MemWriteout), .clk(CLK));  // open: clr
  Register #(.width(1)) register_6 (.D(multiplexer_6_out), .en(not_1_out), .Q(RegWriteout), .clk(CLK));  // open: clr
  Register #(.width(5)) register_7 (.D(multiplexer_7_out), .en(not_1_out), .Q(WriteRegout), .clk(CLK));  // open: clr
  Register #(.width(32)) register_8 (.D(multiplexer_8_out), .en(not_1_out), .Q(PCout), .clk(CLK));  // open: clr
  Register #(.width(32)) register_9 (.D(multiplexer_9_out), .en(not_1_out), .Q(IRout), .clk(CLK));  // open: clr
  Register #(.width(32)) register_10 (.D(multiplexer_10_out), .en(not_1_out), .Q(ALUout), .clk(CLK));  // open: clr
  Register #(.width(32)) register_11 (.D(multiplexer_11_out), .en(not_1_out), .Q(Bout), .clk(CLK));  // open: clr
  Register #(.width(32)) register_12 (.D(multiplexer_12_out), .en(not_1_out), .Q(Aout), .clk(CLK));  // open: clr
endmodule

module MEM_WB (
  input  JALin,
  input  RegWritein,
  input  MemToRegin,
  input  Systemcallin,
  input  [31:0] IRin,
  input  [31:0] PCin,
  input  [4:0] WriteRegin,
  input  [31:0] ALUin,
  input  [31:0] MDin,
  input  [31:0] Ain,
  input  [31:0] Bin,
  input  [31:0] PC_4in,
  input  CLK,
  input  \同步清零 ,
  input  \使能端 ,
  output JALout,
  output RegWriteout,
  output MemToRegout,
  output Systemcallout,
  output [31:0] IRout,
  output [31:0] PCout,
  output [4:0] WriteRegout,
  output [31:0] ALUout,
  output [31:0] MDout,
  output [31:0] Aout,
  output [31:0] Bout,
  output [31:0] PC_4out
);

  wire multiplexer_1_out, multiplexer_2_out, multiplexer_3_out, multiplexer_4_out, not_1_out;
  wire [4:0] multiplexer_7_out;
  wire [31:0] multiplexer_5_out, multiplexer_6_out, multiplexer_8_out, multiplexer_9_out, multiplexer_10_out,
       multiplexer_11_out, multiplexer_12_out;

  Multiplexer #(.enable("false")) multiplexer_1 (.in0(JALin), .in1(1'b0), .out(multiplexer_1_out), .sel(\同步清零 ));
  Multiplexer #(.enable("false")) multiplexer_2 (.in0(RegWritein), .in1(1'b0), .out(multiplexer_2_out), .sel(\同步清零 ));
  Multiplexer #(.enable("false")) multiplexer_3 (.in0(MemToRegin), .in1(1'b0), .out(multiplexer_3_out), .sel(\同步清零 ));
  Multiplexer #(.enable("false")) multiplexer_4 (.in0(Systemcallin), .in1(1'b0), .out(multiplexer_4_out), .sel(\同步清零 ));
  Multiplexer #(.width(32), .enable("false")) multiplexer_5 (
    .in0(IRin), .in1({32{1'b0}}), .out(multiplexer_5_out), .sel(\同步清零 ));
  Multiplexer #(.width(32), .enable("false")) multiplexer_6 (
    .in0(PCin), .in1({32{1'b0}}), .out(multiplexer_6_out), .sel(\同步清零 ));
  Multiplexer #(.width(5), .enable("false")) multiplexer_7 (
    .in0(WriteRegin), .in1({5{1'b0}}), .out(multiplexer_7_out), .sel(\同步清零 ));
  Multiplexer #(.width(32), .enable("false")) multiplexer_8 (
    .in0(ALUin), .in1({32{1'b0}}), .out(multiplexer_8_out), .sel(\同步清零 ));
  Multiplexer #(.width(32), .enable("false")) multiplexer_9 (
    .in0(MDin), .in1({32{1'b0}}), .out(multiplexer_9_out), .sel(\同步清零 ));
  Multiplexer #(.width(32), .enable("false")) multiplexer_10 (
    .in0(Ain), .in1({32{1'b0}}), .out(multiplexer_10_out), .sel(\同步清零 ));
  Multiplexer #(.width(32), .enable("false")) multiplexer_11 (
    .in0(Bin), .in1({32{1'b0}}), .out(multiplexer_11_out), .sel(\同步清零 ));
  Multiplexer #(.width(32), .enable("false")) multiplexer_12 (
    .in0(PC_4in), .in1({32{1'b0}}), .out(multiplexer_12_out), .sel(\同步清零 ));
  not not_1 (not_1_out, \使能端 );
  Register #(.width(1)) register_1 (.D(multiplexer_1_out), .en(not_1_out), .Q(JALout), .clk(CLK));  // open: clr
  Register #(.width(1)) register_2 (.D(multiplexer_2_out), .en(not_1_out), .Q(RegWriteout), .clk(CLK));  // open: clr
  Register #(.width(1)) register_3 (.D(multiplexer_3_out), .en(not_1_out), .Q(MemToRegout), .clk(CLK));  // open: clr
  Register #(.width(1)) register_4 (.D(multiplexer_4_out), .en(not_1_out), .Q(Systemcallout), .clk(CLK));  // open: clr
  Register #(.width(32)) register_5 (.D(multiplexer_5_out), .en(not_1_out), .Q(IRout), .clk(CLK));  // open: clr
  Register #(.width(32)) register_6 (.D(multiplexer_6_out), .en(not_1_out), .Q(PCout), .clk(CLK));  // open: clr
  Register #(.width(5)) register_7 (.D(multiplexer_7_out), .en(not_1_out), .Q(WriteRegout), .clk(CLK));  // open: clr
  Register #(.width(32)) register_8 (.D(multiplexer_8_out), .en(not_1_out), .Q(ALUout), .clk(CLK));  // open: clr
  Register #(.width(32)) register_9 (.D(multiplexer_9_out), .en(not_1_out), .Q(MDout), .clk(CLK));  // open: clr
  Register #(.width(32)) register_10 (.D(multiplexer_10_out), .en(not_1_out), .Q(Aout), .clk(CLK));  // open: clr
  Register #(.width(32)) register_11 (.D(multiplexer_11_out), .en(not_1_out), .Q(Bout), .clk(CLK));  // open: clr
  Register #(.width(32)) register_12 (.D(multiplexer_12_out), .en(not_1_out), .Q(PC_4out), .clk(CLK));  // open: clr
endmodule

module \源寄存器使用情况  (
  input  OP0,
  input  OP1,
  input  OP2,
  input  OP3,
  input  OP4,
  input  OP5,
  input  F1,
  input  F2,
  input  F0,
  input  F3,
  input  F4,
  input  F5,
  output R1_Used,
  output R2_Used
);

  wire and_1_out, and_2_out, and_3_out, and_4_out, and_5_out, and_6_out, and_7_out, and_8_out, and_9_out,
       and_10_out, and_11_out, and_12_out, and_13_out, and_14_out, and_15_out, and_16_out, and_17_out,
       and_18_out, and_19_out, and_20_out, and_21_out, and_22_out, and_23_out, and_24_out, and_25_out,
       and_26_out, and_27_out, and_28_out, and_29_out, and_30_out, and_31_out, and_32_out, and_33_out,
       and_34_out, and_35_out, and_36_out, and_37_out, and_38_out, and_39_out, and_40_out, and_41_out,
       and_42_out, not_1_out, not_2_out, not_3_out, not_4_out, not_5_out, not_6_out, not_7_out, not_8_out,
       not_9_out, not_10_out, not_11_out, not_12_out, not_13_out, not_14_out, not_15_out, not_16_out,
       not_17_out, not_18_out, not_19_out, not_20_out, not_21_out, not_22_out, not_23_out, not_24_out,
       not_25_out, not_26_out, not_27_out, not_28_out, not_29_out, not_30_out, not_31_out, not_32_out,
       not_33_out, not_34_out, not_35_out, not_36_out, not_37_out, not_38_out, not_39_out, not_40_out,
       not_41_out, not_42_out, not_43_out, not_44_out, not_45_out, not_46_out, not_47_out, not_48_out,
       not_49_out, not_50_out, not_51_out, not_52_out, not_53_out, not_54_out, not_55_out, not_56_out,
       not_57_out, not_58_out, not_59_out, not_60_out, not_61_out, not_62_out, not_63_out, not_64_out,
       not_65_out, not_66_out, not_67_out, not_68_out, not_69_out, not_70_out, not_71_out, not_72_out,
       not_73_out, not_74_out, not_75_out, not_76_out, not_77_out, not_78_out, not_79_out, not_80_out,
       not_81_out, not_82_out, not_83_out, not_84_out, not_85_out, not_86_out, not_87_out, not_88_out,
       not_89_out, not_90_out, not_91_out, not_92_out, not_93_out, not_94_out, not_95_out, not_96_out,
       not_97_out, not_98_out, not_99_out, not_100_out, not_101_out, not_102_out, not_103_out, not_104_out,
       not_105_out, not_106_out, not_107_out, not_108_out, not_109_out, not_110_out, not_111_out,
       not_112_out, not_113_out, not_114_out, not_115_out, not_116_out, not_117_out, not_118_out,
       not_119_out, not_120_out, not_121_out, not_122_out, not_123_out, not_124_out, not_125_out,
       not_126_out, not_127_out, not_128_out, not_129_out, not_130_out, not_131_out, not_132_out,
       not_133_out, not_134_out, not_135_out, not_136_out, not_137_out, not_138_out, not_139_out,
       not_140_out, not_141_out, not_142_out, not_143_out, not_144_out, not_145_out, not_146_out,
       not_147_out, not_148_out, not_149_out, not_150_out, not_151_out, not_152_out, not_153_out,
       not_154_out, not_155_out, not_156_out, not_157_out, not_158_out, not_159_out, not_160_out,
       not_161_out, not_162_out, not_163_out, not_164_out, not_165_out, not_166_out, not_167_out,
       not_168_out, not_169_out, not_170_out, not_171_out, not_172_out, not_173_out, not_174_out,
       not_175_out, not_176_out, not_177_out, not_178_out, not_179_out, not_180_out, not_181_out,
       not_182_out, not_183_out, not_184_out, not_185_out, not_186_out, not_187_out, not_188_out,
       not_189_out, not_190_out, not_191_out, not_192_out, not_193_out, not_194_out, not_195_out,
       not_196_out, not_197_out, not_198_out, not_199_out, not_200_out, not_201_out, not_202_out,
       not_203_out, not_204_out, not_205_out, not_206_out, not_207_out, not_208_out, not_209_out,
       not_210_out, not_211_out, not_212_out, not_213_out, not_214_out, not_215_out, not_216_out,
       not_217_out, not_218_out, not_219_out, not_220_out, not_221_out, not_222_out, not_223_out,
       not_224_out, not_225_out, not_226_out, not_227_out, not_228_out, not_229_out, not_230_out,
       not_231_out, not_232_out, not_233_out, not_234_out, not_235_out, not_236_out, not_237_out,
       not_238_out, not_239_out, not_240_out, not_241_out, not_242_out, not_243_out, not_244_out,
       not_245_out, not_246_out, not_247_out, not_248_out, not_249_out, not_250_out, not_251_out,
       not_252_out, not_253_out, not_254_out, not_255_out, not_256_out, not_257_out, not_258_out,
       not_259_out, not_260_out, not_261_out, not_262_out, not_263_out, not_264_out, not_265_out,
       not_266_out, not_267_out, not_268_out, not_269_out, not_270_out, not_271_out, not_272_out,
       not_273_out, not_274_out, not_275_out, not_276_out, not_277_out, not_278_out, not_279_out,
       not_280_out, not_281_out, not_282_out, not_283_out, not_284_out, not_285_out, not_286_out,
       not_287_out, not_288_out, not_289_out, not_290_out, not_291_out, not_292_out, not_293_out,
       not_294_out, not_295_out, not_296_out, not_297_out, not_298_out, not_299_out, not_300_out,
       not_301_out, not_302_out, not_303_out, not_304_out, not_305_out, not_306_out, not_307_out,
       not_308_out, not_309_out, not_310_out, not_311_out, not_312_out, not_313_out, not_314_out,
       not_315_out, not_316_out, not_317_out, not_318_out, not_319_out, not_320_out, not_321_out,
       not_322_out, not_323_out;

  not not_1 (not_1_out, OP5);
  not not_2 (not_2_out, OP4);
  not not_3 (not_3_out, OP3);
  not not_4 (not_4_out, OP2);
  not not_5 (not_5_out, OP1);
  not not_6 (not_6_out, OP0);
  not not_7 (not_7_out, F5);
  not not_8 (not_8_out, F4);
  not not_9 (not_9_out, F3);
  not not_10 (not_10_out, F2);
  not not_11 (not_11_out, F1);
  not not_12 (not_12_out, F0);
  not not_13 (not_13_out, OP5);
  not not_14 (not_14_out, OP4);
  not not_15 (not_15_out, OP3);
  not not_16 (not_16_out, OP2);
  not not_17 (not_17_out, OP1);
  not not_18 (not_18_out, OP0);
  not not_19 (not_19_out, F5);
  not not_20 (not_20_out, F4);
  not not_21 (not_21_out, F3);
  not not_22 (not_22_out, F2);
  not not_23 (not_23_out, OP5);
  not not_24 (not_24_out, OP4);
  not not_25 (not_25_out, OP3);
  not not_26 (not_26_out, OP2);
  not not_27 (not_27_out, OP1);
  not not_28 (not_28_out, OP0);
  not not_29 (not_29_out, F5);
  not not_30 (not_30_out, F4);
  not not_31 (not_31_out, F3);
  not not_32 (not_32_out, F2);
  not not_33 (not_33_out, F0);
  not not_34 (not_34_out, OP5);
  not not_35 (not_35_out, OP4);
  not not_36 (not_36_out, OP3);
  not not_37 (not_37_out, OP2);
  not not_38 (not_38_out, OP1);
  not not_39 (not_39_out, OP0);
  not not_40 (not_40_out, F4);
  not not_41 (not_41_out, F3);
  not not_42 (not_42_out, F2);
  not not_43 (not_43_out, F1);
  not not_44 (not_44_out, F0);
  not not_45 (not_45_out, OP5);
  not not_46 (not_46_out, OP4);
  not not_47 (not_47_out, OP3);
  not not_48 (not_48_out, OP2);
  not not_49 (not_49_out, OP1);
  not not_50 (not_50_out, OP0);
  not not_51 (not_51_out, F4);
  not not_52 (not_52_out, F3);
  not not_53 (not_53_out, F2);
  not not_54 (not_54_out, F1);
  not not_55 (not_55_out, OP5);
  not not_56 (not_56_out, OP4);
  not not_57 (not_57_out, OP3);
  not not_58 (not_58_out, OP2);
  not not_59 (not_59_out, OP1);
  not not_60 (not_60_out, OP0);
  not not_61 (not_61_out, F4);
  not not_62 (not_62_out, F3);
  not not_63 (not_63_out, F2);
  not not_64 (not_64_out, F0);
  not not_65 (not_65_out, OP5);
  not not_66 (not_66_out, OP4);
  not not_67 (not_67_out, OP3);
  not not_68 (not_68_out, OP2);
  not not_69 (not_69_out, OP1);
  not not_70 (not_70_out, OP0);
  not not_71 (not_71_out, F4);
  not not_72 (not_72_out, F3);
  not not_73 (not_73_out, F1);
  not not_74 (not_74_out, F0);
  not not_75 (not_75_out, OP5);
  not not_76 (not_76_out, OP4);
  not not_77 (not_77_out, OP3);
  not not_78 (not_78_out, OP2);
  not not_79 (not_79_out, OP1);
  not not_80 (not_80_out, OP0);
  not not_81 (not_81_out, F4);
  not not_82 (not_82_out, F3);
  not not_83 (not_83_out, F1);
  not not_84 (not_84_out, OP5);
  not not_85 (not_85_out, OP4);
  not not_86 (not_86_out, OP3);
  not not_87 (not_87_out, OP2);
  not not_88 (not_88_out, OP1);
  not not_89 (not_89_out, OP0);
  not not_90 (not_90_out, F4);
  not not_91 (not_91_out, F3);
  not not_92 (not_92_out, OP5);
  not not_93 (not_93_out, OP4);
  not not_94 (not_94_out, OP3);
  not not_95 (not_95_out, OP2);
  not not_96 (not_96_out, OP1);
  not not_97 (not_97_out, OP0);
  not not_98 (not_98_out, F4);
  not not_99 (not_99_out, F2);
  not not_100 (not_100_out, F0);
  not not_101 (not_101_out, OP5);
  not not_102 (not_102_out, OP4);
  not not_103 (not_103_out, OP3);
  not not_104 (not_104_out, OP2);
  not not_105 (not_105_out, OP1);
  not not_106 (not_106_out, OP0);
  not not_107 (not_107_out, F4);
  not not_108 (not_108_out, F2);
  not not_109 (not_109_out, OP5);
  not not_110 (not_110_out, OP4);
  not not_111 (not_111_out, OP3);
  not not_112 (not_112_out, OP2);
  not not_113 (not_113_out, OP1);
  not not_114 (not_114_out, OP0);
  not not_115 (not_115_out, F5);
  not not_116 (not_116_out, F4);
  not not_117 (not_117_out, F2);
  not not_118 (not_118_out, F1);
  not not_119 (not_119_out, F0);
  not not_120 (not_120_out, OP5);
  not not_121 (not_121_out, OP4);
  not not_122 (not_122_out, OP3);
  not not_123 (not_123_out, OP2);
  not not_124 (not_124_out, OP1);
  not not_125 (not_125_out, OP0);
  not not_126 (not_126_out, F5);
  not not_127 (not_127_out, F4);
  not not_128 (not_128_out, F1);
  not not_129 (not_129_out, F0);
  not not_130 (not_130_out, OP5);
  not not_131 (not_131_out, OP4);
  not not_132 (not_132_out, OP3);
  not not_133 (not_133_out, OP1);
  not not_134 (not_134_out, OP0);
  not not_135 (not_135_out, OP5);
  not not_136 (not_136_out, OP4);
  not not_137 (not_137_out, OP3);
  not not_138 (not_138_out, OP1);
  not not_139 (not_139_out, OP5);
  not not_140 (not_140_out, OP4);
  not not_141 (not_141_out, OP2);
  not not_142 (not_142_out, OP1);
  not not_143 (not_143_out, OP0);
  not not_144 (not_144_out, OP5);
  not not_145 (not_145_out, OP4);
  not not_146 (not_146_out, OP1);
  not not_147 (not_147_out, OP0);
  not not_148 (not_148_out, OP5);
  not not_149 (not_149_out, OP4);
  not not_150 (not_150_out, OP2);
  not not_151 (not_151_out, OP1);
  not not_152 (not_152_out, OP5);
  not not_153 (not_153_out, OP4);
  not not_154 (not_154_out, OP2);
  not not_155 (not_155_out, OP0);
  not not_156 (not_156_out, OP5);
  not not_157 (not_157_out, OP4);
  not not_158 (not_158_out, OP1);
  not not_159 (not_159_out, OP4);
  not not_160 (not_160_out, OP3);
  not not_161 (not_161_out, OP2);
  not not_162 (not_162_out, OP4);
  not not_163 (not_163_out, OP2);
  not not_164 (not_164_out, OP5);
  not not_165 (not_165_out, OP4);
  not not_166 (not_166_out, OP3);
  not not_167 (not_167_out, OP2);
  not not_168 (not_168_out, OP1);
  not not_169 (not_169_out, OP0);
  not not_170 (not_170_out, F4);
  not not_171 (not_171_out, F3);
  not not_172 (not_172_out, F2);
  not not_173 (not_173_out, OP5);
  not not_174 (not_174_out, OP4);
  not not_175 (not_175_out, OP2);
  not not_176 (not_176_out, OP4);
  not not_177 (not_177_out, OP3);
  not not_178 (not_178_out, OP2);
  not not_179 (not_179_out, OP1);
  not not_180 (not_180_out, OP0);
  not not_181 (not_181_out, OP5);
  not not_182 (not_182_out, OP4);
  not not_183 (not_183_out, OP3);
  not not_184 (not_184_out, OP2);
  not not_185 (not_185_out, OP1);
  not not_186 (not_186_out, OP5);
  not not_187 (not_187_out, OP4);
  not not_188 (not_188_out, OP3);
  not not_189 (not_189_out, OP2);
  not not_190 (not_190_out, OP1);
  not not_191 (not_191_out, OP0);
  not not_192 (not_192_out, F5);
  not not_193 (not_193_out, F4);
  not not_194 (not_194_out, F3);
  not not_195 (not_195_out, F2);
  not not_196 (not_196_out, F1);
  not not_197 (not_197_out, F0);
  not not_198 (not_198_out, OP5);
  not not_199 (not_199_out, OP4);
  not not_200 (not_200_out, OP3);
  not not_201 (not_201_out, OP2);
  not not_202 (not_202_out, OP1);
  not not_203 (not_203_out, OP0);
  not not_204 (not_204_out, F5);
  not not_205 (not_205_out, F4);
  not not_206 (not_206_out, F3);
  not not_207 (not_207_out, F2);
  not not_208 (not_208_out, OP5);
  not not_209 (not_209_out, OP4);
  not not_210 (not_210_out, OP3);
  not not_211 (not_211_out, OP2);
  not not_212 (not_212_out, OP1);
  not not_213 (not_213_out, OP0);
  not not_214 (not_214_out, F5);
  not not_215 (not_215_out, F4);
  not not_216 (not_216_out, F3);
  not not_217 (not_217_out, F2);
  not not_218 (not_218_out, F0);
  not not_219 (not_219_out, OP5);
  not not_220 (not_220_out, OP4);
  not not_221 (not_221_out, OP3);
  not not_222 (not_222_out, OP2);
  not not_223 (not_223_out, OP1);
  not not_224 (not_224_out, OP0);
  not not_225 (not_225_out, F4);
  not not_226 (not_226_out, F3);
  not not_227 (not_227_out, F2);
  not not_228 (not_228_out, F1);
  not not_229 (not_229_out, F0);
  not not_230 (not_230_out, OP5);
  not not_231 (not_231_out, OP4);
  not not_232 (not_232_out, OP3);
  not not_233 (not_233_out, OP2);
  not not_234 (not_234_out, OP1);
  not not_235 (not_235_out, OP0);
  not not_236 (not_236_out, F4);
  not not_237 (not_237_out, F3);
  not not_238 (not_238_out, F2);
  not not_239 (not_239_out, F1);
  not not_240 (not_240_out, OP5);
  not not_241 (not_241_out, OP4);
  not not_242 (not_242_out, OP3);
  not not_243 (not_243_out, OP2);
  not not_244 (not_244_out, OP1);
  not not_245 (not_245_out, OP0);
  not not_246 (not_246_out, F4);
  not not_247 (not_247_out, F3);
  not not_248 (not_248_out, F2);
  not not_249 (not_249_out, F0);
  not not_250 (not_250_out, OP5);
  not not_251 (not_251_out, OP4);
  not not_252 (not_252_out, OP3);
  not not_253 (not_253_out, OP2);
  not not_254 (not_254_out, OP1);
  not not_255 (not_255_out, OP0);
  not not_256 (not_256_out, F4);
  not not_257 (not_257_out, F3);
  not not_258 (not_258_out, F1);
  not not_259 (not_259_out, F0);
  not not_260 (not_260_out, OP5);
  not not_261 (not_261_out, OP4);
  not not_262 (not_262_out, OP3);
  not not_263 (not_263_out, OP2);
  not not_264 (not_264_out, OP1);
  not not_265 (not_265_out, OP0);
  not not_266 (not_266_out, F4);
  not not_267 (not_267_out, F3);
  not not_268 (not_268_out, F1);
  not not_269 (not_269_out, OP5);
  not not_270 (not_270_out, OP4);
  not not_271 (not_271_out, OP3);
  not not_272 (not_272_out, OP2);
  not not_273 (not_273_out, OP1);
  not not_274 (not_274_out, OP0);
  not not_275 (not_275_out, F4);
  not not_276 (not_276_out, F3);
  not not_277 (not_277_out, OP5);
  not not_278 (not_278_out, OP4);
  not not_279 (not_279_out, OP3);
  not not_280 (not_280_out, OP2);
  not not_281 (not_281_out, OP1);
  not not_282 (not_282_out, OP0);
  not not_283 (not_283_out, F4);
  not not_284 (not_284_out, F2);
  not not_285 (not_285_out, F0);
  not not_286 (not_286_out, OP5);
  not not_287 (not_287_out, OP4);
  not not_288 (not_288_out, OP3);
  not not_289 (not_289_out, OP2);
  not not_290 (not_290_out, OP1);
  not not_291 (not_291_out, OP0);
  not not_292 (not_292_out, F4);
  not not_293 (not_293_out, F2);
  not not_294 (not_294_out, OP5);
  not not_295 (not_295_out, OP4);
  not not_296 (not_296_out, OP3);
  not not_297 (not_297_out, OP2);
  not not_298 (not_298_out, OP1);
  not not_299 (not_299_out, OP0);
  not not_300 (not_300_out, F5);
  not not_301 (not_301_out, F4);
  not not_302 (not_302_out, F1);
  not not_303 (not_303_out, F0);
  not not_304 (not_304_out, OP5);
  not not_305 (not_305_out, OP4);
  not not_306 (not_306_out, OP3);
  not not_307 (not_307_out, OP1);
  not not_308 (not_308_out, OP0);
  not not_309 (not_309_out, OP5);
  not not_310 (not_310_out, OP4);
  not not_311 (not_311_out, OP3);
  not not_312 (not_312_out, OP1);
  not not_313 (not_313_out, OP4);
  not not_314 (not_314_out, OP2);
  not not_315 (not_315_out, OP5);
  not not_316 (not_316_out, OP4);
  not not_317 (not_317_out, OP3);
  not not_318 (not_318_out, OP2);
  not not_319 (not_319_out, OP1);
  not not_320 (not_320_out, OP0);
  not not_321 (not_321_out, F4);
  not not_322 (not_322_out, F3);
  not not_323 (not_323_out, F2);
  and and_1 (and_1_out, not_1_out, not_2_out, not_3_out, not_4_out, not_5_out, not_6_out, not_7_out, not_8_out, not_9_out, not_10_out, not_11_out, not_12_out);
  and and_2 (and_2_out, not_13_out, not_14_out, not_15_out, not_16_out, not_17_out, not_18_out, not_19_out, not_20_out, not_21_out, not_22_out, F1, F0);
  and and_3 (and_3_out, not_23_out, not_24_out, not_25_out, not_26_out, not_27_out, not_28_out, not_29_out, not_30_out, not_31_out, not_32_out, F1, not_33_out);
  and and_4 (and_4_out, not_34_out, not_35_out, not_36_out, not_37_out, not_38_out, not_39_out, F5, not_40_out, not_41_out, not_42_out, not_43_out, not_44_out);
  and and_5 (and_5_out, not_45_out, not_46_out, not_47_out, not_48_out, not_49_out, not_50_out, F5, not_51_out, not_52_out, not_53_out, not_54_out, F0);
  and and_6 (and_6_out, not_55_out, not_56_out, not_57_out, not_58_out, not_59_out, not_60_out, F5, not_61_out, not_62_out, not_63_out, F1, not_64_out);
  and and_7 (and_7_out, not_65_out, not_66_out, not_67_out, not_68_out, not_69_out, not_70_out, F5, not_71_out, not_72_out, F2, not_73_out, not_74_out);
  and and_8 (and_8_out, not_75_out, not_76_out, not_77_out, not_78_out, not_79_out, not_80_out, F5, not_81_out, not_82_out, F2, not_83_out, F0);
  and and_9 (and_9_out, not_84_out, not_85_out, not_86_out, not_87_out, not_88_out, not_89_out, F5, not_90_out, not_91_out, F2, F1, F0);
  and and_10 (and_10_out, not_92_out, not_93_out, not_94_out, not_95_out, not_96_out, not_97_out, F5, not_98_out, F3, not_99_out, F1, not_100_out);
  and and_11 (and_11_out, not_101_out, not_102_out, not_103_out, not_104_out, not_105_out, not_106_out, F5, not_107_out, F3, not_108_out, F1, F0);
  and and_12 (and_12_out, not_109_out, not_110_out, not_111_out, not_112_out, not_113_out, not_114_out, not_115_out, not_116_out, F3, not_117_out, not_118_out, not_119_out);
  and and_13 (and_13_out, not_120_out, not_121_out, not_122_out, not_123_out, not_124_out, not_125_out, not_126_out, not_127_out, F3, F2, not_128_out, not_129_out);
  and and_14 (and_14_out, not_130_out, not_131_out, not_132_out, OP2, not_133_out, not_134_out);
  and and_15 (and_15_out, not_135_out, not_136_out, not_137_out, OP2, not_138_out, OP0);
  and and_16 (and_16_out, not_139_out, not_140_out, OP3, not_141_out, not_142_out, not_143_out);
  and and_17 (and_17_out, not_144_out, not_145_out, OP3, OP2, not_146_out, not_147_out);
  and and_18 (and_18_out, not_148_out, not_149_out, OP3, not_150_out, not_151_out, OP0);
  and and_19 (and_19_out, not_152_out, not_153_out, OP3, not_154_out, OP1, not_155_out);
  and and_20 (and_20_out, not_156_out, not_157_out, OP3, OP2, not_158_out, OP0);
  and and_21 (and_21_out, OP5, not_159_out, not_160_out, not_161_out, OP1, OP0);
  and and_22 (and_22_out, OP5, not_162_out, OP3, not_163_out, OP1, OP0);
  and and_23 (and_23_out, not_164_out, not_165_out, not_166_out, not_167_out, not_168_out, not_169_out, F5, not_170_out, not_171_out, not_172_out, F1, F0);
  and and_24 (and_24_out, not_173_out, not_174_out, OP3, not_175_out, OP1, OP0);
  and and_25 (and_25_out, OP5, not_176_out, not_177_out, not_178_out, not_179_out, not_180_out);
  and and_26 (and_26_out, not_181_out, not_182_out, not_183_out, not_184_out, not_185_out, OP0);
  and and_27 (and_27_out, not_186_out, not_187_out, not_188_out, not_189_out, not_190_out, not_191_out, not_192_out, not_193_out, not_194_out, not_195_out, not_196_out, not_197_out);
  and and_28 (and_28_out, not_198_out, not_199_out, not_200_out, not_201_out, not_202_out, not_203_out, not_204_out, not_205_out, not_206_out, not_207_out, F1, F0);
  and and_29 (and_29_out, not_208_out, not_209_out, not_210_out, not_211_out, not_212_out, not_213_out, not_214_out, not_215_out, not_216_out, not_217_out, F1, not_218_out);
  and and_30 (and_30_out, not_219_out, not_220_out, not_221_out, not_222_out, not_223_out, not_224_out, F5, not_225_out, not_226_out, not_227_out, not_228_out, not_229_out);
  and and_31 (and_31_out, not_230_out, not_231_out, not_232_out, not_233_out, not_234_out, not_235_out, F5, not_236_out, not_237_out, not_238_out, not_239_out, F0);
  and and_32 (and_32_out, not_240_out, not_241_out, not_242_out, not_243_out, not_244_out, not_245_out, F5, not_246_out, not_247_out, not_248_out, F1, not_249_out);
  and and_33 (and_33_out, not_250_out, not_251_out, not_252_out, not_253_out, not_254_out, not_255_out, F5, not_256_out, not_257_out, F2, not_258_out, not_259_out);
  and and_34 (and_34_out, not_260_out, not_261_out, not_262_out, not_263_out, not_264_out, not_265_out, F5, not_266_out, not_267_out, F2, not_268_out, F0);
  and and_35 (and_35_out, not_269_out, not_270_out, not_271_out, not_272_out, not_273_out, not_274_out, F5, not_275_out, not_276_out, F2, F1, F0);
  and and_36 (and_36_out, not_277_out, not_278_out, not_279_out, not_280_out, not_281_out, not_282_out, F5, not_283_out, F3, not_284_out, F1, not_285_out);
  and and_37 (and_37_out, not_286_out, not_287_out, not_288_out, not_289_out, not_290_out, not_291_out, F5, not_292_out, F3, not_293_out, F1, F0);
  and and_38 (and_38_out, not_294_out, not_295_out, not_296_out, not_297_out, not_298_out, not_299_out, not_300_out, not_301_out, F3, F2, not_302_out, not_303_out);
  and and_39 (and_39_out, not_304_out, not_305_out, not_306_out, OP2, not_307_out, not_308_out);
  and and_40 (and_40_out, not_309_out, not_310_out, not_311_out, OP2, not_312_out, OP0);
  and and_41 (and_41_out, OP5, not_313_out, OP3, not_314_out, OP1, OP0);
  and and_42 (and_42_out, not_315_out, not_316_out, not_317_out, not_318_out, not_319_out, not_320_out, F5, not_321_out, not_322_out, not_323_out, F1, F0);
  or or_1 (R1_Used, and_1_out, and_2_out, and_3_out, and_4_out, and_5_out, and_6_out, and_7_out, and_8_out, and_9_out, and_10_out, and_11_out, and_12_out, and_13_out, and_14_out, and_15_out, and_16_out, and_17_out, and_18_out, and_19_out, and_20_out, and_21_out, and_22_out, and_23_out, and_24_out, and_25_out, and_26_out);
  or or_2 (R2_Used, and_27_out, and_28_out, and_29_out, and_30_out, and_31_out, and_32_out, and_33_out, and_34_out, and_35_out, and_36_out, and_37_out, and_38_out, and_39_out, and_40_out, and_41_out, and_42_out);
endmodule
module \数据相关检测  (
  input  [4:0] EX_WriteReg,
  input  [5:0] OP_CODE,
  input  [4:0] R1,
  input  [4:0] MEM_WriteReg,
  input  [5:0] FUNC,
  input  [4:0] R2,
  input  EX_RegWrite,
  input  MEM_RegWrite,
  output Relevant
);

  wire comparator_1_eq, comparator_2_eq, comparator_3_eq, comparator_4_eq, comparator_5_eq, comparator_6_eq,
       multiplexer_1_out, multiplexer_2_out, multiplexer_3_out, multiplexer_4_out, multiplexer_5_out,
       multiplexer_6_out, multiplexer_7_out, multiplexer_8_out, multiplexer_9_out, multiplexer_10_out,
       or_1_out, or_2_out, \源寄存器使用情况_1_r1_used , \源寄存器使用情况_1_r2_used ;

  Comparator #(.width(5)) comparator_1 (.a(R1), .b({5{1'b0}}), .eq(comparator_1_eq));  // open: gt, lt
  Comparator #(.width(5)) comparator_2 (.a(R2), .b({5{1'b0}}), .eq(comparator_2_eq));  // open: gt, lt
  Comparator #(.width(5)) comparator_3 (.a(R1), .b(EX_WriteReg), .eq(comparator_3_eq));  // open: gt, lt
  Comparator #(.width(5)) comparator_4 (.a(R2), .b(EX_WriteReg), .eq(comparator_4_eq));  // open: gt, lt
  Comparator #(.width(5)) comparator_5 (.a(R1), .b(MEM_WriteReg), .eq(comparator_5_eq));  // open: gt, lt
  Comparator #(.width(5)) comparator_6 (.a(R2), .b(MEM_WriteReg), .eq(comparator_6_eq));  // open: gt, lt
  \源寄存器使用情况  \u_源寄存器使用情况_1  (
    .OP0(OP_CODE[0]), .OP1(OP_CODE[1]), .OP2(OP_CODE[2]), .OP3(OP_CODE[3]), .OP4(OP_CODE[4]),
    .OP5(OP_CODE[5]), .F1(FUNC[1]), .F2(FUNC[2]), .F0(FUNC[0]), .F3(FUNC[3]), .F4(FUNC[4]), .F5(FUNC[5]),
    .R1_Used(\源寄存器使用情况_1_r1_used ), .R2_Used(\源寄存器使用情况_1_r2_used ));
  Multiplexer #(.enable("false")) multiplexer_1 (
    .in0(comparator_3_eq), .in1(1'b0), .out(multiplexer_1_out), .sel(comparator_1_eq));
  Multiplexer #(.enable("false")) multiplexer_2 (
    .in0(comparator_4_eq), .in1(1'b0), .out(multiplexer_2_out), .sel(comparator_2_eq));
  Multiplexer #(.enable("false")) multiplexer_3 (
    .in0(comparator_5_eq), .in1(1'b0), .out(multiplexer_3_out), .sel(comparator_1_eq));
  Multiplexer #(.enable("false")) multiplexer_4 (
    .in0(comparator_6_eq), .in1(1'b0), .out(multiplexer_4_out), .sel(comparator_2_eq));
  Multiplexer #(.enable("false")) multiplexer_5 (
    .in0(1'b0), .in1(multiplexer_1_out), .out(multiplexer_5_out), .sel(\源寄存器使用情况_1_r1_used ));
  Multiplexer #(.enable("false")) multiplexer_6 (
    .in0(1'b0), .in1(multiplexer_2_out), .out(multiplexer_6_out), .sel(\源寄存器使用情况_1_r2_used ));
  Multiplexer #(.enable("false")) multiplexer_7 (
    .in0(1'b0), .in1(multiplexer_3_out), .out(multiplexer_7_out), .sel(\源寄存器使用情况_1_r1_used ));
  Multiplexer #(.enable("false")) multiplexer_8 (
    .in0(1'b0), .in1(multiplexer_4_out), .out(multiplexer_8_out), .sel(\源寄存器使用情况_1_r2_used ));
  or or_1 (or_1_out, multiplexer_5_out, multiplexer_6_out);
  or or_2 (or_2_out, multiplexer_7_out, multiplexer_8_out);
  Multiplexer #(.enable("false")) multiplexer_9 (
    .in0(1'b0), .in1(or_1_out), .out(multiplexer_9_out), .sel(EX_RegWrite));
  Multiplexer #(.enable("false")) multiplexer_10 (
    .in0(1'b0), .in1(or_2_out), .out(multiplexer_10_out), .sel(MEM_RegWrite));
  or or_3 (Relevant, multiplexer_9_out, multiplexer_10_out);
endmodule
